// Logisim project calculator.circ as structural Verilog: 7 circuits, main circuit main
module main (
);

  wire adder_1_cout, and_1_out, and_2_out, and_3_out, and_4_out, and_5_out, and_6_out, and_7_out, and_8_out,
       button_1_out, button_3_out, button_4_out, button_16_out, coder_2b_1_pressed, coder_2b_2_pressed,
       coder_4b_h_1_pressed, decoder_1_out0, decoder_1_out1, decoder_1_out2, decoder_2_out0, decoder_2_out2,
       demultiplexer_1_out0, demultiplexer_1_out1, demultiplexer_2_out0, demultiplexer_2_out1, not_1_out,
       not_2_out, not_3_out, not_4_out, num_input_system_32b_ns_1_overflow, on_finder_32b_1_out_2, or_2_out,
       or_3_out, or_4_out, or_5_out, or_6_out, or_7_out, or_8_out, or_9_out, or_10_out, or_11_out,
       s_r_ff_1_q, s_r_ff_2_q, s_r_ff_3_q;
  wire [1:0] coder_2b_1_out, coder_2b_2_out, multiplexer_1_out, multiplexer_6_out, register_1_q, register_2_q;
  wire [2:1] or_1_out;
  wire [3:0] button_2_out, coder_4b_h_1_out, digit_finder_32b_ns_1_out_3, digit_finder_32b_ns_1_out_4,
       digit_finder_32b_ns_1_out_5, digit_finder_32b_ns_1_out_6, digit_finder_32b_ns_1_out_7,
       digit_finder_32b_ns_1_out_8, digit_finder_32b_ns_1_out_9, digit_finder_32b_ns_1_out_10,
       digit_finder_32b_ns_1_out_11, digit_finder_32b_ns_1_out_12, multiplexer_3_out;
  wire [9:0] button_15_out;
  wire [15:0] bit_extender_1_out;
  wire [31:0] A_q, adder_1_out, B_q, divider_1_out, multiplexer_2_out, multiplexer_4_out, multiplexer_5_out,
       multiplexer_7_out, multiplier_1_cout, multiplier_1_out, num_input_system_32b_ns_1_out, register_3_q,
       subtractor_1_out;

  coder_2b coder_2b_1 (.in({1'b0, or_1_out, 1'b0}), .out(coder_2b_1_out), .pressed(coder_2b_1_pressed));  // open: zero
  or or_1 (or_1_out[1], button_16_out, coder_2b_2_pressed);
  Register #(.width(2), .trigger("high")) register_1 (
    .D(coder_2b_1_out), .en(1'b1), .Q(register_1_q), .clk(coder_2b_1_pressed), .clr(button_1_out));
  Multiplexer #(.width(2), .enable("false")) multiplexer_1 (
    .in0(register_1_q), .in1(2'b11), .out(multiplexer_1_out), .sel(s_r_ff_1_q));
  Multiplexer #(.select(2), .width(32), .enable("false")) multiplexer_2 (
    .in0(A_q), .in1(B_q), .in2(register_3_q), .in3({32{1'b0}}), .out(multiplexer_2_out),
    .sel(multiplexer_1_out));
  digit_finder_32b_ns digit_finder_32b_ns_1 (
    .in_2(multiplexer_2_out), .out_7(digit_finder_32b_ns_1_out_7), .out_8(digit_finder_32b_ns_1_out_8),
    .out_9(digit_finder_32b_ns_1_out_9), .out_10(digit_finder_32b_ns_1_out_10),
    .out_11(digit_finder_32b_ns_1_out_11), .out_12(digit_finder_32b_ns_1_out_12),
    .out_3(digit_finder_32b_ns_1_out_3), .out_4(digit_finder_32b_ns_1_out_4),
    .out_5(digit_finder_32b_ns_1_out_5), .out_6(digit_finder_32b_ns_1_out_6));  // open: number_of_digits, enable_Negatative
  Decoder #(.select(2), .enable("false")) decoder_1 (
    .out0(decoder_1_out0), .out1(decoder_1_out1), .out2(decoder_1_out2), .sel(register_1_q));  // open: out3
  and and_1 (and_1_out, decoder_1_out2, not_1_out);
  Button button_1 (.out(button_1_out));
  not not_1 (not_1_out, or_1_out[2]);
  Hex_Digit_Display hex_digit_display_1 (.value(digit_finder_32b_ns_1_out_12));  // open: dp
  Hex_Digit_Display hex_digit_display_2 (.value(digit_finder_32b_ns_1_out_11));  // open: dp
  Button button_2 (.out(button_2_out[0]));
  Button button_3 (.out(button_3_out));
  Button button_4 (.out(button_4_out));
  Button button_5 (.out(button_2_out[1]));
  Button button_6 (.out(button_2_out[2]));
  Button button_7 (.out(button_2_out[3]));
  Hex_Digit_Display hex_digit_display_3 (.value(digit_finder_32b_ns_1_out_10));  // open: dp
  Hex_Digit_Display hex_digit_display_4 (.value(digit_finder_32b_ns_1_out_9));  // open: dp
  Button button_8 (.out(button_15_out[7]));
  Button button_9 (.out(button_15_out[4]));
  Button button_10 (.out(button_15_out[1]));
  Button button_11 (.out(or_1_out[2]));
  coder_2b coder_2b_2 (.in(button_2_out), .out(coder_2b_2_out), .pressed(coder_2b_2_pressed));  // open: zero
  Hex_Digit_Display hex_digit_display_5 (.value(digit_finder_32b_ns_1_out_8));  // open: dp
  Hex_Digit_Display hex_digit_display_6 (.value(digit_finder_32b_ns_1_out_7));  // open: dp
  Button button_12 (.out(button_15_out[8]));
  Button button_13 (.out(button_15_out[5]));
  Button button_14 (.out(button_15_out[2]));
  Button button_15 (.out(button_15_out[0]));
  Button button_16 (.out(button_16_out));
  Hex_Digit_Display hex_digit_display_7 (.value(digit_finder_32b_ns_1_out_6));  // open: dp
  Hex_Digit_Display hex_digit_display_8 (.value(digit_finder_32b_ns_1_out_5));  // open: dp
  Button button_17 (.out(button_15_out[9]));
  Button button_18 (.out(button_15_out[6]));
  Button button_19 (.out(button_15_out[3]));
  Hex_Digit_Display hex_digit_display_9 (.value(multiplexer_3_out));  // open: dp
  Hex_Digit_Display hex_digit_display_10 (.value(digit_finder_32b_ns_1_out_4));  // open: dp
  Multiplexer #(.width(4), .enable("false")) multiplexer_3 (
    .in0(digit_finder_32b_ns_1_out_3), .in1(4'b1110), .out(multiplexer_3_out), .sel(s_r_ff_1_q));
  assign bit_extender_1_out = {{6{1'b0}}, button_15_out};  // Bit_Extender bit_extender_1
  coder_4b_h coder_4b_h_1 (
    .pressed(coder_4b_h_1_pressed), .in(bit_extender_1_out), .out(coder_4b_h_1_out));  // open: zero
  or or_2 (or_2_out, and_8_out, num_input_system_32b_ns_1_overflow);
  and and_2 (and_2_out, or_3_out, not_2_out);
  or or_3 (or_3_out, button_4_out, coder_4b_h_1_pressed);
  and and_3 (and_3_out, button_3_out, and_4_out);
  and and_4 (and_4_out, or_5_out, not_3_out);
  S_R_Flip_Flop #(.trigger("high")) s_r_ff_1 (
    .S(or_2_out), .clk(1'b1), .R(and_3_out), .Q(s_r_ff_1_q), .preset(1'b0), .reset(button_1_out), .en(1'b1));  // open: Qn
  or or_4 (or_4_out, 1'b0, button_3_out, button_1_out, coder_2b_2_pressed);
  not not_2 (not_2_out, decoder_1_out2);
  or or_5 (or_5_out, decoder_1_out0, decoder_1_out1);
  not not_3 (not_3_out, and_8_out);
  num_input_system_32b_ns num_input_system_32b_ns_1 (
    .out(num_input_system_32b_ns_1_out), .overFlow(num_input_system_32b_ns_1_overflow), .set(and_2_out),
    .Bkspace(button_4_out), .in(coder_4b_h_1_out), .reset(or_4_out));
  Multiplexer #(.width(32), .enable("false")) multiplexer_4 (
    .in0(num_input_system_32b_ns_1_out), .in1(register_3_q), .out(multiplexer_4_out), .sel(and_1_out));
  or or_6 (or_6_out, and_1_out, demultiplexer_1_out0);
  or or_7 (or_7_out, button_1_out, demultiplexer_2_out0);
  S_R_Flip_Flop #(.trigger("high")) s_r_ff_2 (
    .S(coder_2b_2_pressed), .clk(1'b1), .R(1'b0), .Q(s_r_ff_2_q), .preset(1'b0), .reset(button_1_out),
    .en(1'b1));  // open: Qn
  Multiplexer #(.width(32), .enable("false")) multiplexer_5 (
    .in0(num_input_system_32b_ns_1_out), .in1(A_q), .out(multiplexer_5_out), .sel(button_16_out));
  Register #(.width(32), .trigger("high")) A (
    .D(multiplexer_4_out), .en(1'b1), .Q(A_q), .clk(or_6_out), .clr(or_7_out));
  or or_8 (or_8_out, button_16_out, demultiplexer_1_out1);
  Demultiplexer #(.enable("false")) demultiplexer_1 (
    .out0(demultiplexer_1_out0), .out1(demultiplexer_1_out1), .in(or_3_out), .sel(s_r_ff_2_q));
  Demultiplexer #(.enable("false")) demultiplexer_2 (
    .out0(demultiplexer_2_out0), .out1(demultiplexer_2_out1), .in(button_3_out), .sel(s_r_ff_2_q));
  Multiplexer #(.width(2), .enable("false")) multiplexer_6 (
    .in0(coder_2b_2_out), .in1(2'b10), .out(multiplexer_6_out), .sel(button_16_out));
  Register #(.width(32), .trigger("high")) B (
    .D(multiplexer_5_out), .en(1'b1), .Q(B_q), .clk(or_8_out), .clr(or_9_out));
  or or_9 (or_9_out, demultiplexer_2_out1, coder_2b_2_pressed, button_1_out);
  Register #(.width(2), .trigger("high")) register_2 (
    .D(multiplexer_6_out), .en(1'b1), .Q(register_2_q), .clk(or_10_out), .clr(button_1_out));
  or or_10 (or_10_out, button_16_out, coder_2b_2_pressed);
  Adder #(.width(32)) adder_1 (.a(A_q), .b(B_q), .out(adder_1_out), .cout(adder_1_cout));  // open: cin
  Subtractor #(.width(32)) subtractor_1 (.a(A_q), .b(B_q), .out(subtractor_1_out));  // open: bin, bout
  Multiplier #(.width(32)) multiplier_1 (
    .a(A_q), .b(B_q), .out(multiplier_1_out), .cout(multiplier_1_cout));  // open: cin
  Divider #(.width(32)) divider_1 (.a(A_q), .b(B_q), .out(divider_1_out));  // open: upper, rem
  on_finder_32b on_finder_32b_1 (.in_1(multiplier_1_cout), .out_2(on_finder_32b_1_out_2));
  and and_5 (and_5_out, adder_1_cout, decoder_2_out0);
  and and_6 (and_6_out, on_finder_32b_1_out_2, decoder_2_out2);
  or or_11 (or_11_out, and_5_out, and_6_out);
  and and_7 (and_7_out, or_11_out, or_1_out[2], not_4_out);
  not not_4 (not_4_out, and_1_out);
  and and_8 (and_8_out, s_r_ff_3_q, decoder_1_out2);
  Multiplexer #(.select(2), .width(32), .enable("false")) multiplexer_7 (
    .in0(adder_1_out), .in1(subtractor_1_out), .in2(multiplier_1_out), .in3(divider_1_out),
    .out(multiplexer_7_out), .sel(register_2_q));
  Decoder #(.select(2), .enable("false")) decoder_2 (
    .out0(decoder_2_out0), .out2(decoder_2_out2), .sel(register_2_q));  // open: out1, out3
  Register #(.width(32), .trigger("high")) register_3 (
    .D(multiplexer_7_out), .en(1'b1), .Q(register_3_q), .clk(or_1_out[2]), .clr(button_1_out));
  S_R_Flip_Flop #(.trigger("high")) s_r_ff_3 (
    .S(and_7_out), .clk(1'b1), .R(1'b0), .Q(s_r_ff_3_q), .preset(1'b0), .reset(button_1_out), .en(1'b1));  // open: Qn

  // Notes on the sheet:
  //   CE
  //   C
  //   +
  //   Bkspce
  //   X
  //   7
  //   _
  //   4
  //   1
  //   =
  //   /
  //   8
  //   5
  //   3
  //   2
  //   0
  //   9
  //   6
  //   ^2
  //   2 2b
  //   ^2
  //   =
  //   C
  //   CE
  //   1 1b
  //   0 1b
  //   10 32b
  //   0 32b
  //   3 2b
  //   A
  //   B
  //   ALU
  //   0 32b
  //   NIS
  //   KP psd
  //   backSpace
  //   operator psd
  //   A,B switch
  //   KP + BS psd
  //   KP bus
  //   operator bus
  //   overflow error
  //   hex e 4b
  //   stage 2
  //   stage 1
  //   stage 0
  //   not equals and stage2(send ALU to A)
endmodule

module digit_finder_32b_ns (
  input  enable_Negatative,
  input  [31:0] in_2,
  output [3:0] out_3,
  output [3:0] out_4,
  output [3:0] out_5,
  output [3:0] out_6,
  output [3:0] out_7,
  output [3:0] out_8,
  output [3:0] out_9,
  output [3:0] out_10,
  output [3:0] out_11,
  output [3:0] out_12,
  output [3:0] number_of_digits
);

  wire on_finder_32b_1_out_2, on_finder_32b_2_out_2, on_finder_32b_3_out_2, on_finder_32b_4_out_2,
       on_finder_32b_5_out_2, on_finder_32b_6_out_2, on_finder_32b_7_out_2, on_finder_32b_8_out_2,
       on_finder_32b_9_out_2, on_finder_32b_10_out_2;
  wire [3:0] adder_1_out, adder_2_out, adder_3_out, adder_4_out, adder_5_out, adder_6_out, adder_7_out,
       adder_8_out, bit_extender_1_out, bit_extender_3_out, bit_extender_5_out, bit_extender_8_out,
       bit_extender_9_out, bit_extender_11_out, bit_extender_13_out, bit_extender_16_out,
       bit_extender_17_out, bit_extender_20_out;
  wire [31:0] divider_1_out, divider_2_out, divider_3_out, divider_4_out, divider_5_out, divider_6_out,
       divider_7_out, divider_8_out, divider_9_out, multiplexer_1_out, multiplier_1_out, multiplier_2_out,
       multiplier_3_out, multiplier_4_out, multiplier_5_out, multiplier_6_out, multiplier_7_out,
       multiplier_8_out, multiplier_9_out, negator_1_out, subtractor_1_out, subtractor_2_out,
       subtractor_3_out, subtractor_4_out, subtractor_5_out, subtractor_6_out, subtractor_7_out,
       subtractor_8_out, subtractor_9_out;

  Negator #(.width(32)) negator_1 (.in(in_2), .out(negator_1_out));
  Multiplexer #(.width(32), .enable("false")) multiplexer_1 (
    .in0(in_2), .in1(negator_1_out), .out(multiplexer_1_out), .sel(in_2[31]));
  on_finder_32b on_finder_32b_1 (.in_1(multiplexer_1_out), .out_2(on_finder_32b_1_out_2));
  Subtractor #(.width(32)) subtractor_1 (
    .a(multiplexer_1_out), .b(multiplier_1_out), .out(subtractor_1_out));  // open: bin, bout
  Multiplier #(.width(32)) multiplier_1 (.a(divider_1_out), .b(32'ha), .out(multiplier_1_out));  // open: cin, cout
  Divider #(.width(32)) divider_1 (.a(multiplexer_1_out), .b(32'ha), .out(divider_1_out));  // open: upper, rem
  assign bit_extender_1_out = {{3{1'b0}}, on_finder_32b_1_out_2};  // Bit_Extender bit_extender_1
  Bit_Extender #(.in_width(32), .out_width(4)) bit_extender_2 (.in(subtractor_1_out), .out(out_3));
  Subtractor #(.width(32)) subtractor_2 (
    .a(divider_1_out), .b(multiplier_2_out), .out(subtractor_2_out));  // open: bin, bout
  Multiplier #(.width(32)) multiplier_2 (.a(divider_2_out), .b(32'ha), .out(multiplier_2_out));  // open: cin, cout
  Divider #(.width(32)) divider_2 (.a(divider_1_out), .b(32'ha), .out(divider_2_out));  // open: upper, rem
  on_finder_32b on_finder_32b_2 (.in_1(divider_1_out), .out_2(on_finder_32b_2_out_2));
  assign bit_extender_3_out = {{3{1'b0}}, on_finder_32b_2_out_2};  // Bit_Extender bit_extender_3
  Bit_Extender #(.in_width(32), .out_width(4)) bit_extender_4 (.in(subtractor_2_out), .out(out_4));
  on_finder_32b on_finder_32b_3 (.in_1(divider_2_out), .out_2(on_finder_32b_3_out_2));
  assign bit_extender_5_out = {{3{1'b0}}, on_finder_32b_3_out_2};  // Bit_Extender bit_extender_5
  Adder #(.width(4)) adder_1 (.a(bit_extender_3_out), .b(bit_extender_1_out), .out(adder_1_out));  // open: cin, cout
  Bit_Extender #(.in_width(32), .out_width(4)) bit_extender_6 (.in(subtractor_3_out), .out(out_5));
  Subtractor #(.width(32)) subtractor_3 (
    .a(divider_2_out), .b(multiplier_3_out), .out(subtractor_3_out));  // open: bin, bout
  Multiplier #(.width(32)) multiplier_3 (.a(divider_3_out), .b(32'ha), .out(multiplier_3_out));  // open: cin, cout
  Divider #(.width(32)) divider_3 (.a(divider_2_out), .b(32'ha), .out(divider_3_out));  // open: upper, rem
  on_finder_32b on_finder_32b_4 (.in_1(divider_3_out), .out_2(on_finder_32b_4_out_2));
  Adder #(.width(4)) adder_2 (.a(bit_extender_5_out), .b(adder_1_out), .out(adder_2_out));  // open: cin, cout
  Bit_Extender #(.in_width(32), .out_width(4)) bit_extender_7 (.in(subtractor_4_out), .out(out_6));
  Subtractor #(.width(32)) subtractor_4 (
    .a(divider_3_out), .b(multiplier_4_out), .out(subtractor_4_out));  // open: bin, bout
  Multiplier #(.width(32)) multiplier_4 (.a(divider_4_out), .b(32'ha), .out(multiplier_4_out));  // open: cin, cout
  Divider #(.width(32)) divider_4 (.a(divider_3_out), .b(32'ha), .out(divider_4_out));  // open: upper, rem
  on_finder_32b on_finder_32b_5 (.in_1(divider_4_out), .out_2(on_finder_32b_5_out_2));
  assign bit_extender_8_out = {{3{1'b0}}, on_finder_32b_4_out_2};  // Bit_Extender bit_extender_8
  Adder #(.width(4)) adder_3 (.a(bit_extender_8_out), .b(adder_2_out), .out(adder_3_out));  // open: cin, cout
  Subtractor #(.width(32)) subtractor_5 (
    .a(divider_4_out), .b(multiplier_5_out), .out(subtractor_5_out));  // open: bin, bout
  Multiplier #(.width(32)) multiplier_5 (.a(divider_5_out), .b(32'ha), .out(multiplier_5_out));  // open: cin, cout
  Divider #(.width(32)) divider_5 (.a(divider_4_out), .b(32'ha), .out(divider_5_out));  // open: upper, rem
  assign bit_extender_9_out = {{3{1'b0}}, on_finder_32b_5_out_2};  // Bit_Extender bit_extender_9
  Bit_Extender #(.in_width(32), .out_width(4)) bit_extender_10 (.in(subtractor_5_out), .out(out_7));
  Subtractor #(.width(32)) subtractor_6 (
    .a(divider_5_out), .b(multiplier_6_out), .out(subtractor_6_out));  // open: bin, bout
  Multiplier #(.width(32)) multiplier_6 (.a(divider_6_out), .b(32'ha), .out(multiplier_6_out));  // open: cin, cout
  Divider #(.width(32)) divider_6 (.a(divider_5_out), .b(32'ha), .out(divider_6_out));  // open: upper, rem
  on_finder_32b on_finder_32b_6 (.in_1(divider_5_out), .out_2(on_finder_32b_6_out_2));
  assign bit_extender_11_out = {{3{1'b0}}, on_finder_32b_6_out_2};  // Bit_Extender bit_extender_11
  Adder #(.width(4)) adder_4 (.a(bit_extender_9_out), .b(adder_3_out), .out(adder_4_out));  // open: cin, cout
  Bit_Extender #(.in_width(32), .out_width(4)) bit_extender_12 (.in(subtractor_6_out), .out(out_8));
  on_finder_32b on_finder_32b_7 (.in_1(divider_6_out), .out_2(on_finder_32b_7_out_2));
  assign bit_extender_13_out = {{3{1'b0}}, on_finder_32b_7_out_2};  // Bit_Extender bit_extender_13
  Adder #(.width(4)) adder_5 (.a(bit_extender_11_out), .b(adder_4_out), .out(adder_5_out));  // open: cin, cout
  Bit_Extender #(.in_width(32), .out_width(4)) bit_extender_14 (.in(subtractor_7_out), .out(out_9));
  Subtractor #(.width(32)) subtractor_7 (
    .a(divider_6_out), .b(multiplier_7_out), .out(subtractor_7_out));  // open: bin, bout
  Multiplier #(.width(32)) multiplier_7 (.a(divider_7_out), .b(32'ha), .out(multiplier_7_out));  // open: cin, cout
  Divider #(.width(32)) divider_7 (.a(divider_6_out), .b(32'ha), .out(divider_7_out));  // open: upper, rem
  on_finder_32b on_finder_32b_8 (.in_1(divider_7_out), .out_2(on_finder_32b_8_out_2));
  Adder #(.width(4)) adder_6 (.a(bit_extender_13_out), .b(adder_5_out), .out(adder_6_out));  // open: cin, cout
  Bit_Extender #(.in_width(32), .out_width(4)) bit_extender_15 (.in(subtractor_8_out), .out(out_10));
  Subtractor #(.width(32)) subtractor_8 (
    .a(divider_7_out), .b(multiplier_8_out), .out(subtractor_8_out));  // open: bin, bout
  Multiplier #(.width(32)) multiplier_8 (.a(divider_8_out), .b(32'ha), .out(multiplier_8_out));  // open: cin, cout
  Divider #(.width(32)) divider_8 (.a(divider_7_out), .b(32'ha), .out(divider_8_out));  // open: upper, rem
  on_finder_32b on_finder_32b_9 (.in_1(divider_8_out), .out_2(on_finder_32b_9_out_2));
  assign bit_extender_16_out = {{3{1'b0}}, on_finder_32b_8_out_2};  // Bit_Extender bit_extender_16
  Adder #(.width(4)) adder_7 (.a(bit_extender_16_out), .b(adder_6_out), .out(adder_7_out));  // open: cin, cout
  Subtractor #(.width(32)) subtractor_9 (
    .a(divider_8_out), .b(multiplier_9_out), .out(subtractor_9_out));  // open: bin, bout
  Multiplier #(.width(32)) multiplier_9 (.a(divider_9_out), .b(32'ha), .out(multiplier_9_out));  // open: cin, cout
  Divider #(.width(32)) divider_9 (.a(divider_8_out), .b(32'ha), .out(divider_9_out));  // open: upper, rem
  assign bit_extender_17_out = {{3{1'b0}}, on_finder_32b_9_out_2};  // Bit_Extender bit_extender_17
  Bit_Extender #(.in_width(32), .out_width(4)) bit_extender_18 (.in(subtractor_9_out), .out(out_11));
  Bit_Extender #(.in_width(32), .out_width(4)) bit_extender_19 (.in(divider_9_out), .out(out_12));
  on_finder_32b on_finder_32b_10 (.in_1(divider_9_out), .out_2(on_finder_32b_10_out_2));
  assign bit_extender_20_out = {{3{1'b0}}, on_finder_32b_10_out_2};  // Bit_Extender bit_extender_20
  Adder #(.width(4)) adder_8 (.a(bit_extender_17_out), .b(adder_7_out), .out(adder_8_out));  // open: cin, cout
  Adder #(.width(4)) adder_9 (.a(bit_extender_20_out), .b(adder_8_out), .out(number_of_digits));  // open: cin, cout
endmodule

module on_finder_32b (
  input  [31:0] in_1,
  output out_2
);

  or or_1 (out_2, in_1[16], in_1[31], in_1[30], in_1[29], in_1[28], in_1[27], in_1[26], in_1[25], in_1[24], in_1[23], in_1[22], in_1[21], in_1[20], in_1[19], in_1[18], in_1[17], in_1[15], in_1[14], in_1[13], in_1[12], in_1[11], in_1[10], in_1[9], in_1[8], in_1[7], in_1[6], in_1[5], in_1[4], in_1[3], in_1[2], in_1[1], in_1[0]);
endmodule

module num_input_system_32b_ns (
  input  set,
  input  Bkspace,
  input  [3:0] in,
  input  reset,
  output [31:0] out,
  output overFlow
);

  wire adder_1_cout, and_1_out, not_1_out, not_2_out, on_finder_32b_1_out_2, or_1_out;
  wire [31:0] adder_1_out, bit_extender_1_out, divider_1_out, multiplexer_1_out, multiplier_1_cout,
       multiplier_1_out, prev_q;

  Register #(.width(32), .trigger("high")) prev (.D(out), .en(1'b1), .Q(prev_q), .clk(not_1_out), .clr(reset));
  not not_1 (not_1_out, set);
  Divider #(.width(32)) divider_1 (.a(prev_q), .b(32'ha), .out(divider_1_out));  // open: upper, rem
  Multiplier #(.width(32)) multiplier_1 (
    .a(prev_q), .b(32'ha), .out(multiplier_1_out), .cout(multiplier_1_cout));  // open: cin
  assign bit_extender_1_out = {{28{1'b0}}, in};  // Bit_Extender bit_extender_1
  Adder #(.width(32)) adder_1 (
    .a(multiplier_1_out), .b(bit_extender_1_out), .out(adder_1_out), .cout(adder_1_cout));  // open: cin
  on_finder_32b on_finder_32b_1 (.in_1(multiplier_1_cout), .out_2(on_finder_32b_1_out_2));
  Multiplexer #(.width(32), .enable("false")) multiplexer_1 (
    .in0(adder_1_out), .in1(divider_1_out), .out(multiplexer_1_out), .sel(Bkspace));
  Register #(.width(32), .trigger("high")) curr (.D(multiplexer_1_out), .en(1'b1), .Q(out), .clk(set), .clr(reset));
  and and_1 (and_1_out, or_1_out, not_2_out);
  or or_1 (or_1_out, on_finder_32b_1_out_2, adder_1_cout);
  not not_2 (not_2_out, Bkspace);
  S_R_Flip_Flop #(.trigger("high")) s_r_ff_1 (
    .S(and_1_out), .clk(set), .R(1'b0), .Q(overFlow), .reset(reset), .en(1'b1));  // open: Qn, preset
endmodule

module coder_4b_h (
  input  [15:0] in,
  output pressed,
  output [3:0] out,
  output zero
);

  wire [3:0] or_2_out;

  or or_1 (pressed, in[15], in[14], in[13], in[12], in[11], in[10], in[9], in[8], in[7], in[6], in[5], in[4], in[3], in[2], in[1], in[0]);
  assign or_2_out = 4'b0000 | {3'b000, in[1]} | {2'b00, in[2], 1'b0} | {2'b00, {2{in[3]}}} | {1'b0, in[4], 2'b00} | {1'b0, in[5], 1'b0, in[5]} | {1'b0, {2{in[6]}}, 1'b0} | {1'b0, {3{in[7]}}} | {in[8], 3'b000} | {in[9], 2'b00, in[9]} | {in[10], 1'b0, in[10], 1'b0} | {in[11], 1'b0, {2{in[11]}}} | {{2{in[12]}}, 2'b00} | {{2{in[13]}}, 1'b0, in[13]} | {{3{in[14]}}, 1'b0} | {4{in[15]}};  // OR_Gate or_2, 4 bits wide
  Register #(.width(4), .trigger("high")) register_1 (.D(or_2_out), .en(1'b1), .Q(out), .clk(pressed));  // open: clr

  assign zero = in[0];
endmodule

module coder_4b (
  input  [15:0] in,
  output pressed,
  output [3:0] out,
  output zero
);

  or or_1 (pressed, in[15], in[14], in[13], in[12], in[11], in[10], in[9], in[8], in[7], in[6], in[5], in[4], in[3], in[2], in[1], in[0]);
  assign out = 4'b0000 | {3'b000, in[1]} | {2'b00, in[2], 1'b0} | {2'b00, {2{in[3]}}} | {1'b0, in[4], 2'b00} | {1'b0, in[5], 1'b0, in[5]} | {1'b0, {2{in[6]}}, 1'b0} | {1'b0, {3{in[7]}}} | {in[8], 3'b000} | {in[9], 2'b00, in[9]} | {in[10], 1'b0, in[10], 1'b0} | {in[11], 1'b0, {2{in[11]}}} | {{2{in[12]}}, 2'b00} | {{2{in[13]}}, 1'b0, in[13]} | {{3{in[14]}}, 1'b0} | {4{in[15]}};  // OR_Gate or_2, 4 bits wide

  assign zero = in[0];
endmodule

module coder_2b (
  input  [3:0] in,
  output zero,
  output pressed,
  output [1:0] out
);

  or or_1 (pressed, in[0], in[1], in[2], in[3]);
  assign out = 2'b00 | {1'b0, in[1]} | {in[2], 1'b0} | {2{in[3]}};  // OR_Gate or_2, 2 bits wide

  assign zero = in[0];
endmodule
