// Logisim project clock.circ as structural Verilog: 1 circuit, main circuit main
module main (
  input  in_1,
  output [31:0] out_2
);

  wire and_1_out, and_2_out, button_1_out, button_2_out, button_3_out, clock_1_out, comparator_1_eq,
       comparator_1_gt, comparator_2_gt, multiplexer_4_out, not_1_out, or_2_out, or_3_out;
  wire [3:0] bit_extender_1_out, bit_extender_2_out, bit_extender_3_out, bit_extender_4_out;
  wire [31:0] adder_1_out, adder_2_out, divider_1_out, divider_2_out, divider_3_out, divider_4_out,
       divider_5_out, multiplexer_1_out, multiplexer_2_out, multiplexer_3_out, multiplexer_5_out,
       multiplier_1_out, multiplier_2_out, multiplier_3_out, or_1_out, prev_sec_q, subtractor_1_out,
       subtractor_2_out, subtractor_3_out, subtractor_4_out;

  assign or_1_out = multiplexer_3_out | multiplexer_2_out;  // OR_Gate or_1, 32 bits wide
  Register #(.width(32), .trigger("high")) prev_sec (
    .D(out_2), .Q(prev_sec_q), .clk(not_1_out), .clr(or_2_out));  // open: en
  not not_1 (not_1_out, multiplexer_4_out);
  Multiplexer #(.width(32), .enable("false")) multiplexer_1 (
    .in0(32'h1), .in1(or_1_out), .out(multiplexer_1_out), .sel(in_1));
  Multiplexer #(.width(32), .enable("false")) multiplexer_2 (
    .in0({32{1'b0}}), .in1(32'h3c), .out(multiplexer_2_out), .sel(and_2_out));
  Multiplexer #(.width(32), .enable("false")) multiplexer_3 (
    .in0({32{1'b0}}), .in1(32'he10), .out(multiplexer_3_out), .sel(and_1_out));
  Comparator #(.width(32)) comparator_1 (
    .a(prev_sec_q), .b(32'h15180), .gt(comparator_1_gt), .eq(comparator_1_eq));  // open: lt
  or or_2 (or_2_out, comparator_1_eq, button_1_out, comparator_1_gt);
  Adder #(.width(32)) adder_1 (.a(prev_sec_q), .b(multiplexer_1_out), .out(adder_1_out));  // open: cin, cout
  Multiplexer #(.enable("false")) multiplexer_4 (
    .in0(clock_1_out), .in1(or_3_out), .out(multiplexer_4_out), .sel(in_1));
  Clock #(.highDuration(16), .lowDuration(16)) clock_1 (.out(clock_1_out));
  Register #(.width(32), .trigger("high")) seconds (
    .D(adder_1_out), .Q(out_2), .clk(multiplexer_4_out), .clr(or_2_out));  // open: en
  or or_3 (or_3_out, and_1_out, and_2_out);
  Divider #(.width(32)) divider_1 (.a(out_2), .b(32'h3c), .out(divider_1_out));  // open: upper, rem
  Button button_1 (.out(button_1_out));
  and and_1 (and_1_out, in_1, button_2_out);
  Button button_2 (.out(button_2_out));
  Button button_3 (.out(button_3_out));
  and and_2 (and_2_out, button_3_out, in_1);
  Subtractor #(.width(32)) subtractor_1 (
    .a(divider_1_out), .b(multiplier_1_out), .out(subtractor_1_out));  // open: bin, bout
  Multiplier #(.width(32)) multiplier_1 (.a(32'h3c), .b(divider_2_out), .out(multiplier_1_out));  // open: cin, cout
  Divider #(.width(32)) divider_2 (.a(divider_1_out), .b(32'h3c), .out(divider_2_out));  // open: upper, rem
  LED PM (.in(comparator_2_gt));
  Subtractor #(.width(32)) subtractor_2 (
    .a(subtractor_1_out), .b(multiplier_2_out), .out(subtractor_2_out));  // open: bin, bout
  Multiplier #(.width(32)) multiplier_2 (.a(divider_3_out), .b(32'ha), .out(multiplier_2_out));  // open: cin, cout
  Divider #(.width(32)) divider_3 (.a(subtractor_1_out), .b(32'ha), .out(divider_3_out));  // open: upper, rem
  Divider #(.width(32)) divider_4 (.a(multiplier_1_out), .b(32'h3c), .out(divider_4_out));  // open: upper, rem
  Hex_Digit_Display hex_digit_display_1 (.value(bit_extender_3_out));  // open: dp
  Hex_Digit_Display hex_digit_display_2 (.value(bit_extender_4_out));  // open: dp
  Bit_Extender #(.in_width(32), .out_width(4)) bit_extender_1 (.in(subtractor_2_out), .out(bit_extender_1_out));
  Bit_Extender #(.in_width(32), .out_width(4)) bit_extender_2 (.in(divider_3_out), .out(bit_extender_2_out));
  Adder #(.width(32)) adder_2 (.a(32'h1), .b(divider_4_out), .out(adder_2_out));  // open: cin, cout
  Hex_Digit_Display hex_digit_display_3 (.value(bit_extender_2_out));  // open: dp
  Comparator #(.width(32)) comparator_2 (.a(adder_2_out), .b(32'hc), .gt(comparator_2_gt));  // open: eq, lt
  Multiplexer #(.width(32), .enable("false")) multiplexer_5 (
    .in0(adder_2_out), .in1(subtractor_3_out), .out(multiplexer_5_out), .sel(comparator_2_gt));
  Subtractor #(.width(32)) subtractor_3 (.a(adder_2_out), .b(32'hc), .out(subtractor_3_out));  // open: bin, bout
  Hex_Digit_Display hex_digit_display_4 (.value(bit_extender_1_out));  // open: dp
  Subtractor #(.width(32)) subtractor_4 (
    .a(multiplexer_5_out), .b(multiplier_3_out), .out(subtractor_4_out));  // open: bin, bout
  Multiplier #(.width(32)) multiplier_3 (.a(32'ha), .b(divider_5_out), .out(multiplier_3_out));  // open: cin, cout
  Divider #(.width(32)) divider_5 (.a(multiplexer_5_out), .b(32'ha), .out(divider_5_out));  // open: upper, rem
  Bit_Extender #(.in_width(32), .out_width(4)) bit_extender_3 (.in(subtractor_4_out), .out(bit_extender_3_out));
  Bit_Extender #(.in_width(32), .out_width(4)) bit_extender_4 (.in(divider_5_out), .out(bit_extender_4_out));

  // Notes on the sheet:
  //   :
endmodule
