// Logisim project clock2.circ as structural Verilog: 4 circuits, main circuit main
module main (
  input  _12hr,
  input  set
);

  wire clock_1_out, coder_2b_1_pressed, comparator_1_eq, comparator_1_lt, comparator_2_eq, comparator_2_lt,
       comparator_3_eq, comparator_3_lt, comparator_4_eq, comparator_4_gt, comparator_5_eq, comparator_5_gt,
       comparator_6_eq, comparator_6_gt, decoder_1_out0, decoder_1_out1, decoder_1_out2,
       demultiplexer_1_out0, demultiplexer_1_out1, demultiplexer_1_out2, multiplexer_1_out, not_1_out,
       not_2_out, or_1_out, or_2_out, or_3_out, or_4_out, or_5_out, or_6_out, or_7_out, or_8_out, zero_out;
  wire [1:0] coder_2b_1_out, multiplexer_8_out, n24_hr_to_12hr_converter_8b_1_am, plus_10_out, register_1_q;
  wire [2:0] hr_3_out;
  wire [3:0] bit_extender_3_out, hr_2_digit_0, hr_2_digit_1, min_2_digit_0, min_2_digit_1, sec_5_digit_0,
       sec_5_digit_1;
  wire [7:0] adder_1_out, adder_2_out, adder_3_out, adder_4_out, adder_5_out, adder_6_out,
       bit_extender_1_out, bit_extender_2_out, hr_buf_q, hr_q, min_buf_q, min_q, multiplexer_2_out,
       multiplexer_3_out, multiplexer_4_out, multiplexer_5_out, multiplexer_6_out, multiplexer_7_out,
       multiplexer_9_out, multiplexer_10_out, multiplexer_11_out, multiplexer_12_out, multiplexer_13_out,
       multiplexer_14_out, multiplexer_15_out, multiplexer_16_out, multiplexer_17_out, multiplexer_18_out,
       multiplexer_19_out, n24_hr_to_12hr_converter_8b_1__12hr_out, sec_2_q, sec_3_q, sec_4_q, sec_buf_q,
       sec_q;

  not not_1 (not_1_out, clock_1_out);
  Multiplexer #(.enable("false")) multiplexer_1 (.in0(not_1_out), .in1(or_8_out), .out(multiplexer_1_out), .sel(set));
  Register #(.trigger("high")) hr_buf (
    .D(multiplexer_10_out), .Q(hr_buf_q), .clk(multiplexer_1_out), .clr(zero_out));  // open: en
  Register #(.trigger("high")) min_buf (
    .D(multiplexer_12_out), .Q(min_buf_q), .clk(multiplexer_1_out), .clr(zero_out));  // open: en
  Register #(.trigger("high")) sec_buf (
    .D(multiplexer_15_out), .Q(sec_buf_q), .clk(multiplexer_1_out), .clr(zero_out));  // open: en
  Clock #(.highDuration(16), .lowDuration(16)) clock_1 (.out(clock_1_out));
  Adder adder_1 (.a(bit_extender_1_out), .b(hr_buf_q), .out(adder_1_out));  // open: cin, cout
  assign bit_extender_1_out = {{7{1'b0}}, or_2_out};  // Bit_Extender bit_extender_1
  Adder adder_2 (.a(bit_extender_2_out), .b(min_buf_q), .out(adder_2_out));  // open: cin, cout
  assign bit_extender_2_out = {{7{1'b0}}, or_3_out};  // Bit_Extender bit_extender_2
  Adder adder_3 (.a(8'h1), .b(sec_buf_q), .out(adder_3_out));  // open: cin, cout
  Comparator comparator_1 (.a(8'h18), .b(adder_1_out), .eq(comparator_1_eq), .lt(comparator_1_lt));  // open: gt
  or or_1 (or_1_out, comparator_1_lt, comparator_1_eq);
  Multiplexer #(.width(8), .enable("false")) multiplexer_2 (
    .in0(adder_1_out), .in1({8{1'b0}}), .out(multiplexer_2_out), .sel(or_1_out));
  Multiplexer #(.width(8), .enable("false")) multiplexer_3 (
    .in0(multiplexer_2_out), .in1(hr_buf_q), .out(multiplexer_3_out), .sel(set));
  or or_2 (or_2_out, comparator_2_eq, comparator_2_lt);
  Comparator comparator_2 (.a(8'h3c), .b(adder_2_out), .eq(comparator_2_eq), .lt(comparator_2_lt));  // open: gt
  Multiplexer #(.width(8), .enable("false")) multiplexer_4 (
    .in0(adder_2_out), .in1({8{1'b0}}), .out(multiplexer_4_out), .sel(or_2_out));
  Multiplexer #(.width(8), .enable("false")) multiplexer_5 (
    .in0(multiplexer_4_out), .in1(min_buf_q), .out(multiplexer_5_out), .sel(set));
  or or_3 (or_3_out, comparator_3_lt, comparator_3_eq);
  Comparator comparator_3 (.a(8'h3c), .b(adder_3_out), .eq(comparator_3_eq), .lt(comparator_3_lt));  // open: gt
  Multiplexer #(.width(8), .enable("false")) multiplexer_6 (
    .in0(adder_3_out), .in1({8{1'b0}}), .out(multiplexer_6_out), .sel(or_3_out));
  Multiplexer #(.width(8), .enable("false")) multiplexer_7 (
    .in0(multiplexer_6_out), .in1(sec_buf_q), .out(multiplexer_7_out), .sel(set));
  _24_hr_to_12hr_converter_8b u_24_hr_to_12hr_converter_8b_1 (
    ._24_hr_in(hr_q), ._12hr_out(n24_hr_to_12hr_converter_8b_1__12hr_out),
    .PM(n24_hr_to_12hr_converter_8b_1_am[1]), .AM(n24_hr_to_12hr_converter_8b_1_am[0]));
  or or_4 (or_4_out, set, clock_1_out);
  Register #(.trigger("high")) hr (.D(multiplexer_3_out), .Q(hr_q), .clk(or_4_out), .clr(zero_out));  // open: en
  Register #(.trigger("high")) min (.D(multiplexer_5_out), .Q(min_q), .clk(or_4_out), .clr(zero_out));  // open: en
  Register #(.trigger("high")) sec (.D(multiplexer_7_out), .Q(sec_q), .clk(or_4_out), .clr(zero_out));  // open: en
  Multiplexer #(.width(2), .enable("false")) multiplexer_8 (
    .in0(2'b00), .in1(n24_hr_to_12hr_converter_8b_1_am), .out(multiplexer_8_out), .sel(_12hr));
  Multiplexer #(.width(8), .enable("false")) multiplexer_9 (
    .in0(hr_q), .in1(n24_hr_to_12hr_converter_8b_1__12hr_out), .out(multiplexer_9_out), .sel(_12hr));
  Register #(.trigger("high")) sec_2 (.D(hr_q), .Q(sec_2_q), .clk(not_2_out));  // open: en, clr
  not not_2 (not_2_out, or_8_out);
  Register #(.trigger("high")) sec_3 (.D(min_q), .Q(sec_3_q), .clk(not_2_out));  // open: en, clr
  Register #(.trigger("high")) sec_4 (.D(sec_q), .Q(sec_4_q), .clk(not_2_out));  // open: en, clr
  Button zero (.out(zero_out));
  digit_finder_8b hr_2 (.digit_0(hr_2_digit_0), .digit_1(hr_2_digit_1), .input_8b(multiplexer_9_out));  // open: digit_2
  digit_finder_8b min_2 (.digit_0(min_2_digit_0), .digit_1(min_2_digit_1), .input_8b(min_q));  // open: digit_2
  digit_finder_8b sec_5 (.digit_0(sec_5_digit_0), .digit_1(sec_5_digit_1), .input_8b(sec_q));  // open: digit_2
  Multiplexer #(.width(8), .enable("false")) multiplexer_10 (
    .in0(sec_2_q), .in1(multiplexer_11_out), .out(multiplexer_10_out), .sel(set));
  Multiplexer #(.width(8), .enable("false")) multiplexer_11 (
    .in0(multiplexer_16_out), .in1({8{1'b0}}), .out(multiplexer_11_out), .sel(or_5_out));
  Multiplexer #(.width(8), .enable("false")) multiplexer_12 (
    .in0(sec_3_q), .in1(multiplexer_13_out), .out(multiplexer_12_out), .sel(set));
  Multiplexer #(.width(8), .enable("false")) multiplexer_13 (
    .in0(multiplexer_17_out), .in1({8{1'b0}}), .out(multiplexer_13_out), .sel(or_6_out));
  Multiplexer #(.width(8), .enable("false")) multiplexer_14 (
    .in0(multiplexer_18_out), .in1({8{1'b0}}), .out(multiplexer_14_out), .sel(or_7_out));
  Multiplexer #(.width(8), .enable("false")) multiplexer_15 (
    .in0(sec_4_q), .in1(multiplexer_14_out), .out(multiplexer_15_out), .sel(set));
  LED PM (.in(multiplexer_8_out[1]));
  LED AM (.in(multiplexer_8_out[0]));
  Hex_Digit_Display hex_digit_display_1 (.value(hr_2_digit_1));  // open: dp
  Adder adder_4 (.a(sec_2_q), .b(multiplexer_19_out), .out(adder_4_out));  // open: cin, cout
  Comparator comparator_4 (.a(multiplexer_16_out), .b(8'h18), .gt(comparator_4_gt), .eq(comparator_4_eq));  // open: lt
  Adder adder_5 (.a(sec_3_q), .b(multiplexer_19_out), .out(adder_5_out));  // open: cin, cout
  Comparator comparator_5 (.a(multiplexer_17_out), .b(8'h3c), .gt(comparator_5_gt), .eq(comparator_5_eq));  // open: lt
  Adder adder_6 (.a(sec_4_q), .b(multiplexer_19_out), .out(adder_6_out));  // open: cin, cout
  Comparator comparator_6 (.a(multiplexer_18_out), .b(8'h3c), .gt(comparator_6_gt), .eq(comparator_6_eq));  // open: lt
  Hex_Digit_Display hex_digit_display_2 (.value(min_2_digit_1));  // open: dp
  Hex_Digit_Display hex_digit_display_3 (.value(hr_2_digit_0));  // open: dp
  Multiplexer #(.width(8), .enable("false")) multiplexer_16 (
    .in0(sec_2_q), .in1(adder_4_out), .out(multiplexer_16_out), .sel(demultiplexer_1_out0));
  or or_5 (or_5_out, comparator_4_gt, comparator_4_eq);
  Multiplexer #(.width(8), .enable("false")) multiplexer_17 (
    .in0(sec_3_q), .in1(adder_5_out), .out(multiplexer_17_out), .sel(demultiplexer_1_out1));
  or or_6 (or_6_out, comparator_5_gt, comparator_5_eq);
  Multiplexer #(.width(8), .enable("false")) multiplexer_18 (
    .in0(sec_4_q), .in1(adder_6_out), .out(multiplexer_18_out), .sel(demultiplexer_1_out2));
  or or_7 (or_7_out, comparator_6_gt, comparator_6_eq);
  Hex_Digit_Display hex_digit_display_4 (.value(min_2_digit_0));  // open: dp
  Hex_Digit_Display hex_digit_display_5 (.value(sec_5_digit_1));  // open: dp
  Multiplexer #(.width(8), .enable("false")) multiplexer_19 (
    .in0(8'h1), .in1(8'ha), .out(multiplexer_19_out), .sel(plus_10_out[0]));
  Hex_Digit_Display hex_digit_display_6 (.value(sec_5_digit_0));  // open: dp
  or or_8 (or_8_out, plus_10_out[0], plus_10_out[1]);
  Demultiplexer #(.select(2), .enable("false")) demultiplexer_1 (
    .out0(demultiplexer_1_out0), .out1(demultiplexer_1_out1), .out2(demultiplexer_1_out2), .in(or_8_out),
    .sel(register_1_q));  // open: out3
  coder_2b coder_2b_1 (.pressed(coder_2b_1_pressed), .in(bit_extender_3_out), .out(coder_2b_1_out));  // open: zero
  Button plus_1 (.out(plus_10_out[1]));
  Button plus_10 (.out(plus_10_out[0]));
  Button hr_3 (.out(hr_3_out[0]));
  Button min_3 (.out(hr_3_out[1]));
  Button sec_6 (.out(hr_3_out[2]));
  assign bit_extender_3_out = {{1{1'b0}}, hr_3_out};  // Bit_Extender bit_extender_3
  LED led_1 (.in(decoder_1_out0));
  LED led_2 (.in(decoder_1_out1));
  LED led_3 (.in(decoder_1_out2));
  Decoder #(.select(2), .enable("false")) decoder_1 (
    .out0(decoder_1_out0), .out1(decoder_1_out1), .out2(decoder_1_out2), .sel(register_1_q));  // open: out3
  Register #(.width(2), .trigger("high")) register_1 (
    .D(coder_2b_1_out), .Q(register_1_q), .clk(coder_2b_1_pressed));  // open: en, clr

  // Notes on the sheet:
  //   :
  //   :
endmodule

module digit_finder_8b (
  input  [7:0] input_8b,
  output [3:0] digit_0,
  output [3:0] digit_1,
  output [3:0] digit_2
);

  wire [7:0] divider_1_out, divider_2_out, multiplier_1_out, multiplier_2_out, subtractor_1_out,
       subtractor_2_out;

  Bit_Extender #(.out_width(4)) bit_extender_1 (.in(subtractor_1_out), .out(digit_0));
  Subtractor subtractor_1 (.a(input_8b), .b(multiplier_1_out), .out(subtractor_1_out));  // open: bin, bout
  Multiplier multiplier_1 (.a(divider_1_out), .b(8'ha), .out(multiplier_1_out));  // open: cin, cout
  Divider divider_1 (.a(input_8b), .b(8'ha), .out(divider_1_out));  // open: upper, rem
  Bit_Extender #(.out_width(4)) bit_extender_2 (.in(subtractor_2_out), .out(digit_1));
  Subtractor subtractor_2 (.a(divider_1_out), .b(multiplier_2_out), .out(subtractor_2_out));  // open: bin, bout
  Multiplier multiplier_2 (.a(divider_2_out), .b(8'ha), .out(multiplier_2_out));  // open: cin, cout
  Divider divider_2 (.a(divider_1_out), .b(8'ha), .out(divider_2_out));  // open: upper, rem
  Bit_Extender #(.out_width(4)) bit_extender_3 (.in(divider_2_out), .out(digit_2));
endmodule

module _24_hr_to_12hr_converter_8b (
  input  [7:0] _24_hr_in,
  output [7:0] _12hr_out,
  output PM,
  output AM
);

  wire comparator_1_eq, comparator_2_eq, comparator_2_gt;
  wire [7:0] multiplexer_1_out, subtractor_1_out;

  Comparator comparator_1 (.a(_24_hr_in), .b({8{1'b0}}), .eq(comparator_1_eq));  // open: gt, lt
  Comparator comparator_2 (.a(_24_hr_in), .b(8'hc), .gt(comparator_2_gt), .eq(comparator_2_eq), .lt(AM));
  or or_1 (PM, comparator_2_eq, comparator_2_gt);
  Subtractor subtractor_1 (.a(_24_hr_in), .b(8'hc), .out(subtractor_1_out));  // open: bin, bout
  Multiplexer #(.width(8), .enable("false")) multiplexer_1 (
    .in0(_24_hr_in), .in1(subtractor_1_out), .out(multiplexer_1_out), .sel(comparator_2_gt));
  Multiplexer #(.width(8), .enable("false")) multiplexer_2 (
    .in0(multiplexer_1_out), .in1(8'hc), .out(_12hr_out), .sel(comparator_1_eq));
endmodule

module coder_2b (
  input  [3:0] in,
  output zero,
  output pressed,
  output [1:0] out
);

  or or_1 (pressed, in[0], in[1], in[2], in[3]);
  assign out = 2'b00 | {1'b0, in[1]} | {in[2], 1'b0} | {2{in[3]}};  // OR_Gate or_2, 2 bits wide

  assign zero = in[0];
endmodule
