// Logisim project comparator.circ as structural Verilog: 1 circuit, main circuit main
module main (
  input  [3:0] A,
  input  [3:0] B,
  input  in_3,
  output out_4,
  output out_5,
  output out_6
);

  wire and_1_out, and_2_out, and_3_out, and_4_out, and_5_out, and_6_out, and_7_out, and_8_out, not_1_out,
       not_2_out, not_3_out, not_4_out, not_5_out, not_6_out, not_7_out, not_8_out, not_9_out, not_10_out,
       not_11_out, not_12_out, not_13_out, or_1_out, or_2_out, or_3_out, or_4_out;

  or or_1 (or_1_out, and_1_out, or_2_out);
  and and_1 (and_1_out, not_1_out, B[0]);
  not not_1 (not_1_out, A[0]);
  or or_2 (or_2_out, and_2_out, or_3_out);
  and and_2 (and_2_out, not_2_out, B[1]);
  not not_2 (not_2_out, A[1]);
  or or_3 (or_3_out, and_3_out, or_4_out);
  and and_3 (and_3_out, not_3_out, B[2]);
  not not_3 (not_3_out, A[2]);
  or or_4 (or_4_out, and_4_out, in_3);
  and and_4 (and_4_out, not_4_out, B[3]);
  not not_4 (not_4_out, A[3]);
  and and_5 (and_5_out, A[0], not_5_out, not_6_out);
  not not_5 (not_5_out, or_2_out);
  not not_6 (not_6_out, B[0]);
  not not_7 (not_7_out, or_3_out);
  and and_6 (and_6_out, A[1], not_7_out, not_8_out);
  not not_8 (not_8_out, B[1]);
  and and_7 (and_7_out, A[2], not_9_out, not_10_out);
  not not_9 (not_9_out, or_4_out);
  not not_10 (not_10_out, B[2]);
  not not_11 (not_11_out, in_3);
  and and_8 (and_8_out, A[3], not_11_out, not_12_out);
  not not_12 (not_12_out, B[3]);
  or or_5 (out_4, and_5_out, and_6_out, and_7_out, and_8_out);
  nor nor_1 (out_5, or_1_out, out_4);
  and and_9 (out_6, or_1_out, not_13_out);
  not not_13 (not_13_out, out_4);

  // Notes on the sheet:
  //   A?B
endmodule
