// Logisim project computer.circ as structural Verilog
// 0:ALU wr
module main (
  input  RESET_PROGRAM_MEMORY,
  input  reset_safety,
  input  [31:0] PM_A_in,
  input  [31:0] PM_B_in,
  input  [31:0] PM_C_in,
  input  [31:0] PM_D_in,
  input  run,
  input  reset_system,
  input  [7:0] Programing_Q,
  input  Write_rom_out_to_PM,
  input  run_from_rom,
  input  set,
  input  \program ,
  input  [31:0] user_0_select_2,
  input  [31:0] user_1_select_3,
  input  [31:0] user_2_select_4,
  input  [31:0] user_3_select_5,
  input  [31:0] user_4_select_6,
  input  [31:0] user_5_select_7,
  input  [31:0] user_6_select_8,
  input  [31:0] user_7_select_9,
  input  [31:0] user_8_select_10,
  input  [31:0] user_9_select_11,
  input  [31:0] user_10_select_12,
  input  [31:0] user_11_select_13,
  input  [31:0] user_12_select_14,
  input  [31:0] user_13_select_15,
  output [31:0] direct_ALU_out,
  output [31:0] direct_ALU_Zero,
  output [31:0] direct_ReadMux_Out,
  output [31:0] direct_RAM_Out,
  output [31:0] ALU_Out,
  output [31:0] ALU_Zero,
  output [31:0] ReadMux_Out,
  output [31:0] RAM_Out,
  output [31:0] PM_A_out__Controls,
  output [31:0] PM_B_out__Output_expansion,
  output [31:0] BIN__out,
  output clock_high_speed,
  output clock_low_speed,
  output [31:0] PM_C_out__Constant,
  output [31:0] PM_D_out__Goto,
  output [7:0] current_step
);

  wire and_1_out, and_2_out, and_4_out, and_5_out, and_6_out, and_7_out, and_8_out, and_10_out, and_11_out,
       buffer_1_out, buffer_2_out, buffer_3_out, buffer_4_out, buffer_5_out, buffer_6_out, buffer_7_out,
       buffer_8_out, buffer_9_out, buffer_10_out, buffer_11_out, buffer_12_out, buffer_13_out, buffer_14_out,
       buffer_15_out, buffer_16_out, buffer_17_out, buffer_18_out, buffer_19_out, buffer_20_out,
       buffer_21_out, buffer_22_out, buffer_23_out, buffer_24_out, buffer_25_out, buffer_26_out,
       buffer_27_out, buffer_28_out, buffer_29_out, buffer_30_out, buffer_31_out, buffer_32_out,
       buffer_33_out, buffer_34_out, buffer_35_out, buffer_36_out, buffer_37_out, buffer_38_out,
       buffer_39_out, buffer_40_out, buffer_41_out, buffer_42_out, buffer_43_out, buffer_44_out,
       buffer_45_out, buffer_46_out, buffer_47_out, buffer_48_out, buffer_49_out, buffer_50_out,
       buffer_51_out, buffer_52_out, buffer_53_out, buffer_54_out, buffer_55_out, buffer_56_out,
       buffer_57_out, buffer_58_out, buffer_59_out, buffer_60_out, buffer_61_out, buffer_62_out,
       buffer_63_out, buffer_64_out, buffer_65_out, buffer_66_out, buffer_67_out, buffer_68_out,
       buffer_69_out, comparator_1_lt, comparator_2_eq, demultiplexer_2_out0, demultiplexer_2_out1,
       demultiplexer_3_out0, demultiplexer_3_out1, demultiplexer_5_out0, demultiplexer_5_out1,
       High_speed__x_out, multiplexer_17_out, not_1_out, not_2_out, not_3_out, not_4_out, not_69_out,
       on_finder_8b_1_on, or_1_out, or_2_out, or_3_out;
  wire [0:0] multiplexer_9_out;
  wire [1:0] bit_extender_4_out, multiplexer_9_out_5;
  wire [1:1] and_9_out;
  wire [2:0] not_5_out, not_6_out, not_7_out, not_9_out, not_10_out, not_11_out, not_12_out, not_13_out,
       not_14_out, not_15_out, not_16_out, not_17_out, not_18_out, not_19_out, not_20_out, not_21_out,
       not_22_out, not_23_out, not_24_out, not_25_out, not_26_out, not_27_out, not_28_out, not_29_out,
       not_30_out, not_31_out, not_32_out, not_33_out, not_34_out, not_35_out, not_36_out, not_37_out,
       not_38_out, not_39_out, not_40_out, not_41_out, not_42_out, not_43_out, not_44_out, not_45_out,
       not_46_out, not_47_out, not_48_out, not_49_out, not_50_out, not_51_out, not_52_out, not_53_out,
       not_54_out, not_55_out, not_56_out, not_57_out, not_58_out, not_59_out, not_60_out, not_61_out,
       not_62_out, not_63_out, not_64_out, not_65_out, not_66_out, not_67_out, not_68_out;
  wire [3:0] bit_extender_3_out, bit_extender_5_out, digit_finder_32b_ns_1_out_2,
       digit_finder_32b_ns_1_out_3, digit_finder_32b_ns_1_out_4, digit_finder_32b_ns_1_out_5,
       digit_finder_32b_ns_1_out_6, digit_finder_32b_ns_1_out_7, digit_finder_32b_ns_1_out_8,
       digit_finder_32b_ns_1_out_9, digit_finder_32b_ns_1_out_10, digit_finder_32b_ns_1_out_11,
       multiplexer_4_out, multiplexer_9_out_4, multiplexer_9_out_6;
  wire [4:0] multiplexer_9_out_7, not_8_out;
  wire [6:0] bit_extender_6_out;
  wire [7:0] bit_extender_1_out, bit_extender_2_out, demultiplexer_1_out0, demultiplexer_1_out1,
       demultiplexer_4_out0, demultiplexer_4_out1, hex_to_ascii_1_ascii_out, hex_to_ascii_2_ascii_out,
       hex_to_ascii_3_ascii_out, hex_to_ascii_4_ascii_out, hex_to_ascii_5_ascii_out,
       hex_to_ascii_6_ascii_out, hex_to_ascii_7_ascii_out, hex_to_ascii_8_ascii_out,
       hex_to_ascii_9_ascii_out, hex_to_ascii_10_ascii_out, multiplexer_2_out, multiplexer_3_out,
       multiplexer_9_out_2, multiplexer_9_out_3, multiplexer_16_out, multiplexer_22_out,
       program_step_controller_8b_1_out, program_step_controller_8b_2_out, program_step_controller_8b_3_out;
  wire [31:0] A_q, B_q, demultiplexer_6_out0, demultiplexer_6_out1, demultiplexer_7_out0,
       demultiplexer_7_out1, demultiplexer_8_out0, demultiplexer_8_out1, demultiplexer_9_out0,
       demultiplexer_9_out1, fib_rom_1_a_2, fib_rom_1_b_2, fib_rom_1_c_2, fib_rom_1_d_2, multiplexer_5_out,
       multiplexer_6_out, multiplexer_7_out, multiplexer_8_out, multiplexer_10_out, multiplexer_11_out,
       multiplexer_18_out, multiplexer_19_out, multiplexer_20_out, multiplexer_21_out, multiplexer_24_out,
       program_mem_1_a_2, program_mem_1_b_2, program_mem_1_c_2, program_mem_1_d_2;

  not not_1 (not_1_out, Write_rom_out_to_PM);
  and and_1 (and_1_out, clock_low_speed, and_5_out);
  Clock High_speed__x (.out(High_speed__x_out));
  buf buffer_1 (buffer_1_out, buffer_8_out);
  buf buffer_2 (buffer_2_out, buffer_1_out);
  buf buffer_3 (buffer_3_out, buffer_2_out);
  buf buffer_4 (buffer_4_out, buffer_12_out);
  buf buffer_5 (buffer_5_out, buffer_4_out);
  buf buffer_6 (buffer_6_out, buffer_5_out);
  and and_2 (and_2_out, not_1_out, and_4_out);
  and and_3 (clock_high_speed, High_speed__x_out, run);
  Bit_Extender #(.in_width(32), .out_width(8)) bit_extender_1 (.in(direct_ReadMux_Out), .out(bit_extender_1_out));
  buf buffer_7 (buffer_7_out, or_1_out);
  buf buffer_8 (buffer_8_out, buffer_7_out);
  buf buffer_9 (buffer_9_out, buffer_10_out);
  buf buffer_10 (buffer_10_out, buffer_3_out);
  buf buffer_11 (buffer_11_out, buffer_9_out);
  buf buffer_12 (buffer_12_out, buffer_13_out);
  buf buffer_13 (buffer_13_out, buffer_11_out);
  buf buffer_14 (buffer_14_out, buffer_6_out);
  Multiplexer #(.width(8), .enable("false")) multiplexer_1 (
    .in0(program_step_controller_8b_1_out), .in1(Programing_Q), .out(current_step), .sel(\program ));
  program_step_controller_8b program_step_controller_8b_1 (
    .reset(reset_system), .step(and_1_out), .Out(program_step_controller_8b_1_out), .goto(and_2_out),
    .goto_Q(bit_extender_2_out));
  program_step_controller_8b program_step_controller_8b_2 (
    .reset(not_2_out), .step(clock_high_speed), .Out(program_step_controller_8b_2_out));  // open: goto, goto_Q
  Multiplexer #(.width(8), .enable("false")) multiplexer_2 (
    .in0(multiplexer_9_out_2), .in1(bit_extender_1_out), .out(multiplexer_2_out), .sel(multiplexer_8_out[6]));
  or or_1 (or_1_out, \program , and_6_out);
  and and_4 (and_4_out, or_2_out, not_4_out, and_1_out);
  and and_5 (and_5_out, not_4_out, run);
  Comparator comparator_1 (.a(program_step_controller_8b_2_out), .b(8'hb), .lt(comparator_1_lt));  // open: gt, eq
  not not_2 (not_2_out, comparator_1_lt);
  T_Flip_Flop t_ff_1 (.clk(not_2_out), .T(1'b1), .Q(clock_low_speed));  // open: Qn, preset, reset, en
  Multiplexer #(.width(8), .enable("false")) multiplexer_3 (
    .in0(multiplexer_9_out_3), .in1(bit_extender_1_out), .out(multiplexer_3_out), .sel(multiplexer_8_out[5]));
  and and_6 (and_6_out, and_1_out, run);
  Comparator #(.width(32), .mode("unsigned")) comparator_2 (
    .a(direct_ALU_out), .b(32'h1), .eq(comparator_2_eq));  // open: gt, lt
  on_finder_8b on_finder_8b_1 (.in(bit_extender_2_out), .on(on_finder_8b_1_on));
  Bit_Extender #(.in_width(32), .out_width(8)) bit_extender_2 (.in(multiplexer_5_out), .out(bit_extender_2_out));
  Multiplexer #(.width(4), .enable("false")) multiplexer_4 (
    .in0(multiplexer_9_out_6), .in1(bit_extender_3_out), .out(multiplexer_4_out), .sel(multiplexer_8_out[4]));
  Bit_Extender #(.in_width(32), .out_width(4)) bit_extender_3 (.in(direct_ReadMux_Out), .out(bit_extender_3_out));
  or or_2 (or_2_out, and_7_out, and_8_out);
  and and_7 (and_7_out, comparator_2_eq, on_finder_8b_1_on);
  and and_8 (and_8_out, not_3_out, on_finder_8b_1_on);
  not not_3 (not_3_out, multiplexer_9_out[0]);
  Multiplexer #(.width(32), .enable("false")) multiplexer_5 (
    .in0(multiplexer_6_out), .in1(direct_ReadMux_Out), .out(multiplexer_5_out), .sel(multiplexer_8_out[7]));
  not not_4 (not_4_out, \program );
  buf buffer_15 (buffer_15_out, buffer_16_out);
  buf buffer_16 (buffer_16_out, buffer_19_out);
  buf buffer_17 (buffer_17_out, buffer_15_out);
  assign not_5_out = ~not_7_out;  // NOT_Gate not_5, 3 bits wide
  assign not_6_out = ~not_5_out;  // NOT_Gate not_6, 3 bits wide
  assign not_7_out = ~not_19_out;  // NOT_Gate not_7, 3 bits wide
  assign {not_8_out[4:3], not_8_out[0]} = ~not_6_out;  // NOT_Gate not_8, 3 bits wide
  assign not_9_out = ~not_15_out;  // NOT_Gate not_9, 3 bits wide
  assign not_10_out = ~not_9_out;  // NOT_Gate not_10, 3 bits wide
  assign not_11_out = ~not_10_out;  // NOT_Gate not_11, 3 bits wide
  assign not_12_out = ~not_30_out;  // NOT_Gate not_12, 3 bits wide
  assign not_13_out = ~not_12_out;  // NOT_Gate not_13, 3 bits wide
  assign not_14_out = ~not_13_out;  // NOT_Gate not_14, 3 bits wide
  assign not_15_out = ~not_14_out;  // NOT_Gate not_15, 3 bits wide
  assign not_16_out = ~{multiplexer_9_out_7[4:3], multiplexer_9_out_7[0]};  // NOT_Gate not_16, 3 bits wide
  assign not_17_out = ~not_16_out;  // NOT_Gate not_17, 3 bits wide
  assign not_18_out = ~not_17_out;  // NOT_Gate not_18, 3 bits wide
  buf buffer_18 (buffer_18_out, buffer_21_out);
  buf buffer_19 (buffer_19_out, buffer_20_out);
  buf buffer_20 (buffer_20_out, buffer_18_out);
  buf buffer_21 (buffer_21_out, buffer_29_out);
  buf buffer_22 (buffer_22_out, buffer_23_out);
  buf buffer_23 (buffer_23_out, buffer_25_out);
  buf buffer_24 (buffer_24_out, buffer_22_out);
  buf buffer_25 (buffer_25_out, buffer_17_out);
  and and_9 (and_9_out[1], RESET_PROGRAM_MEMORY, reset_safety);
  and and_10 (and_10_out, set, \program );
  assign not_19_out = ~not_20_out;  // NOT_Gate not_19, 3 bits wide
  assign not_20_out = ~not_21_out;  // NOT_Gate not_20, 3 bits wide
  assign not_21_out = ~not_22_out;  // NOT_Gate not_21, 3 bits wide
  assign not_22_out = ~not_37_out;  // NOT_Gate not_22, 3 bits wide
  assign not_23_out = ~not_25_out;  // NOT_Gate not_23, 3 bits wide
  assign not_24_out = ~not_11_out;  // NOT_Gate not_24, 3 bits wide
  assign not_25_out = ~not_24_out;  // NOT_Gate not_25, 3 bits wide
  assign not_26_out = ~not_23_out;  // NOT_Gate not_26, 3 bits wide
  assign not_27_out = ~not_28_out;  // NOT_Gate not_27, 3 bits wide
  assign not_28_out = ~not_45_out;  // NOT_Gate not_28, 3 bits wide
  assign not_29_out = ~not_27_out;  // NOT_Gate not_29, 3 bits wide
  assign not_30_out = ~not_29_out;  // NOT_Gate not_30, 3 bits wide
  assign not_31_out = ~not_34_out;  // NOT_Gate not_31, 3 bits wide
  assign not_32_out = ~not_18_out;  // NOT_Gate not_32, 3 bits wide
  assign not_33_out = ~not_31_out;  // NOT_Gate not_33, 3 bits wide
  assign not_34_out = ~not_32_out;  // NOT_Gate not_34, 3 bits wide
  buf buffer_26 (buffer_26_out, buffer_27_out);
  buf buffer_27 (buffer_27_out, buffer_28_out);
  buf buffer_28 (buffer_28_out, buffer_35_out);
  buf buffer_29 (buffer_29_out, buffer_26_out);
  buf buffer_30 (buffer_30_out, buffer_31_out);
  buf buffer_31 (buffer_31_out, buffer_32_out);
  buf buffer_32 (buffer_32_out, buffer_24_out);
  buf buffer_33 (buffer_33_out, buffer_30_out);
  assign not_35_out = ~not_51_out;  // NOT_Gate not_35, 3 bits wide
  assign not_36_out = ~not_35_out;  // NOT_Gate not_36, 3 bits wide
  assign not_37_out = ~not_38_out;  // NOT_Gate not_37, 3 bits wide
  assign not_38_out = ~not_36_out;  // NOT_Gate not_38, 3 bits wide
  assign not_39_out = ~not_41_out;  // NOT_Gate not_39, 3 bits wide
  assign not_40_out = ~not_42_out;  // NOT_Gate not_40, 3 bits wide
  assign not_41_out = ~not_40_out;  // NOT_Gate not_41, 3 bits wide
  assign not_42_out = ~not_26_out;  // NOT_Gate not_42, 3 bits wide
  assign not_43_out = ~not_44_out;  // NOT_Gate not_43, 3 bits wide
  assign not_44_out = ~not_46_out;  // NOT_Gate not_44, 3 bits wide
  assign not_45_out = ~not_43_out;  // NOT_Gate not_45, 3 bits wide
  assign not_46_out = ~not_61_out;  // NOT_Gate not_46, 3 bits wide
  assign not_47_out = ~not_49_out;  // NOT_Gate not_47, 3 bits wide
  assign not_48_out = ~not_50_out;  // NOT_Gate not_48, 3 bits wide
  assign not_49_out = ~not_48_out;  // NOT_Gate not_49, 3 bits wide
  assign not_50_out = ~not_33_out;  // NOT_Gate not_50, 3 bits wide
  buf buffer_34 (buffer_34_out, buffer_43_out);
  buf buffer_35 (buffer_35_out, buffer_37_out);
  buf buffer_36 (buffer_36_out, buffer_34_out);
  buf buffer_37 (buffer_37_out, buffer_36_out);
  buf buffer_38 (buffer_38_out, buffer_40_out);
  buf buffer_39 (buffer_39_out, buffer_33_out);
  buf buffer_40 (buffer_40_out, buffer_41_out);
  buf buffer_41 (buffer_41_out, buffer_39_out);
  assign not_51_out = ~not_52_out;  // NOT_Gate not_51, 3 bits wide
  assign not_52_out = ~not_53_out;  // NOT_Gate not_52, 3 bits wide
  assign not_53_out = ~not_54_out;  // NOT_Gate not_53, 3 bits wide
  assign not_54_out = ~not_67_out;  // NOT_Gate not_54, 3 bits wide
  assign not_55_out = ~not_58_out;  // NOT_Gate not_55, 3 bits wide
  assign not_56_out = ~not_39_out;  // NOT_Gate not_56, 3 bits wide
  assign not_57_out = ~not_55_out;  // NOT_Gate not_57, 3 bits wide
  assign not_58_out = ~not_56_out;  // NOT_Gate not_58, 3 bits wide
  assign not_59_out = ~not_62_out;  // NOT_Gate not_59, 3 bits wide
  assign not_60_out = ~not_59_out;  // NOT_Gate not_60, 3 bits wide
  assign not_61_out = ~not_60_out;  // NOT_Gate not_61, 3 bits wide
  assign not_62_out = ~not_68_out;  // NOT_Gate not_62, 3 bits wide
  assign not_63_out = ~not_47_out;  // NOT_Gate not_63, 3 bits wide
  assign not_64_out = ~not_66_out;  // NOT_Gate not_64, 3 bits wide
  assign not_65_out = ~not_63_out;  // NOT_Gate not_65, 3 bits wide
  assign not_66_out = ~not_65_out;  // NOT_Gate not_66, 3 bits wide
  buf buffer_42 (buffer_42_out, buffer_44_out);
  buf buffer_43 (buffer_43_out, buffer_42_out);
  buf buffer_44 (buffer_44_out, buffer_45_out);
  buf buffer_45 (buffer_45_out, buffer_50_out);
  buf buffer_46 (buffer_46_out, buffer_49_out);
  buf buffer_47 (buffer_47_out, buffer_38_out);
  buf buffer_48 (buffer_48_out, buffer_47_out);
  buf buffer_49 (buffer_49_out, buffer_48_out);
  assign not_67_out = ~not_57_out;  // NOT_Gate not_67, 3 bits wide
  assign not_68_out = ~not_64_out;  // NOT_Gate not_68, 3 bits wide
  Multiplexer #(.width(32), .enable("false")) multiplexer_6 (
    .in0(PM_D_out__Goto), .in1({32{1'b0}}), .out(multiplexer_6_out), .sel(\program ));
  Multiplexer #(.width(32), .enable("false")) multiplexer_7 (
    .in0(PM_C_out__Constant), .in1({32{1'b0}}), .out(multiplexer_7_out), .sel(\program ));
  Multiplexer #(.width(32), .enable("false")) multiplexer_8 (
    .in0(PM_B_out__Output_expansion), .in1({32{1'b0}}), .out(multiplexer_8_out), .sel(\program ));
  Multiplexer #(.width(32), .enable("false")) multiplexer_9 (
    .in0(PM_A_out__Controls), .in1({32{1'b0}}),
    .out({multiplexer_9_out_2, multiplexer_9_out_3, multiplexer_9_out_4, multiplexer_9_out_5, multiplexer_9_out_6, multiplexer_9_out_7[4:3], not_8_out[2:1], multiplexer_9_out_7[0], multiplexer_9_out[0]}),
    .sel(\program ));
  Bit_Extender #(.in_width(32), .out_width(2)) bit_extender_4 (.in(multiplexer_8_out), .out(bit_extender_4_out));
  buf buffer_50 (buffer_50_out, buffer_51_out);
  buf buffer_51 (buffer_51_out, buffer_52_out);
  buf buffer_52 (buffer_52_out, buffer_53_out);
  buf buffer_53 (buffer_53_out, buffer_58_out);
  buf buffer_54 (buffer_54_out, buffer_57_out);
  buf buffer_55 (buffer_55_out, buffer_46_out);
  buf buffer_56 (buffer_56_out, buffer_55_out);
  buf buffer_57 (buffer_57_out, buffer_56_out);
  Multiplexer #(.width(32), .enable("false")) multiplexer_10 (
    .in0({32{1'b0}}), .in1(multiplexer_11_out), .out(multiplexer_10_out), .sel(multiplexer_8_out[2]));
  Multiplexer #(.select(2), .width(32), .enable("false")) multiplexer_11 (
    .in0(direct_RAM_Out), .in1(direct_ReadMux_Out), .in2(direct_ALU_Zero), .in3(direct_ALU_out),
    .out(multiplexer_11_out), .sel(bit_extender_4_out));
  buf buffer_58 (buffer_58_out, multiplexer_8_out[2]);
  buf buffer_59 (buffer_59_out, buffer_61_out);
  buf buffer_60 (buffer_60_out, buffer_54_out);
  buf buffer_61 (buffer_61_out, buffer_60_out);
  Register #(.width(32)) register_1 (
    .D(multiplexer_10_out), .Q(BIN__out), .clk(buffer_59_out), .clr(reset_system));  // open: en
  digit_finder_32b_ns digit_finder_32b_ns_1 (
    .out_2(digit_finder_32b_ns_1_out_2), .out_3(digit_finder_32b_ns_1_out_3),
    .out_4(digit_finder_32b_ns_1_out_4), .out_5(digit_finder_32b_ns_1_out_5),
    .out_6(digit_finder_32b_ns_1_out_6), .out_7(digit_finder_32b_ns_1_out_7),
    .out_8(digit_finder_32b_ns_1_out_8), .out_9(digit_finder_32b_ns_1_out_9),
    .out_10(digit_finder_32b_ns_1_out_10), .out_11(digit_finder_32b_ns_1_out_11), .in_1(BIN__out));
  fib_rom fib_rom_1 (
    .D(demultiplexer_9_out1), .C(demultiplexer_8_out1), .B(demultiplexer_7_out1), .A(demultiplexer_6_out1),
    .A_2(fib_rom_1_a_2), .B_2(fib_rom_1_b_2), .C_2(fib_rom_1_c_2), .D_2(fib_rom_1_d_2),
    .R(demultiplexer_5_out1), .R_Q(demultiplexer_4_out1), .Rst(demultiplexer_3_out1),
    .Wr(demultiplexer_2_out1), .Wr_Q(demultiplexer_1_out1));
  Demultiplexer #(.width(8), .enable("false")) demultiplexer_1 (
    .out0(demultiplexer_1_out0), .out1(demultiplexer_1_out1), .in(Programing_Q), .sel(run_from_rom));
  Demultiplexer #(.enable("false")) demultiplexer_2 (
    .out0(demultiplexer_2_out0), .out1(demultiplexer_2_out1), .in(and_10_out), .sel(run_from_rom));
  Demultiplexer #(.enable("false")) demultiplexer_3 (
    .out0(demultiplexer_3_out0), .out1(demultiplexer_3_out1), .in(and_9_out[1]), .sel(run_from_rom));
  Demultiplexer #(.width(8), .enable("false")) demultiplexer_4 (
    .out0(demultiplexer_4_out0), .out1(demultiplexer_4_out1), .in(current_step), .sel(run_from_rom));
  Demultiplexer #(.enable("false")) demultiplexer_5 (
    .out0(demultiplexer_5_out0), .out1(demultiplexer_5_out1), .in(buffer_14_out), .sel(run_from_rom));
  Multiplexer #(.width(32), .enable("false")) multiplexer_12 (
    .in0(program_mem_1_d_2), .in1(fib_rom_1_d_2), .out(PM_D_out__Goto), .sel(run_from_rom));
  Multiplexer #(.width(32), .enable("false")) multiplexer_13 (
    .in0(program_mem_1_c_2), .in1(fib_rom_1_c_2), .out(PM_C_out__Constant), .sel(run_from_rom));
  Multiplexer #(.width(32), .enable("false")) multiplexer_14 (
    .in0(program_mem_1_b_2), .in1(fib_rom_1_b_2), .out(PM_B_out__Output_expansion), .sel(run_from_rom));
  Multiplexer #(.width(32), .enable("false")) multiplexer_15 (
    .in0(program_mem_1_a_2), .in1(fib_rom_1_a_2), .out(PM_A_out__Controls), .sel(run_from_rom));
  Demultiplexer #(.width(32), .enable("false")) demultiplexer_6 (
    .out0(demultiplexer_6_out0), .out1(demultiplexer_6_out1), .in(PM_A_in), .sel(run_from_rom));
  Demultiplexer #(.width(32), .enable("false")) demultiplexer_7 (
    .out0(demultiplexer_7_out0), .out1(demultiplexer_7_out1), .in(PM_B_in), .sel(run_from_rom));
  Demultiplexer #(.width(32), .enable("false")) demultiplexer_8 (
    .out0(demultiplexer_8_out0), .out1(demultiplexer_8_out1), .in(PM_C_in), .sel(run_from_rom));
  Demultiplexer #(.width(32), .enable("false")) demultiplexer_9 (
    .out0(demultiplexer_9_out0), .out1(demultiplexer_9_out1), .in(PM_D_in), .sel(run_from_rom));
  Hex_Digit_Display hex_digit_display_1 (.value(digit_finder_32b_ns_1_out_11));  // open: dp
  buf buffer_62 (buffer_62_out, buffer_63_out);
  buf buffer_63 (buffer_63_out, buffer_64_out);
  buf buffer_64 (buffer_64_out, buffer_65_out);
  buf buffer_65 (buffer_65_out, buffer_66_out);
  buf buffer_66 (buffer_66_out, buffer_69_out);
  buf buffer_67 (buffer_67_out, buffer_68_out);
  buf buffer_68 (buffer_68_out, demultiplexer_5_out1);
  buf buffer_69 (buffer_69_out, buffer_67_out);
  Hex_Digit_Display hex_digit_display_2 (.value(digit_finder_32b_ns_1_out_10));  // open: dp
  Multiplexer #(.width(8), .enable("false")) multiplexer_16 (
    .in0(demultiplexer_1_out0), .in1(demultiplexer_4_out1), .out(multiplexer_16_out),
    .sel(Write_rom_out_to_PM));
  Multiplexer #(.enable("false")) multiplexer_17 (
    .in0(demultiplexer_2_out0), .in1(buffer_62_out), .out(multiplexer_17_out), .sel(Write_rom_out_to_PM));
  Multiplexer #(.width(32), .enable("false")) multiplexer_18 (
    .in0(demultiplexer_6_out0), .in1(fib_rom_1_a_2), .out(multiplexer_18_out), .sel(Write_rom_out_to_PM));
  Multiplexer #(.width(32), .enable("false")) multiplexer_19 (
    .in0(demultiplexer_7_out0), .in1(fib_rom_1_b_2), .out(multiplexer_19_out), .sel(Write_rom_out_to_PM));
  Multiplexer #(.width(32), .enable("false")) multiplexer_20 (
    .in0(demultiplexer_8_out0), .in1(fib_rom_1_c_2), .out(multiplexer_20_out), .sel(Write_rom_out_to_PM));
  Multiplexer #(.width(32), .enable("false")) multiplexer_21 (
    .in0(demultiplexer_9_out0), .in1(fib_rom_1_d_2), .out(multiplexer_21_out), .sel(Write_rom_out_to_PM));
  Register #(.width(32)) register_2 (
    .D(direct_ALU_out), .Q(ALU_Out), .clk(buffer_59_out), .clr(reset_system));  // open: en
  Hex_Digit_Display hex_digit_display_3 (.value(digit_finder_32b_ns_1_out_9));  // open: dp
  Hex_Digit_Display hex_digit_display_4 (.value(digit_finder_32b_ns_1_out_8));  // open: dp
  Register #(.width(32)) register_3 (
    .D(direct_ALU_Zero), .Q(ALU_Zero), .clk(buffer_59_out), .clr(reset_system));  // open: en
  Hex_Digit_Display hex_digit_display_5 (.value(digit_finder_32b_ns_1_out_6));  // open: dp
  Hex_Digit_Display hex_digit_display_6 (.value(digit_finder_32b_ns_1_out_7));  // open: dp
  program_mem program_mem_1 (
    .Rst(demultiplexer_3_out0), .R_Q(demultiplexer_4_out0), .R(demultiplexer_5_out0),
    .Wr_Q(multiplexer_16_out), .Wr(multiplexer_17_out), .D(multiplexer_21_out), .C(multiplexer_20_out),
    .B(multiplexer_19_out), .A(multiplexer_18_out), .A_2(program_mem_1_a_2), .B_2(program_mem_1_b_2),
    .C_2(program_mem_1_c_2), .D_2(program_mem_1_d_2));
  Register #(.width(32)) register_4 (
    .D(direct_ReadMux_Out), .Q(ReadMux_Out), .clk(buffer_59_out), .clr(reset_system));  // open: en
  Hex_Digit_Display hex_digit_display_7 (.value(digit_finder_32b_ns_1_out_5));  // open: dp
  Register #(.width(32)) register_5 (
    .D(direct_RAM_Out), .Q(RAM_Out), .clk(buffer_59_out), .clr(reset_system));  // open: en
  Hex_Digit_Display hex_digit_display_8 (.value(digit_finder_32b_ns_1_out_3));  // open: dp
  Hex_Digit_Display hex_digit_display_9 (.value(digit_finder_32b_ns_1_out_4));  // open: dp
  not not_69 (not_69_out, clock_low_speed);
  Hex_Digit_Display hex_digit_display_10 (.value(digit_finder_32b_ns_1_out_2));  // open: dp
  or or_3 (or_3_out, reset_system, not_69_out);
  and and_11 (and_11_out, clock_low_speed, buffer_59_out, clock_high_speed);
  TTY tty_1 (.data(bit_extender_6_out), .clk(and_11_out), .clr(reset_system));  // open: we
  HEX_to_ascii hex_to_ascii_1 (.BIN_IN(digit_finder_32b_ns_1_out_11), .ASCII_out(hex_to_ascii_1_ascii_out));
  HEX_to_ascii hex_to_ascii_2 (.BIN_IN(digit_finder_32b_ns_1_out_10), .ASCII_out(hex_to_ascii_2_ascii_out));
  HEX_to_ascii hex_to_ascii_3 (.BIN_IN(digit_finder_32b_ns_1_out_9), .ASCII_out(hex_to_ascii_3_ascii_out));
  HEX_to_ascii hex_to_ascii_4 (.BIN_IN(digit_finder_32b_ns_1_out_8), .ASCII_out(hex_to_ascii_4_ascii_out));
  HEX_to_ascii hex_to_ascii_5 (.BIN_IN(digit_finder_32b_ns_1_out_7), .ASCII_out(hex_to_ascii_5_ascii_out));
  Register #(.width(32)) A (
    .D(direct_ReadMux_Out), .Q(A_q), .clk(not_8_out[3]), .clr(multiplexer_8_out[3]));  // open: en
  Register #(.width(32)) B (
    .D(direct_ReadMux_Out), .Q(B_q), .clk(not_8_out[4]), .clr(multiplexer_8_out[3]));  // open: en
  program_step_controller_8b program_step_controller_8b_3 (
    .reset(or_3_out), .step(clock_high_speed), .Out(program_step_controller_8b_3_out), .goto(1'b0),
    .goto_Q({8{1'b0}}));
  Bit_Extender #(.out_width(4)) bit_extender_5 (.in(program_step_controller_8b_3_out), .out(bit_extender_5_out));
  Multiplexer #(.select(4), .width(8), .enable("false")) multiplexer_22 (
    .in0(hex_to_ascii_1_ascii_out), .in1(hex_to_ascii_2_ascii_out), .in2(hex_to_ascii_3_ascii_out),
    .in3(hex_to_ascii_4_ascii_out), .in4(hex_to_ascii_5_ascii_out), .in5(hex_to_ascii_6_ascii_out),
    .in6(hex_to_ascii_7_ascii_out), .in7(hex_to_ascii_8_ascii_out), .in8(hex_to_ascii_9_ascii_out),
    .in9(hex_to_ascii_10_ascii_out), .in10(8'hd), .out(multiplexer_22_out), .sel(bit_extender_5_out));  // open: in11, in12, in13, in14, in15
  HEX_to_ascii hex_to_ascii_6 (.BIN_IN(digit_finder_32b_ns_1_out_6), .ASCII_out(hex_to_ascii_6_ascii_out));
  HEX_to_ascii hex_to_ascii_7 (.BIN_IN(digit_finder_32b_ns_1_out_5), .ASCII_out(hex_to_ascii_7_ascii_out));
  HEX_to_ascii hex_to_ascii_8 (.BIN_IN(digit_finder_32b_ns_1_out_4), .ASCII_out(hex_to_ascii_8_ascii_out));
  HEX_to_ascii hex_to_ascii_9 (.BIN_IN(digit_finder_32b_ns_1_out_3), .ASCII_out(hex_to_ascii_9_ascii_out));
  HEX_to_ascii hex_to_ascii_10 (.BIN_IN(digit_finder_32b_ns_1_out_2), .ASCII_out(hex_to_ascii_10_ascii_out));
  ALU_32b_ns alu_32b_ns_1 (
    .A_in(A_q), .B_in(B_q), .\output (direct_ALU_out), .Zero(direct_ALU_Zero), .Fnctn(multiplexer_4_out));
  Bit_Extender #(.out_width(7)) bit_extender_6 (.in(multiplexer_22_out), .out(bit_extender_6_out));
  Multiplexer #(.select(4), .width(32), .enable("false")) multiplexer_23 (
    .in0(direct_RAM_Out), .in1(multiplexer_7_out), .in2(user_0_select_2), .in3(user_1_select_3),
    .in4(user_2_select_4), .in5(user_3_select_5), .in6(user_4_select_6), .in7(user_5_select_7),
    .in8(user_6_select_8), .in9(user_7_select_9), .in10(user_8_select_10), .in11(user_9_select_11),
    .in12(user_10_select_12), .in13(user_11_select_13), .in14(user_12_select_14), .in15(user_13_select_15),
    .out(direct_ReadMux_Out), .sel(multiplexer_9_out_4));
  Multiplexer #(.select(2), .width(32), .enable("false")) multiplexer_24 (
    .in0(direct_ALU_out), .in1(direct_ALU_Zero), .in2(direct_ReadMux_Out), .in3(multiplexer_7_out),
    .out(multiplexer_24_out), .sel(multiplexer_9_out_5));
  memory_32bx256 memory_32bx256_1 (
    .out(direct_RAM_Out), .In(multiplexer_24_out), .reset(not_8_out[2]), .wright(not_8_out[0]),
    .wright_Q(multiplexer_2_out), .read(not_8_out[1]), .read_Q(multiplexer_3_out));

  // Notes on the sheet:
  //   D
  //   DEC. out
  //   paper tape
  //   Write Mux
  //   Read Mux
  //   Ram
endmodule

module program_mem (
  input  Rst,
  input  [7:0] R_Q,
  input  R,
  input  [7:0] Wr_Q,
  input  Wr,
  input  [31:0] D,
  input  [31:0] C,
  input  [31:0] B,
  input  [31:0] A,
  output [31:0] A_2,
  output [31:0] B_2,
  output [31:0] C_2,
  output [31:0] D_2
);

  memory_32bx256 u_A (.out(A_2), .In(A), .reset(Rst), .wright(Wr), .wright_Q(Wr_Q), .read(R), .read_Q(R_Q));
  memory_32bx256 u_B (.out(B_2), .In(B), .reset(Rst), .wright(Wr), .wright_Q(Wr_Q), .read(R), .read_Q(R_Q));
  memory_32bx256 u_C (.out(C_2), .In(C), .reset(Rst), .wright(Wr), .wright_Q(Wr_Q), .read(R), .read_Q(R_Q));
  memory_32bx256 u_D (.out(D_2), .In(D), .reset(Rst), .wright(Wr), .wright_Q(Wr_Q), .read(R), .read_Q(R_Q));
endmodule

module program_step_controller_8b (
  input  [7:0] goto_Q,
  input  goto,
  input  reset,
  input  step,
  output [7:0] Out
);

  wire d_ff_1_q, not_1_out;
  wire [7:0] adder_1_out, goto_Q_buf_q, multiplexer_1_out, step_buf_q;

  Register goto_Q_buf (.D(goto_Q), .Q(goto_Q_buf_q), .clk(goto), .clr(reset));  // open: en
  Adder adder_1 (.a(Out), .b(8'h1), .out(adder_1_out));  // open: cin, cout
  Register #(.trigger("high")) step_buf (
    .D(multiplexer_1_out), .Q(step_buf_q), .clk(not_1_out), .clr(reset));  // open: en
  Multiplexer #(.width(8), .enable("false")) multiplexer_1 (
    .in0(adder_1_out), .in1(goto_Q_buf_q), .out(multiplexer_1_out), .sel(d_ff_1_q));
  not not_1 (not_1_out, step);
  Register #(.trigger("high")) u_step (.D(step_buf_q), .Q(Out), .clk(step), .clr(reset));  // open: en
  D_Flip_Flop #(.trigger("falling")) d_ff_1 (
    .clk(step), .D(goto), .Q(d_ff_1_q), .reset(reset));  // open: Qn, preset, en
endmodule

module ALU_32b_ns (
  input  [31:0] A_in,
  input  [3:0] Fnctn,
  input  [31:0] B_in,
  output [31:0] \output ,
  output [31:0] Zero
);

  wire adder_1_cout, comparator_1_eq, comparator_1_gt, comparator_1_lt, decoder_1_out0, decoder_1_out2,
       multiplexer_2_out, not_1_out, not_2_out, on_finder_32b_1_out_2, on_finder_32b_2_out_2, or_2_out,
       or_3_out;
  wire [31:0] adder_1_out, and_1_out, bit_extender_1_out, bit_extender_2_out, bit_extender_3_out,
       bit_extender_4_out, bit_extender_5_out, bit_extender_6_out, divider_1_out, multiplier_1_cout,
       multiplier_1_out, nand_1_out, nor_1_out, or_1_out, subtractor_1_out, xnor_1_out, xor_1_out;

  Adder #(.width(32)) adder_1 (.a(A_in), .b(B_in), .out(adder_1_out), .cout(adder_1_cout));  // open: cin
  Subtractor #(.width(32)) subtractor_1 (.a(A_in), .b(B_in), .out(subtractor_1_out));  // open: bin, bout
  Multiplier #(.width(32)) multiplier_1 (
    .a(A_in), .b(B_in), .out(multiplier_1_out), .cout(multiplier_1_cout));  // open: cin
  Divider #(.width(32)) divider_1 (.a(A_in), .b(B_in), .out(divider_1_out));  // open: upper, rem
  Comparator #(.width(32), .mode("unsigned")) comparator_1 (
    .a(A_in), .b(B_in), .gt(comparator_1_gt), .eq(comparator_1_eq), .lt(comparator_1_lt));
  assign and_1_out = A_in & B_in;  // AND_Gate and_1, 32 bits wide
  assign or_1_out = A_in | B_in;  // OR_Gate or_1, 32 bits wide
  assign xor_1_out = A_in ^ B_in;  // XOR_Gate xor_1, 32 bits wide
  assign nand_1_out = ~(A_in & B_in);  // NAND_Gate nand_1, 32 bits wide
  assign nor_1_out = ~(A_in | B_in);  // NOR_Gate nor_1, 32 bits wide
  assign xnor_1_out = ~(A_in ^ B_in);  // XNOR_Gate xnor_1, 32 bits wide
  assign bit_extender_1_out = {{31{1'b0}}, comparator_1_gt};  // Bit_Extender bit_extender_1
  assign bit_extender_2_out = {{31{1'b0}}, comparator_1_eq};  // Bit_Extender bit_extender_2
  assign bit_extender_3_out = {{31{1'b0}}, comparator_1_lt};  // Bit_Extender bit_extender_3
  not not_1 (not_1_out, comparator_1_eq);
  assign bit_extender_4_out = {{31{1'b0}}, not_1_out};  // Bit_Extender bit_extender_4
  or or_2 (or_2_out, comparator_1_gt, comparator_1_eq);
  assign bit_extender_5_out = {{31{1'b0}}, or_2_out};  // Bit_Extender bit_extender_5
  or or_3 (or_3_out, comparator_1_lt, comparator_1_eq);
  assign bit_extender_6_out = {{31{1'b0}}, or_3_out};  // Bit_Extender bit_extender_6
  Multiplexer #(.select(4), .width(32), .enable("false")) multiplexer_1 (
    .in0(adder_1_out), .in1(subtractor_1_out), .in2(multiplier_1_out), .in3(divider_1_out),
    .in4(bit_extender_1_out), .in5(bit_extender_2_out), .in6(bit_extender_3_out), .in7(bit_extender_4_out),
    .in8(bit_extender_5_out), .in9(bit_extender_6_out), .in10(and_1_out), .in11(or_1_out), .in12(xor_1_out),
    .in13(nand_1_out), .in14(nor_1_out), .in15(xnor_1_out), .out(\output ), .sel(Fnctn));
  on_finder_32b on_finder_32b_1 (.in_1(\output ), .out_2(on_finder_32b_1_out_2));
  Decoder #(.select(4), .enable("false")) decoder_1 (
    .out0(decoder_1_out0), .out2(decoder_1_out2), .sel(Fnctn));  // open: out1, out3, out4, out5, out6, out7, out8, out9, out10, out11, out12, out13, out14, out15
  Multiplexer #(.enable("false")) multiplexer_2 (
    .in0(1'b0), .in1(adder_1_cout), .out(multiplexer_2_out), .sel(decoder_1_out0));
  Multiplexer #(.enable("false")) multiplexer_3 (
    .in0(multiplexer_2_out), .in1(on_finder_32b_2_out_2), .sel(decoder_1_out2));  // open: out
  on_finder_32b on_finder_32b_2 (.in_1(multiplier_1_cout), .out_2(on_finder_32b_2_out_2));
  not not_2 (not_2_out, on_finder_32b_1_out_2);
  assign Zero = {{31{1'b0}}, not_2_out};  // Bit_Extender bit_extender_7
endmodule

module memory_32bx256 (
  input  [31:0] In,
  input  reset,
  input  wright,
  input  [7:0] wright_Q,
  input  read,
  input  [7:0] read_Q,
  output [31:0] out
);

  wire buffer_1_out, buffer_2_out, buffer_3_out, buffer_4_out, buffer_5_out, buffer_6_out, buffer_7_out,
       buffer_8_out, buffer_9_out, buffer_10_out, buffer_11_out, buffer_12_out, demultiplexer_1_out0,
       demultiplexer_1_out1, demultiplexer_1_out2, demultiplexer_1_out3, demultiplexer_1_out4,
       demultiplexer_1_out5, demultiplexer_1_out6, demultiplexer_1_out7, demultiplexer_1_out8,
       demultiplexer_1_out9, demultiplexer_1_out10, demultiplexer_1_out11, demultiplexer_1_out12,
       demultiplexer_1_out13, demultiplexer_1_out14, demultiplexer_1_out15, demultiplexer_2_out0,
       demultiplexer_2_out1, demultiplexer_2_out2, demultiplexer_2_out3, demultiplexer_2_out4,
       demultiplexer_2_out5, demultiplexer_2_out6, demultiplexer_2_out7, demultiplexer_2_out8,
       demultiplexer_2_out9, demultiplexer_2_out10, demultiplexer_2_out11, demultiplexer_2_out12,
       demultiplexer_2_out13, demultiplexer_2_out14, demultiplexer_2_out15, not_1_out, not_2_out, not_3_out,
       not_4_out, not_5_out, not_6_out, not_7_out, not_8_out, not_9_out, not_10_out, not_11_out, not_12_out;
  wire [3:0] bit_extender_1_out, bit_extender_2_out, bit_extender_3_out, bit_extender_4_out;
  wire [7:0] divider_1_out, divider_2_out, multiplier_1_out, multiplier_2_out, subtractor_1_out,
       subtractor_2_out;
  wire [31:0] memory_32bx16_1_out, memory_32bx16_2_out, memory_32bx16_3_out, memory_32bx16_4_out,
       memory_32bx16_5_out, memory_32bx16_6_out, memory_32bx16_7_out, memory_32bx16_8_out,
       memory_32bx16_9_out, memory_32bx16_10_out, memory_32bx16_11_out, memory_32bx16_12_out,
       memory_32bx16_13_out, memory_32bx16_14_out, memory_32bx16_15_out, memory_32bx16_16_out, or_2_out,
       or_3_out, or_4_out, or_5_out;

  buf buffer_1 (buffer_1_out, buffer_3_out);
  buf buffer_2 (buffer_2_out, buffer_1_out);
  buf buffer_3 (buffer_3_out, buffer_5_out);
  buf buffer_4 (buffer_4_out, buffer_10_out);
  buf buffer_5 (buffer_5_out, buffer_4_out);
  buf buffer_6 (buffer_6_out, buffer_7_out);
  buf buffer_7 (buffer_7_out, wright);
  not not_1 (not_1_out, not_2_out);
  not not_2 (not_2_out, not_3_out);
  not not_3 (not_3_out, not_5_out);
  not not_4 (not_4_out, not_10_out);
  not not_5 (not_5_out, not_4_out);
  not not_6 (not_6_out, read);
  not not_7 (not_7_out, not_6_out);
  buf buffer_8 (buffer_8_out, buffer_9_out);
  buf buffer_9 (buffer_9_out, buffer_2_out);
  buf buffer_10 (buffer_10_out, buffer_12_out);
  buf buffer_11 (buffer_11_out, buffer_6_out);
  buf buffer_12 (buffer_12_out, buffer_11_out);
  not not_8 (not_8_out, not_1_out);
  not not_9 (not_9_out, not_8_out);
  not not_10 (not_10_out, not_12_out);
  not not_11 (not_11_out, not_7_out);
  not not_12 (not_12_out, not_11_out);
  Bit_Extender #(.out_width(4)) bit_extender_1 (.in(subtractor_1_out), .out(bit_extender_1_out));
  Bit_Extender #(.out_width(4)) bit_extender_2 (.in(subtractor_2_out), .out(bit_extender_2_out));
  Subtractor subtractor_1 (.a(wright_Q), .b(multiplier_1_out), .out(subtractor_1_out));  // open: bin, bout
  Multiplier multiplier_1 (.a(divider_1_out), .b(8'h10), .out(multiplier_1_out));  // open: cin, cout
  Divider divider_1 (.a(wright_Q), .b(8'h10), .out(divider_1_out));  // open: upper, rem
  Subtractor subtractor_2 (.a(read_Q), .b(multiplier_2_out), .out(subtractor_2_out));  // open: bin, bout
  Multiplier multiplier_2 (.a(divider_2_out), .b(8'h10), .out(multiplier_2_out));  // open: cin, cout
  Divider divider_2 (.a(read_Q), .b(8'h10), .out(divider_2_out));  // open: upper, rem
  Demultiplexer #(.select(4), .enable("false")) demultiplexer_1 (
    .out0(demultiplexer_1_out0), .out1(demultiplexer_1_out1), .out2(demultiplexer_1_out2),
    .out3(demultiplexer_1_out3), .out4(demultiplexer_1_out4), .out5(demultiplexer_1_out5),
    .out6(demultiplexer_1_out6), .out7(demultiplexer_1_out7), .out8(demultiplexer_1_out8),
    .out9(demultiplexer_1_out9), .out10(demultiplexer_1_out10), .out11(demultiplexer_1_out11),
    .out12(demultiplexer_1_out12), .out13(demultiplexer_1_out13), .out14(demultiplexer_1_out14),
    .out15(demultiplexer_1_out15), .in(buffer_8_out), .sel(bit_extender_3_out));
  Bit_Extender #(.out_width(4)) bit_extender_3 (.in(divider_1_out), .out(bit_extender_3_out));
  Demultiplexer #(.select(4), .enable("false")) demultiplexer_2 (
    .out0(demultiplexer_2_out0), .out1(demultiplexer_2_out1), .out2(demultiplexer_2_out2),
    .out3(demultiplexer_2_out3), .out4(demultiplexer_2_out4), .out5(demultiplexer_2_out5),
    .out6(demultiplexer_2_out6), .out7(demultiplexer_2_out7), .out8(demultiplexer_2_out8),
    .out9(demultiplexer_2_out9), .out10(demultiplexer_2_out10), .out11(demultiplexer_2_out11),
    .out12(demultiplexer_2_out12), .out13(demultiplexer_2_out13), .out14(demultiplexer_2_out14),
    .out15(demultiplexer_2_out15), .in(not_9_out), .sel(bit_extender_4_out));
  Bit_Extender #(.out_width(4)) bit_extender_4 (.in(divider_2_out), .out(bit_extender_4_out));
  assign out = or_5_out | or_4_out | or_3_out | or_2_out;  // OR_Gate or_1, 32 bits wide
  memory_32bx16 memory_32bx16_1 (
    .In(In), .write_Q(bit_extender_1_out), .read_Q(bit_extender_2_out), .Out(memory_32bx16_1_out),
    .wright(demultiplexer_1_out0), .read(demultiplexer_2_out0), .reset(reset));
  memory_32bx16 memory_32bx16_2 (
    .In(In), .write_Q(bit_extender_1_out), .read_Q(bit_extender_2_out), .Out(memory_32bx16_2_out),
    .wright(demultiplexer_1_out1), .read(demultiplexer_2_out1), .reset(reset));
  memory_32bx16 memory_32bx16_3 (
    .In(In), .write_Q(bit_extender_1_out), .read_Q(bit_extender_2_out), .Out(memory_32bx16_3_out),
    .wright(demultiplexer_1_out2), .read(demultiplexer_2_out2), .reset(reset));
  memory_32bx16 memory_32bx16_4 (
    .In(In), .write_Q(bit_extender_1_out), .read_Q(bit_extender_2_out), .Out(memory_32bx16_4_out),
    .wright(demultiplexer_1_out3), .read(demultiplexer_2_out3), .reset(reset));
  assign or_2_out = memory_32bx16_1_out | memory_32bx16_2_out | memory_32bx16_3_out | memory_32bx16_4_out;  // OR_Gate or_2, 32 bits wide
  assign or_3_out = memory_32bx16_5_out | memory_32bx16_6_out | memory_32bx16_7_out | memory_32bx16_8_out;  // OR_Gate or_3, 32 bits wide
  memory_32bx16 memory_32bx16_5 (
    .In(In), .write_Q(bit_extender_1_out), .read_Q(bit_extender_2_out), .Out(memory_32bx16_5_out),
    .wright(demultiplexer_1_out4), .read(demultiplexer_2_out4), .reset(reset));
  memory_32bx16 memory_32bx16_6 (
    .In(In), .write_Q(bit_extender_1_out), .read_Q(bit_extender_2_out), .Out(memory_32bx16_6_out),
    .wright(demultiplexer_1_out5), .read(demultiplexer_2_out5), .reset(reset));
  memory_32bx16 memory_32bx16_7 (
    .In(In), .write_Q(bit_extender_1_out), .read_Q(bit_extender_2_out), .Out(memory_32bx16_7_out),
    .wright(demultiplexer_1_out6), .read(demultiplexer_2_out6), .reset(reset));
  memory_32bx16 memory_32bx16_8 (
    .In(In), .write_Q(bit_extender_1_out), .read_Q(bit_extender_2_out), .Out(memory_32bx16_8_out),
    .wright(demultiplexer_1_out7), .read(demultiplexer_2_out7), .reset(reset));
  memory_32bx16 memory_32bx16_9 (
    .In(In), .write_Q(bit_extender_1_out), .read_Q(bit_extender_2_out), .Out(memory_32bx16_9_out),
    .wright(demultiplexer_1_out8), .read(demultiplexer_2_out8), .reset(reset));
  memory_32bx16 memory_32bx16_10 (
    .In(In), .write_Q(bit_extender_1_out), .read_Q(bit_extender_2_out), .Out(memory_32bx16_10_out),
    .wright(demultiplexer_1_out9), .read(demultiplexer_2_out9), .reset(reset));
  memory_32bx16 memory_32bx16_11 (
    .In(In), .write_Q(bit_extender_1_out), .read_Q(bit_extender_2_out), .Out(memory_32bx16_11_out),
    .wright(demultiplexer_1_out10), .read(demultiplexer_2_out10), .reset(reset));
  memory_32bx16 memory_32bx16_12 (
    .In(In), .write_Q(bit_extender_1_out), .read_Q(bit_extender_2_out), .Out(memory_32bx16_12_out),
    .wright(demultiplexer_1_out11), .read(demultiplexer_2_out11), .reset(reset));
  assign or_4_out = memory_32bx16_9_out | memory_32bx16_10_out | memory_32bx16_11_out | memory_32bx16_12_out;  // OR_Gate or_4, 32 bits wide
  memory_32bx16 memory_32bx16_13 (
    .In(In), .write_Q(bit_extender_1_out), .read_Q(bit_extender_2_out), .Out(memory_32bx16_13_out),
    .wright(demultiplexer_1_out12), .read(demultiplexer_2_out12), .reset(reset));
  memory_32bx16 memory_32bx16_14 (
    .In(In), .write_Q(bit_extender_1_out), .read_Q(bit_extender_2_out), .Out(memory_32bx16_14_out),
    .wright(demultiplexer_1_out13), .read(demultiplexer_2_out13), .reset(reset));
  memory_32bx16 memory_32bx16_15 (
    .In(In), .write_Q(bit_extender_1_out), .read_Q(bit_extender_2_out), .Out(memory_32bx16_15_out),
    .wright(demultiplexer_1_out14), .read(demultiplexer_2_out14), .reset(reset));
  memory_32bx16 memory_32bx16_16 (
    .In(In), .write_Q(bit_extender_1_out), .read_Q(bit_extender_2_out), .Out(memory_32bx16_16_out),
    .wright(demultiplexer_1_out15), .read(demultiplexer_2_out15), .reset(reset));
  assign or_5_out = memory_32bx16_13_out | memory_32bx16_14_out | memory_32bx16_15_out | memory_32bx16_16_out;  // OR_Gate or_5, 32 bits wide
endmodule

module memory_32bx16 (
  input  [31:0] In,
  input  reset,
  input  wright,
  input  [3:0] write_Q,
  input  read,
  input  [3:0] read_Q,
  output [31:0] Out
);

  wire buffer_1_out, demultiplexer_1_out0, demultiplexer_1_out1, demultiplexer_1_out2, demultiplexer_1_out3,
       demultiplexer_1_out4, demultiplexer_1_out5, demultiplexer_1_out6, demultiplexer_1_out7,
       demultiplexer_1_out8, demultiplexer_1_out9, demultiplexer_1_out10, demultiplexer_1_out11,
       demultiplexer_1_out12, demultiplexer_1_out13, demultiplexer_1_out14, demultiplexer_1_out15,
       demultiplexer_2_out0, demultiplexer_2_out1, demultiplexer_2_out2, demultiplexer_2_out3,
       demultiplexer_2_out4, demultiplexer_2_out5, demultiplexer_2_out6, demultiplexer_2_out7,
       demultiplexer_2_out8, demultiplexer_2_out9, demultiplexer_2_out10, demultiplexer_2_out11,
       demultiplexer_2_out12, demultiplexer_2_out13, demultiplexer_2_out14, demultiplexer_2_out15, s_r_ff_1_q;
  wire [31:0] multiplexer_1_out, multiplexer_2_out, multiplexer_3_out, multiplexer_4_out, multiplexer_5_out,
       multiplexer_6_out, multiplexer_7_out, multiplexer_8_out, multiplexer_9_out, multiplexer_10_out,
       multiplexer_11_out, multiplexer_12_out, multiplexer_13_out, multiplexer_14_out, multiplexer_15_out,
       multiplexer_16_out, or_2_out, or_3_out, or_4_out, or_5_out, register_1_q, register_2_q, register_3_q,
       register_4_q, register_5_q, register_6_q, register_7_q, register_8_q, register_9_q, register_10_q,
       register_11_q, register_12_q, register_13_q, register_14_q, register_15_q, register_16_q;

  assign Out = or_5_out | or_4_out | or_3_out | or_2_out;  // OR_Gate or_1, 32 bits wide
  S_R_Flip_Flop s_r_ff_1 (
    .S(1'b1), .clk(wright), .R(1'b0), .Q(s_r_ff_1_q), .reset(s_r_ff_1_q));  // open: Qn, preset, en
  Demultiplexer #(.select(4), .enable("false")) demultiplexer_1 (
    .out0(demultiplexer_1_out0), .out1(demultiplexer_1_out1), .out2(demultiplexer_1_out2),
    .out3(demultiplexer_1_out3), .out4(demultiplexer_1_out4), .out5(demultiplexer_1_out5),
    .out6(demultiplexer_1_out6), .out7(demultiplexer_1_out7), .out8(demultiplexer_1_out8),
    .out9(demultiplexer_1_out9), .out10(demultiplexer_1_out10), .out11(demultiplexer_1_out11),
    .out12(demultiplexer_1_out12), .out13(demultiplexer_1_out13), .out14(demultiplexer_1_out14),
    .out15(demultiplexer_1_out15), .in(s_r_ff_1_q), .sel(write_Q));
  buf buffer_1 (buffer_1_out, read);
  Demultiplexer #(.select(4), .enable("false")) demultiplexer_2 (
    .out0(demultiplexer_2_out0), .out1(demultiplexer_2_out1), .out2(demultiplexer_2_out2),
    .out3(demultiplexer_2_out3), .out4(demultiplexer_2_out4), .out5(demultiplexer_2_out5),
    .out6(demultiplexer_2_out6), .out7(demultiplexer_2_out7), .out8(demultiplexer_2_out8),
    .out9(demultiplexer_2_out9), .out10(demultiplexer_2_out10), .out11(demultiplexer_2_out11),
    .out12(demultiplexer_2_out12), .out13(demultiplexer_2_out13), .out14(demultiplexer_2_out14),
    .out15(demultiplexer_2_out15), .in(buffer_1_out), .sel(read_Q));
  Register #(.width(32)) register_1 (.D(In), .Q(register_1_q), .clk(demultiplexer_1_out0), .clr(reset));  // open: en
  Register #(.width(32)) register_2 (.D(In), .Q(register_2_q), .clk(demultiplexer_1_out1), .clr(reset));  // open: en
  Register #(.width(32)) register_3 (.D(In), .Q(register_3_q), .clk(demultiplexer_1_out2), .clr(reset));  // open: en
  Register #(.width(32)) register_4 (.D(In), .Q(register_4_q), .clk(demultiplexer_1_out3), .clr(reset));  // open: en
  Multiplexer #(.width(32), .enable("false")) multiplexer_1 (
    .in0({32{1'b0}}), .in1(register_1_q), .out(multiplexer_1_out), .sel(demultiplexer_2_out0));
  Multiplexer #(.width(32), .enable("false")) multiplexer_2 (
    .in0({32{1'b0}}), .in1(register_2_q), .out(multiplexer_2_out), .sel(demultiplexer_2_out1));
  Multiplexer #(.width(32), .enable("false")) multiplexer_3 (
    .in0({32{1'b0}}), .in1(register_3_q), .out(multiplexer_3_out), .sel(demultiplexer_2_out2));
  Multiplexer #(.width(32), .enable("false")) multiplexer_4 (
    .in0({32{1'b0}}), .in1(register_4_q), .out(multiplexer_4_out), .sel(demultiplexer_2_out3));
  assign or_2_out = multiplexer_1_out | multiplexer_2_out | multiplexer_3_out | multiplexer_4_out;  // OR_Gate or_2, 32 bits wide
  Register #(.width(32)) register_5 (.D(In), .Q(register_5_q), .clk(demultiplexer_1_out4), .clr(reset));  // open: en
  Register #(.width(32)) register_6 (.D(In), .Q(register_6_q), .clk(demultiplexer_1_out5), .clr(reset));  // open: en
  Register #(.width(32)) register_7 (.D(In), .Q(register_7_q), .clk(demultiplexer_1_out6), .clr(reset));  // open: en
  Register #(.width(32)) register_8 (.D(In), .Q(register_8_q), .clk(demultiplexer_1_out7), .clr(reset));  // open: en
  Multiplexer #(.width(32), .enable("false")) multiplexer_5 (
    .in0({32{1'b0}}), .in1(register_5_q), .out(multiplexer_5_out), .sel(demultiplexer_2_out4));
  Multiplexer #(.width(32), .enable("false")) multiplexer_6 (
    .in0({32{1'b0}}), .in1(register_6_q), .out(multiplexer_6_out), .sel(demultiplexer_2_out5));
  Multiplexer #(.width(32), .enable("false")) multiplexer_7 (
    .in0({32{1'b0}}), .in1(register_7_q), .out(multiplexer_7_out), .sel(demultiplexer_2_out6));
  Multiplexer #(.width(32), .enable("false")) multiplexer_8 (
    .in0({32{1'b0}}), .in1(register_8_q), .out(multiplexer_8_out), .sel(demultiplexer_2_out7));
  assign or_3_out = multiplexer_5_out | multiplexer_6_out | multiplexer_7_out | multiplexer_8_out;  // OR_Gate or_3, 32 bits wide
  Register #(.width(32)) register_9 (.D(In), .Q(register_9_q), .clk(demultiplexer_1_out8), .clr(reset));  // open: en
  Register #(.width(32)) register_10 (.D(In), .Q(register_10_q), .clk(demultiplexer_1_out9), .clr(reset));  // open: en
  Register #(.width(32)) register_11 (.D(In), .Q(register_11_q), .clk(demultiplexer_1_out10), .clr(reset));  // open: en
  Register #(.width(32)) register_12 (.D(In), .Q(register_12_q), .clk(demultiplexer_1_out11), .clr(reset));  // open: en
  Multiplexer #(.width(32), .enable("false")) multiplexer_9 (
    .in0({32{1'b0}}), .in1(register_9_q), .out(multiplexer_9_out), .sel(demultiplexer_2_out8));
  Multiplexer #(.width(32), .enable("false")) multiplexer_10 (
    .in0({32{1'b0}}), .in1(register_10_q), .out(multiplexer_10_out), .sel(demultiplexer_2_out9));
  Multiplexer #(.width(32), .enable("false")) multiplexer_11 (
    .in0({32{1'b0}}), .in1(register_11_q), .out(multiplexer_11_out), .sel(demultiplexer_2_out10));
  Multiplexer #(.width(32), .enable("false")) multiplexer_12 (
    .in0({32{1'b0}}), .in1(register_12_q), .out(multiplexer_12_out), .sel(demultiplexer_2_out11));
  assign or_4_out = multiplexer_9_out | multiplexer_10_out | multiplexer_11_out | multiplexer_12_out;  // OR_Gate or_4, 32 bits wide
  Register #(.width(32)) register_13 (.D(In), .Q(register_13_q), .clk(demultiplexer_1_out12), .clr(reset));  // open: en
  Multiplexer #(.width(32), .enable("false")) multiplexer_13 (
    .in0({32{1'b0}}), .in1(register_14_q), .out(multiplexer_13_out), .sel(demultiplexer_2_out13));
  Register #(.width(32)) register_14 (.D(In), .Q(register_14_q), .clk(demultiplexer_1_out13), .clr(reset));  // open: en
  Multiplexer #(.width(32), .enable("false")) multiplexer_14 (
    .in0({32{1'b0}}), .in1(register_15_q), .out(multiplexer_14_out), .sel(demultiplexer_2_out14));
  Register #(.width(32)) register_15 (.D(In), .Q(register_15_q), .clk(demultiplexer_1_out14), .clr(reset));  // open: en
  Multiplexer #(.width(32), .enable("false")) multiplexer_15 (
    .in0({32{1'b0}}), .in1(register_16_q), .out(multiplexer_15_out), .sel(demultiplexer_2_out15));
  Register #(.width(32)) register_16 (.D(In), .Q(register_16_q), .clk(demultiplexer_1_out15), .clr(reset));  // open: en
  assign or_5_out = multiplexer_16_out | multiplexer_13_out | multiplexer_14_out | multiplexer_15_out;  // OR_Gate or_5, 32 bits wide
  Multiplexer #(.width(32), .enable("false")) multiplexer_16 (
    .in0({32{1'b0}}), .in1(register_13_q), .out(multiplexer_16_out), .sel(demultiplexer_2_out12));
endmodule

module digit_finder_32b_ns (
  input  [31:0] in_1,
  output [3:0] out_2,
  output [3:0] out_3,
  output [3:0] out_4,
  output [3:0] out_5,
  output [3:0] out_6,
  output [3:0] out_7,
  output [3:0] out_8,
  output [3:0] out_9,
  output [3:0] out_10,
  output [3:0] out_11
);

  wire [31:0] divider_1_out, divider_2_out, divider_3_out, divider_4_out, divider_5_out, divider_6_out,
       divider_7_out, divider_8_out, divider_9_out, multiplier_1_out, multiplier_2_out, multiplier_3_out,
       multiplier_4_out, multiplier_5_out, multiplier_6_out, multiplier_7_out, multiplier_8_out,
       multiplier_9_out, subtractor_1_out, subtractor_2_out, subtractor_3_out, subtractor_4_out,
       subtractor_5_out, subtractor_6_out, subtractor_7_out, subtractor_8_out, subtractor_9_out;

  Bit_Extender #(.in_width(32), .out_width(4)) bit_extender_1 (.in(subtractor_1_out), .out(out_2));
  Subtractor #(.width(32)) subtractor_1 (.a(in_1), .b(multiplier_1_out), .out(subtractor_1_out));  // open: bin, bout
  Multiplier #(.width(32)) multiplier_1 (.a(divider_1_out), .b(32'ha), .out(multiplier_1_out));  // open: cin, cout
  Divider #(.width(32)) divider_1 (.a(in_1), .b(32'ha), .out(divider_1_out));  // open: upper, rem
  Bit_Extender #(.in_width(32), .out_width(4)) bit_extender_2 (.in(subtractor_2_out), .out(out_3));
  Subtractor #(.width(32)) subtractor_2 (
    .a(divider_1_out), .b(multiplier_2_out), .out(subtractor_2_out));  // open: bin, bout
  Multiplier #(.width(32)) multiplier_2 (.a(divider_2_out), .b(32'ha), .out(multiplier_2_out));  // open: cin, cout
  Divider #(.width(32)) divider_2 (.a(divider_1_out), .b(32'ha), .out(divider_2_out));  // open: upper, rem
  Subtractor #(.width(32)) subtractor_3 (
    .a(divider_2_out), .b(multiplier_3_out), .out(subtractor_3_out));  // open: bin, bout
  Multiplier #(.width(32)) multiplier_3 (.a(divider_3_out), .b(32'ha), .out(multiplier_3_out));  // open: cin, cout
  Divider #(.width(32)) divider_3 (.a(divider_2_out), .b(32'ha), .out(divider_3_out));  // open: upper, rem
  Bit_Extender #(.in_width(32), .out_width(4)) bit_extender_3 (.in(subtractor_3_out), .out(out_4));
  Subtractor #(.width(32)) subtractor_4 (
    .a(divider_3_out), .b(multiplier_4_out), .out(subtractor_4_out));  // open: bin, bout
  Multiplier #(.width(32)) multiplier_4 (.a(divider_4_out), .b(32'ha), .out(multiplier_4_out));  // open: cin, cout
  Divider #(.width(32)) divider_4 (.a(divider_3_out), .b(32'ha), .out(divider_4_out));  // open: upper, rem
  Bit_Extender #(.in_width(32), .out_width(4)) bit_extender_4 (.in(subtractor_4_out), .out(out_5));
  Bit_Extender #(.in_width(32), .out_width(4)) bit_extender_5 (.in(subtractor_5_out), .out(out_6));
  Subtractor #(.width(32)) subtractor_5 (
    .a(divider_4_out), .b(multiplier_5_out), .out(subtractor_5_out));  // open: bin, bout
  Multiplier #(.width(32)) multiplier_5 (.a(divider_5_out), .b(32'ha), .out(multiplier_5_out));  // open: cin, cout
  Divider #(.width(32)) divider_5 (.a(divider_4_out), .b(32'ha), .out(divider_5_out));  // open: upper, rem
  Bit_Extender #(.in_width(32), .out_width(4)) bit_extender_6 (.in(subtractor_6_out), .out(out_7));
  Subtractor #(.width(32)) subtractor_6 (
    .a(divider_5_out), .b(multiplier_6_out), .out(subtractor_6_out));  // open: bin, bout
  Multiplier #(.width(32)) multiplier_6 (.a(divider_6_out), .b(32'ha), .out(multiplier_6_out));  // open: cin, cout
  Divider #(.width(32)) divider_6 (.a(divider_5_out), .b(32'ha), .out(divider_6_out));  // open: upper, rem
  Subtractor #(.width(32)) subtractor_7 (
    .a(divider_6_out), .b(multiplier_7_out), .out(subtractor_7_out));  // open: bin, bout
  Multiplier #(.width(32)) multiplier_7 (.a(divider_7_out), .b(32'ha), .out(multiplier_7_out));  // open: cin, cout
  Divider #(.width(32)) divider_7 (.a(divider_6_out), .b(32'ha), .out(divider_7_out));  // open: upper, rem
  Bit_Extender #(.in_width(32), .out_width(4)) bit_extender_7 (.in(subtractor_7_out), .out(out_8));
  Subtractor #(.width(32)) subtractor_8 (
    .a(divider_7_out), .b(multiplier_8_out), .out(subtractor_8_out));  // open: bin, bout
  Multiplier #(.width(32)) multiplier_8 (.a(divider_8_out), .b(32'ha), .out(multiplier_8_out));  // open: cin, cout
  Divider #(.width(32)) divider_8 (.a(divider_7_out), .b(32'ha), .out(divider_8_out));  // open: upper, rem
  Bit_Extender #(.in_width(32), .out_width(4)) bit_extender_8 (.in(subtractor_8_out), .out(out_9));
  Bit_Extender #(.in_width(32), .out_width(4)) bit_extender_9 (.in(subtractor_9_out), .out(out_10));
  Subtractor #(.width(32)) subtractor_9 (
    .a(divider_8_out), .b(multiplier_9_out), .out(subtractor_9_out));  // open: bin, bout
  Multiplier #(.width(32)) multiplier_9 (.a(divider_9_out), .b(32'ha), .out(multiplier_9_out));  // open: cin, cout
  Divider #(.width(32)) divider_9 (.a(divider_8_out), .b(32'ha), .out(divider_9_out));  // open: upper, rem
  Bit_Extender #(.in_width(32), .out_width(4)) bit_extender_10 (.in(divider_9_out), .out(out_11));
endmodule

module on_finder_32b (
  input  [31:0] in_1,
  output out_2
);

  or or_1 (out_2, in_1[16], in_1[31], in_1[30], in_1[29], in_1[28], in_1[27], in_1[26], in_1[25], in_1[24], in_1[23], in_1[22], in_1[21], in_1[20], in_1[19], in_1[18], in_1[17], in_1[15], in_1[14], in_1[13], in_1[12], in_1[11], in_1[10], in_1[9], in_1[8], in_1[7], in_1[6], in_1[5], in_1[4], in_1[3], in_1[2], in_1[1], in_1[0]);
endmodule

module HEX_to_ascii (
  input  [3:0] BIN_IN,
  output [7:0] ASCII_out
);

  wire [5:5] decoder_1_out0, decoder_1_out1, decoder_1_out2, decoder_1_out3, decoder_1_out4, decoder_1_out5,
       decoder_1_out6, decoder_1_out7, decoder_1_out8, decoder_1_out9;
  wire [6:6] decoder_1_out10, decoder_1_out11, decoder_1_out12, decoder_1_out13, decoder_1_out14,
       decoder_1_out15;
  wire [7:0] or_1_out, or_2_out;

  Decoder #(.select(4), .enable("false")) decoder_1 (
    .out0(decoder_1_out0[5]), .out1(decoder_1_out1[5]), .out2(decoder_1_out2[5]), .out3(decoder_1_out3[5]),
    .out4(decoder_1_out4[5]), .out5(decoder_1_out5[5]), .out6(decoder_1_out6[5]), .out7(decoder_1_out7[5]),
    .out8(decoder_1_out8[5]), .out9(decoder_1_out9[5]), .out10(decoder_1_out10[6]),
    .out11(decoder_1_out11[6]), .out12(decoder_1_out12[6]), .out13(decoder_1_out13[6]),
    .out14(decoder_1_out14[6]), .out15(decoder_1_out15[6]), .sel(BIN_IN));
  assign or_1_out = {2'b00, {3{decoder_1_out8[5]}}, 3'b000} | {2'b00, {3{decoder_1_out9[5]}}, 2'b00, decoder_1_out9[5]} | {1'b0, {2{decoder_1_out10[6]}}, 4'b0000, decoder_1_out10[6]} | {1'b0, {2{decoder_1_out11[6]}}, 3'b000, decoder_1_out11[6], 1'b0} | {1'b0, {2{decoder_1_out12[6]}}, 3'b000, {2{decoder_1_out12[6]}}} | {1'b0, {2{decoder_1_out13[6]}}, 2'b00, decoder_1_out13[6], 2'b00} | {1'b0, {2{decoder_1_out14[6]}}, 2'b00, decoder_1_out14[6], 1'b0, decoder_1_out14[6]} | {1'b0, {2{decoder_1_out15[6]}}, 2'b00, {2{decoder_1_out15[6]}}, 1'b0};  // OR_Gate or_1, 8 bits wide
  assign or_2_out = {2'b00, {2{decoder_1_out7[5]}}, 1'b0, {3{decoder_1_out7[5]}}} | {2'b00, {2{decoder_1_out6[5]}}, 1'b0, {2{decoder_1_out6[5]}}, 1'b0} | {2'b00, {2{decoder_1_out5[5]}}, 1'b0, decoder_1_out5[5], 1'b0, decoder_1_out5[5]} | {2'b00, {2{decoder_1_out4[5]}}, 1'b0, decoder_1_out4[5], 2'b00} | {2'b00, {2{decoder_1_out3[5]}}, 2'b00, {2{decoder_1_out3[5]}}} | {2'b00, {2{decoder_1_out2[5]}}, 2'b00, decoder_1_out2[5], 1'b0} | {2'b00, {2{decoder_1_out1[5]}}, 3'b000, decoder_1_out1[5]} | {2'b00, {2{decoder_1_out0[5]}}, 4'b0000};  // OR_Gate or_2, 8 bits wide
  assign ASCII_out = or_1_out | or_2_out;  // OR_Gate or_3, 8 bits wide

  // Notes on the sheet:
  //   8
  //   0
  //   f
  //   7
endmodule

module calc_rom (
  input  [31:0] D,
  input  [31:0] C,
  input  [31:0] B,
  input  [31:0] A,
  input  R,
  input  [7:0] R_Q,
  input  Rst,
  input  Wr,
  input  [7:0] Wr_Q,
  output [31:0] A_2,
  output [31:0] B_2,
  output [31:0] C_2,
  output [31:0] D_2
);

  wire and_1_out, buffer_1_out, comparator_1_gt, not_1_out;
  wire [1:0] bit_extender_1_out;
  wire [31:0] multiplexer_5_out, multiplexer_6_out, multiplexer_7_out, multiplexer_8_out;

  Multiplexer #(.width(32), .enable("false")) multiplexer_1 (
    .in0({32{1'b0}}), .in1(multiplexer_8_out), .out(A_2), .sel(buffer_1_out));
  Multiplexer #(.width(32), .enable("false")) multiplexer_2 (
    .in0({32{1'b0}}), .in1(multiplexer_7_out), .out(B_2), .sel(buffer_1_out));
  Multiplexer #(.width(32), .enable("false")) multiplexer_3 (
    .in0({32{1'b0}}), .in1(multiplexer_6_out), .out(C_2), .sel(buffer_1_out));
  buf buffer_1 (buffer_1_out, and_1_out);
  Multiplexer #(.width(32), .enable("false")) multiplexer_4 (
    .in0({32{1'b0}}), .in1(multiplexer_5_out), .out(D_2), .sel(buffer_1_out));
  and and_1 (and_1_out, R, not_1_out);
  Multiplexer #(.select(2), .width(32), .enable("false")) multiplexer_5 (
    .in0({32{1'b0}}), .in1({32{1'b0}}), .in2({32{1'b0}}), .in3(32'h1), .out(multiplexer_5_out),
    .sel(bit_extender_1_out));
  Multiplexer #(.select(2), .width(32), .enable("false")) multiplexer_6 (
    .in0({32{1'b0}}), .in1({32{1'b0}}), .in2({32{1'b0}}), .in3({32{1'b0}}), .out(multiplexer_6_out),
    .sel(bit_extender_1_out));
  Multiplexer #(.select(2), .width(32), .enable("false")) multiplexer_7 (
    .in0(32'h8), .in1({32{1'b0}}), .in2({32{1'b0}}), .in3(32'h17), .out(multiplexer_7_out),
    .sel(bit_extender_1_out));
  Multiplexer #(.select(2), .width(32), .enable("false")) multiplexer_8 (
    .in0(32'h8), .in1(32'h2010), .in2(32'h3020), .in3(32'h4000), .out(multiplexer_8_out),
    .sel(bit_extender_1_out));
  Bit_Extender #(.out_width(2)) bit_extender_1 (.in(R_Q), .out(bit_extender_1_out));
  not not_1 (not_1_out, comparator_1_gt);
  Comparator #(.mode("unsigned")) comparator_1 (.a(R_Q), .b(8'h3), .gt(comparator_1_gt));  // open: eq, lt

  // Notes on the sheet:
  //   0
  //   1
  //   2
  //   3
  //   D
  //   C
  //   B
  //   A
endmodule

module countup_rom (
  input  [31:0] D,
  input  [31:0] C,
  input  [31:0] B,
  input  [31:0] A,
  input  R,
  input  [7:0] R_Q,
  input  Rst,
  input  Wr,
  input  [7:0] Wr_Q,
  output [31:0] A_2,
  output [31:0] B_2,
  output [31:0] C_2,
  output [31:0] D_2
);

  wire and_1_out, buffer_1_out, comparator_1_gt, not_1_out;
  wire [1:0] bit_extender_1_out;
  wire [31:0] multiplexer_5_out, multiplexer_6_out, multiplexer_7_out, multiplexer_8_out;

  Multiplexer #(.width(32), .enable("false")) multiplexer_1 (
    .in0({32{1'b0}}), .in1(multiplexer_8_out), .out(A_2), .sel(buffer_1_out));
  Multiplexer #(.width(32), .enable("false")) multiplexer_2 (
    .in0({32{1'b0}}), .in1(multiplexer_7_out), .out(B_2), .sel(buffer_1_out));
  Multiplexer #(.width(32), .enable("false")) multiplexer_3 (
    .in0({32{1'b0}}), .in1(multiplexer_6_out), .out(C_2), .sel(buffer_1_out));
  buf buffer_1 (buffer_1_out, and_1_out);
  Multiplexer #(.width(32), .enable("false")) multiplexer_4 (
    .in0({32{1'b0}}), .in1(multiplexer_5_out), .out(D_2), .sel(buffer_1_out));
  and and_1 (and_1_out, R, not_1_out);
  Multiplexer #(.select(2), .width(32), .enable("false")) multiplexer_5 (
    .in0({32{1'b0}}), .in1({32{1'b0}}), .in2({32{1'b0}}), .in3(32'h1), .out(multiplexer_5_out),
    .sel(bit_extender_1_out));
  Multiplexer #(.select(2), .width(32), .enable("false")) multiplexer_6 (
    .in0({32{1'b0}}), .in1({32{1'b0}}), .in2({32{1'b0}}), .in3({32{1'b0}}), .out(multiplexer_6_out),
    .sel(bit_extender_1_out));
  Multiplexer #(.select(2), .width(32), .enable("false")) multiplexer_7 (
    .in0(32'h8), .in1({32{1'b0}}), .in2({32{1'b0}}), .in3(32'h17), .out(multiplexer_7_out),
    .sel(bit_extender_1_out));
  Multiplexer #(.select(2), .width(32), .enable("false")) multiplexer_8 (
    .in0(32'h8), .in1(32'h14), .in2(32'h2020), .in3(32'h3002), .out(multiplexer_8_out),
    .sel(bit_extender_1_out));
  Bit_Extender #(.out_width(2)) bit_extender_1 (.in(R_Q), .out(bit_extender_1_out));
  not not_1 (not_1_out, comparator_1_gt);
  Comparator #(.mode("unsigned")) comparator_1 (.a(R_Q), .b(8'h3), .gt(comparator_1_gt));  // open: eq, lt

  // Notes on the sheet:
  //   0
  //   1
  //   2
  //   3
  //   D
  //   C
  //   B
  //   A
endmodule

module countdown_rom (
  input  [31:0] D,
  input  [31:0] C,
  input  [31:0] B,
  input  [31:0] A,
  input  R,
  input  [7:0] R_Q,
  input  Rst,
  input  Wr,
  input  [7:0] Wr_Q,
  output [31:0] A_2,
  output [31:0] B_2,
  output [31:0] C_2,
  output [31:0] D_2
);

  wire and_1_out, buffer_1_out, comparator_1_gt, not_1_out;
  wire [3:0] bit_extender_1_out;
  wire [31:0] multiplexer_1_out, multiplexer_2_out, multiplexer_5_out, multiplexer_8_out;

  Multiplexer #(.select(4), .width(32), .enable("false")) multiplexer_1 (
    .in0({32{1'b0}}), .in1({32{1'b0}}), .in2({32{1'b0}}), .in3({32{1'b0}}), .in4({32{1'b0}}),
    .in5({32{1'b0}}), .in6({32{1'b0}}), .in7(32'h1), .in8(32'h2), .in9({32{1'b0}}), .in10({32{1'b0}}),
    .in11({32{1'b0}}), .in12({32{1'b0}}), .in13({32{1'b0}}), .in14({32{1'b0}}), .in15({32{1'b0}}),
    .out(multiplexer_1_out), .sel(bit_extender_1_out));
  Multiplexer #(.select(4), .width(32), .enable("false")) multiplexer_2 (
    .in0({32{1'b0}}), .in1({32{1'b0}}), .in2({32{1'b0}}), .in3({32{1'b0}}), .in4({32{1'b0}}),
    .in5({32{1'b0}}), .in6({32{1'b0}}), .in7({32{1'b0}}), .in8({32{1'b0}}), .in9({32{1'b0}}),
    .in10({32{1'b0}}), .in11({32{1'b0}}), .in12({32{1'b0}}), .in13({32{1'b0}}), .in14({32{1'b0}}),
    .in15({32{1'b0}}), .out(multiplexer_2_out), .sel(bit_extender_1_out));
  Multiplexer #(.width(32), .enable("false")) multiplexer_3 (
    .in0({32{1'b0}}), .in1(multiplexer_8_out), .out(A_2), .sel(buffer_1_out));
  Multiplexer #(.width(32), .enable("false")) multiplexer_4 (
    .in0({32{1'b0}}), .in1(multiplexer_5_out), .out(B_2), .sel(buffer_1_out));
  Multiplexer #(.select(4), .width(32), .enable("false")) multiplexer_5 (
    .in0(32'h8), .in1(32'h5), .in2({32{1'b0}}), .in3({32{1'b0}}), .in4(32'h7), .in5({32{1'b0}}),
    .in6({32{1'b0}}), .in7({32{1'b0}}), .in8({32{1'b0}}), .in9({32{1'b0}}), .in10({32{1'b0}}),
    .in11({32{1'b0}}), .in12({32{1'b0}}), .in13({32{1'b0}}), .in14({32{1'b0}}), .in15({32{1'b0}}),
    .out(multiplexer_5_out), .sel(bit_extender_1_out));
  Multiplexer #(.width(32), .enable("false")) multiplexer_6 (
    .in0({32{1'b0}}), .in1(multiplexer_2_out), .out(C_2), .sel(buffer_1_out));
  Multiplexer #(.width(32), .enable("false")) multiplexer_7 (
    .in0({32{1'b0}}), .in1(multiplexer_1_out), .out(D_2), .sel(buffer_1_out));
  buf buffer_1 (buffer_1_out, and_1_out);
  and and_1 (and_1_out, R, not_1_out);
  Multiplexer #(.select(4), .width(32), .enable("false")) multiplexer_8 (
    .in0(32'h8), .in1(32'h2802), .in2(32'h3020), .in3(32'h14), .in4(32'h42), .in5(32'h14), .in6(32'hc020),
    .in7(32'h141), .in8({32{1'b0}}), .in9({32{1'b0}}), .in10({32{1'b0}}), .in11({32{1'b0}}),
    .in12({32{1'b0}}), .in13({32{1'b0}}), .in14({32{1'b0}}), .in15({32{1'b0}}), .out(multiplexer_8_out),
    .sel(bit_extender_1_out));
  Bit_Extender #(.out_width(4)) bit_extender_1 (.in(R_Q), .out(bit_extender_1_out));
  not not_1 (not_1_out, comparator_1_gt);
  Comparator comparator_1 (.a(R_Q), .b(8'h8), .gt(comparator_1_gt));  // open: eq, lt

  // Notes on the sheet:
  //   0
  //   1
  //   2
  //   3
  //   4
  //   5
  //   6
  //   7
  //   8
  //   D
  //   0
  //   1
  //   2
  //   3
  //   4
  //   5
  //   6
  //   7
  //   8
  //   C
  //   B
  //   0
  //   1
  //   2
  //   3
  //   4
  //   5
  //   6
  //   7
  //   8
  //   0
  //   1
  //   2
  //   3
  //   4
  //   5
  //   6
  //   7
  //   8
  //   A
endmodule

module fib_rom (
  input  [31:0] D,
  input  [31:0] C,
  input  [31:0] B,
  input  [31:0] A,
  input  R,
  input  [7:0] R_Q,
  input  Rst,
  input  Wr,
  input  [7:0] Wr_Q,
  output [31:0] A_2,
  output [31:0] B_2,
  output [31:0] C_2,
  output [31:0] D_2
);

  wire and_1_out, buffer_1_out, comparator_1_gt, not_1_out;
  wire [3:0] bit_extender_1_out;
  wire [31:0] multiplexer_1_out, multiplexer_2_out, multiplexer_5_out, multiplexer_8_out;

  Multiplexer #(.select(4), .width(32), .enable("false")) multiplexer_1 (
    .in0({32{1'b0}}), .in1({32{1'b0}}), .in2({32{1'b0}}), .in3({32{1'b0}}), .in4({32{1'b0}}),
    .in5({32{1'b0}}), .in6({32{1'b0}}), .in7({32{1'b0}}), .in8({32{1'b0}}), .in9({32{1'b0}}),
    .in10({32{1'b0}}), .in11({32{1'b0}}), .in12({32{1'b0}}), .in13(32'h3), .in14(32'he), .in15({32{1'b0}}),
    .out(multiplexer_1_out), .sel(bit_extender_1_out));
  Multiplexer #(.select(4), .width(32), .enable("false")) multiplexer_2 (
    .in0({32{1'b0}}), .in1({32{1'b0}}), .in2(32'h1), .in3({32{1'b0}}), .in4({32{1'b0}}), .in5({32{1'b0}}),
    .in6({32{1'b0}}), .in7({32{1'b0}}), .in8({32{1'b0}}), .in9(32'h1), .in10({32{1'b0}}), .in11({32{1'b0}}),
    .in12({32{1'b0}}), .in13({32{1'b0}}), .in14({32{1'b0}}), .in15({32{1'b0}}), .out(multiplexer_2_out),
    .sel(bit_extender_1_out));
  Multiplexer #(.width(32), .enable("false")) multiplexer_3 (
    .in0({32{1'b0}}), .in1(multiplexer_8_out), .out(A_2), .sel(buffer_1_out));
  Multiplexer #(.width(32), .enable("false")) multiplexer_4 (
    .in0({32{1'b0}}), .in1(multiplexer_5_out), .out(B_2), .sel(buffer_1_out));
  Multiplexer #(.select(4), .width(32), .enable("false")) multiplexer_5 (
    .in0(32'h8), .in1({32{1'b0}}), .in2({32{1'b0}}), .in3({32{1'b0}}), .in4({32{1'b0}}), .in5({32{1'b0}}),
    .in6(32'h4), .in7({32{1'b0}}), .in8({32{1'b0}}), .in9({32{1'b0}}), .in10({32{1'b0}}), .in11({32{1'b0}}),
    .in12({32{1'b0}}), .in13({32{1'b0}}), .in14({32{1'b0}}), .in15({32{1'b0}}), .out(multiplexer_5_out),
    .sel(bit_extender_1_out));
  Multiplexer #(.width(32), .enable("false")) multiplexer_6 (
    .in0({32{1'b0}}), .in1(multiplexer_2_out), .out(C_2), .sel(buffer_1_out));
  Multiplexer #(.width(32), .enable("false")) multiplexer_7 (
    .in0({32{1'b0}}), .in1(multiplexer_1_out), .out(D_2), .sel(buffer_1_out));
  buf buffer_1 (buffer_1_out, and_1_out);
  and and_1 (and_1_out, R, not_1_out);
  Multiplexer #(.select(4), .width(32), .enable("false")) multiplexer_8 (
    .in0(32'h8), .in1(32'h3002802), .in2(32'h1000c02), .in3(32'h14), .in4(32'h10024), .in5(32'h2000002),
    .in6(32'h10806), .in7(32'h1020806), .in8(32'h30014), .in9(32'h1020), .in10(32'h3000042),
    .in11(32'h30014), .in12(32'hc020), .in13(32'h1c1), .in14({32{1'b0}}), .in15({32{1'b0}}),
    .out(multiplexer_8_out), .sel(bit_extender_1_out));
  Bit_Extender #(.out_width(4)) bit_extender_1 (.in(R_Q), .out(bit_extender_1_out));
  not not_1 (not_1_out, comparator_1_gt);
  Comparator comparator_1 (.a(R_Q), .b(8'he), .gt(comparator_1_gt));  // open: eq, lt

  // Notes on the sheet:
  //   D
  //   0
  //   1
  //   2
  //   3
  //   4
  //   5
  //   6
  //   7
  //   8
  //   9
  //   10
  //   11
  //   12
  //   13
  //   14
  //   0
  //   1
  //   2
  //   3
  //   4
  //   5
  //   6
  //   7
  //   8
  //   9
  //   10
  //   11
  //   12
  //   13
  //   14
  //   C
  //   B
  //   0
  //   1
  //   2
  //   3
  //   4
  //   5
  //   6
  //   7
  //   8
  //   9
  //   10
  //   11
  //   12
  //   13
  //   14
  //   0
  //   1
  //   2
  //   3
  //   4
  //   5
  //   6
  //   7
  //   8
  //   9
  //   10
  //   11
  //   12
  //   13
  //   14
  //   A
endmodule

module on_finder_8b (
  input  [7:0] in,
  output on
);

  or or_1 (on, in[4], in[7], in[6], in[5], in[3], in[2], in[1], in[0]);
endmodule

module cpu_and_ram_32b_ns (
  input  [7:0] Ram_WrQ,
  input  [7:0] Ram_RQ,
  input  [3:0] ReadMux_select_Q,
  input  [1:0] RamMux_select_Q,
  input  [3:0] ALU_Fnctn,
  input  [4:0] _0_RAM_Wr_1_RAM_R_2_RAM_Rst_3_Register_A_4_Register_B,
  input  [31:0] ReadMux_in__select_1,
  input  [31:0] RamMux_in__selsect_3,
  input  [31:0] user_0_select_2,
  input  [31:0] user_1_select_3,
  input  [31:0] user_2_select_4,
  input  [31:0] user_3_select_5,
  input  [31:0] user_4_select_6,
  input  [31:0] user_5_select_7,
  input  [31:0] user_6_select_8,
  input  [31:0] user_7_select_9,
  input  [31:0] user_8_select_10,
  input  [31:0] user_9_select_11,
  input  [31:0] user_10_select_12,
  output [31:0] Ram_out,
  output [31:0] ReadMux_out,
  output [31:0] ALU_zero,
  output [31:0] ALU_out
);

  wire [31:0] multiplexer_2_out, register_1_q, register_2_q;

  Register #(.width(32)) register_1 (
    .D(ReadMux_out), .Q(register_1_q), .clk(_0_RAM_Wr_1_RAM_R_2_RAM_Rst_3_Register_A_4_Register_B[3]));  // open: en, clr
  Register #(.width(32)) register_2 (
    .D(ReadMux_out), .Q(register_2_q), .clk(_0_RAM_Wr_1_RAM_R_2_RAM_Rst_3_Register_A_4_Register_B[4]));  // open: en, clr
  ALU_32b_ns alu_32b_ns_1 (
    .A_in(register_1_q), .B_in(register_2_q), .\output (ALU_out), .Zero(ALU_zero), .Fnctn(ALU_Fnctn));
  Multiplexer #(.select(4), .width(32), .enable("false")) multiplexer_1 (
    .in0(Ram_out), .in1(ReadMux_in__select_1), .in2(user_0_select_2), .in3(user_1_select_3),
    .in4(user_2_select_4), .in5(user_3_select_5), .in6(user_4_select_6), .in7(user_5_select_7),
    .in8(user_6_select_8), .in9(user_7_select_9), .in10(user_8_select_10), .in11(user_9_select_11),
    .in12(user_10_select_12), .in13({32{1'b0}}), .in14(32'h1), .in15(32'ha), .out(ReadMux_out),
    .sel(ReadMux_select_Q));
  Multiplexer #(.select(2), .width(32), .enable("false")) multiplexer_2 (
    .in0(ALU_out), .in1(ALU_zero), .in2(ReadMux_out), .in3(RamMux_in__selsect_3), .out(multiplexer_2_out),
    .sel(RamMux_select_Q));
  memory_32bx256 memory_32bx256_1 (
    .out(Ram_out), .In(multiplexer_2_out), .reset(_0_RAM_Wr_1_RAM_R_2_RAM_Rst_3_Register_A_4_Register_B[2]),
    .wright(_0_RAM_Wr_1_RAM_R_2_RAM_Rst_3_Register_A_4_Register_B[0]), .wright_Q(Ram_WrQ),
    .read(_0_RAM_Wr_1_RAM_R_2_RAM_Rst_3_Register_A_4_Register_B[1]), .read_Q(Ram_RQ));
endmodule

module _1_bit_ALU (
  input  Sub,
  input  Cin,
  input  [3:0] in_3,
  input  A,
  input  B,
  input  less,
  output out_7,
  output set,
  output Cout
);

  wire and_1_out, multiplier_1_cout, multiplier_1_out, n1_bit_adder_1_cout, nor_1_out, not_1_out, not_2_out,
       or_1_out, or_2_out, xor_1_out, xor_2_out;

  or or_1 (or_1_out, Sub, Cin);
  xor xor_1 (xor_1_out, A, B);
  or or_2 (or_2_out, A, B);
  and and_1 (and_1_out, A, B);
  nor nor_1 (nor_1_out, A, B);
  not not_1 (not_1_out, A);
  not not_2 (not_2_out, B);
  xor xor_2 (xor_2_out, B, Sub);
  Multiplier #(.width(1)) multiplier_1 (.a(A), .b(B), .out(multiplier_1_out), .cin(Cin), .cout(multiplier_1_cout));
  or or_3 (Cout, multiplier_1_cout, n1_bit_adder_1_cout);
  _1_bit_Adder u_1_bit_adder_1 (.A(A), .B(xor_2_out), .Out(set), .Cin(or_1_out), .Cout(n1_bit_adder_1_cout));
  Multiplexer #(.select(4), .enable("false")) multiplexer_1 (
    .in0(xor_1_out), .in1(or_2_out), .in2(and_1_out), .in3(nor_1_out), .in4(set), .in5(less),
    .in6(not_1_out), .in7(not_2_out), .in8(multiplier_1_out), .out(out_7), .sel(in_3));  // open: in9, in10, in11, in12, in13, in14, in15

  // Notes on the sheet:
  //   0 xor
  //   1 or
  //   2 and
  //   3 nor
  //   4 adder
  //   5 less
  //   6 not A
  //   7 not B
  //   8 multiplier
endmodule

module _1_bit_Adder (
  input  Cin,
  input  A,
  input  B,
  output Out,
  output Cout
);

  wire and_1_out, and_2_out, xor_1_out;

  xor xor_1 (xor_1_out, A, B);
  and and_1 (and_1_out, Cin, xor_1_out);
  and and_2 (and_2_out, A, B);
  xor xor_2 (Out, Cin, xor_1_out);
  or or_1 (Cout, and_1_out, and_2_out);
endmodule

module _8_bit_ALU (
  input  sub,
  input  [3:0] fs,
  input  [7:0] B,
  input  [7:0] A,
  output [7:0] \output ,
  output Zero,
  output Cout
);

  wire n1_bit_alu_1_cout, n1_bit_alu_2_cout, n1_bit_alu_3_cout, n1_bit_alu_4_cout, n1_bit_alu_5_cout,
       n1_bit_alu_6_cout, n1_bit_alu_7_cout, n1_bit_alu_8_set;

  _1_bit_ALU u_1_bit_alu_1 (
    .A(A[0]), .B(B[0]), .less(n1_bit_alu_8_set), .out_7(\output [0]), .Sub(sub), .Cin(1'b0), .in_3(fs),
    .Cout(n1_bit_alu_1_cout));  // open: set
  _1_bit_ALU u_1_bit_alu_2 (
    .A(A[1]), .B(B[1]), .less(1'b0), .out_7(\output [1]), .Sub(sub), .Cin(n1_bit_alu_1_cout), .in_3(fs),
    .Cout(n1_bit_alu_2_cout));  // open: set
  _1_bit_ALU u_1_bit_alu_3 (
    .A(A[2]), .B(B[2]), .less(1'b0), .out_7(\output [2]), .Sub(sub), .Cin(n1_bit_alu_2_cout), .in_3(fs),
    .Cout(n1_bit_alu_3_cout));  // open: set
  _1_bit_ALU u_1_bit_alu_4 (
    .A(A[3]), .B(B[3]), .less(1'b0), .out_7(\output [3]), .Sub(sub), .Cin(n1_bit_alu_3_cout), .in_3(fs),
    .Cout(n1_bit_alu_4_cout));  // open: set
  _1_bit_ALU u_1_bit_alu_5 (
    .A(A[4]), .B(B[4]), .less(1'b0), .out_7(\output [4]), .Sub(sub), .Cin(n1_bit_alu_4_cout), .in_3(fs),
    .Cout(n1_bit_alu_5_cout));  // open: set
  _1_bit_ALU u_1_bit_alu_6 (
    .A(A[5]), .B(B[5]), .less(1'b0), .out_7(\output [5]), .Sub(sub), .Cin(n1_bit_alu_5_cout), .in_3(fs),
    .Cout(n1_bit_alu_6_cout));  // open: set
  _1_bit_ALU u_1_bit_alu_7 (
    .A(A[6]), .B(B[6]), .less(1'b0), .out_7(\output [6]), .Sub(sub), .Cin(n1_bit_alu_6_cout), .in_3(fs),
    .Cout(n1_bit_alu_7_cout));  // open: set
  _1_bit_ALU u_1_bit_alu_8 (
    .A(A[7]), .B(B[7]), .less(1'b0), .out_7(\output [7]), .Sub(sub), .Cin(n1_bit_alu_7_cout), .in_3(fs),
    .Cout(Cout), .set(n1_bit_alu_8_set));
  nor nor_1 (Zero, \output [0], \output [1], \output [2], \output [3], \output [4], \output [5], \output [6], \output [7]);

  // Notes on the sheet:
  //   0 xor
  //   1 or
  //   2 and
  //   3 nor
  //   4 adder
  //   5 less
  //   6 not A
  //   7 not B
  //   8 multiplier
endmodule

module memory_8b (
  input  [7:0] In,
  input  read,
  input  write,
  input  reset,
  output [7:0] Out,
  output [7:0] pre__Out
);

  wire [7:0] not_1_out, not_2_out;

  assign not_1_out = ~In;  // NOT_Gate not_1, 8 bits wide
  Multiplexer #(.width(8), .enable("false")) multiplexer_1 (.in0({8{1'b0}}), .in1(pre__Out), .out(Out), .sel(read));
  assign not_2_out = ~not_1_out;  // NOT_Gate not_2, 8 bits wide
  D_Flip_Flop #(.trigger("high")) d_ff_1 (
    .clk(write), .D(not_2_out[7]), .Q(pre__Out[7]), .preset(1'b0), .en(1'b1), .reset(reset));  // open: Qn
  D_Flip_Flop #(.trigger("high")) d_ff_2 (
    .clk(write), .D(not_2_out[6]), .Q(pre__Out[6]), .preset(1'b0), .en(1'b1), .reset(reset));  // open: Qn
  D_Flip_Flop #(.trigger("high")) d_ff_3 (
    .clk(write), .D(not_2_out[5]), .Q(pre__Out[5]), .preset(1'b0), .en(1'b1), .reset(reset));  // open: Qn
  D_Flip_Flop #(.trigger("high")) d_ff_4 (
    .clk(write), .D(not_2_out[4]), .Q(pre__Out[4]), .preset(1'b0), .en(1'b1), .reset(reset));  // open: Qn
  D_Flip_Flop #(.trigger("high")) d_ff_5 (
    .clk(write), .D(not_2_out[3]), .Q(pre__Out[3]), .preset(1'b0), .en(1'b1), .reset(reset));  // open: Qn
  D_Flip_Flop #(.trigger("high")) d_ff_6 (
    .clk(write), .D(not_2_out[2]), .Q(pre__Out[2]), .preset(1'b0), .en(1'b1), .reset(reset));  // open: Qn
  D_Flip_Flop #(.trigger("high")) d_ff_7 (
    .clk(write), .D(not_2_out[1]), .Q(pre__Out[1]), .preset(1'b0), .en(1'b1), .reset(reset));  // open: Qn
  D_Flip_Flop #(.trigger("high")) d_ff_8 (
    .clk(write), .D(not_2_out[0]), .Q(pre__Out[0]), .preset(1'b0), .en(1'b1), .reset(reset));  // open: Qn
endmodule

module num_input_system_32b_ns (
  input  set,
  input  Bkspace,
  input  [3:0] in,
  input  reset,
  output [31:0] out,
  output overFlow
);

  wire adder_1_cout, and_1_out, not_1_out, not_2_out, on_finder_32b_1_out_2, or_1_out;
  wire [31:0] adder_1_out, bit_extender_1_out, divider_1_out, multiplexer_1_out, multiplier_1_cout,
       multiplier_1_out, prev_q;

  Register #(.width(32), .trigger("high")) prev (.D(out), .en(1'b1), .Q(prev_q), .clk(not_1_out), .clr(reset));
  not not_1 (not_1_out, set);
  Divider #(.width(32)) divider_1 (.a(prev_q), .b(32'ha), .out(divider_1_out));  // open: upper, rem
  Multiplier #(.width(32)) multiplier_1 (
    .a(prev_q), .b(32'ha), .out(multiplier_1_out), .cout(multiplier_1_cout));  // open: cin
  assign bit_extender_1_out = {{28{1'b0}}, in};  // Bit_Extender bit_extender_1
  Adder #(.width(32)) adder_1 (
    .a(multiplier_1_out), .b(bit_extender_1_out), .out(adder_1_out), .cout(adder_1_cout));  // open: cin
  on_finder_32b on_finder_32b_1 (.in_1(multiplier_1_cout), .out_2(on_finder_32b_1_out_2));
  Multiplexer #(.width(32), .enable("false")) multiplexer_1 (
    .in0(adder_1_out), .in1(divider_1_out), .out(multiplexer_1_out), .sel(Bkspace));
  Register #(.width(32), .trigger("high")) curr (.D(multiplexer_1_out), .en(1'b1), .Q(out), .clk(set), .clr(reset));
  and and_1 (and_1_out, or_1_out, not_2_out);
  or or_1 (or_1_out, on_finder_32b_1_out_2, adder_1_cout);
  not not_2 (not_2_out, Bkspace);
  S_R_Flip_Flop #(.trigger("high")) s_r_ff_1 (
    .S(and_1_out), .clk(set), .R(1'b0), .Q(overFlow), .reset(reset), .en(1'b1));  // open: Qn, preset
endmodule

module coder_4b_h (
  input  [15:0] in,
  output pressed,
  output [3:0] out,
  output zero
);

  wire [3:0] or_2_out;

  or or_1 (pressed, in[15], in[14], in[13], in[12], in[11], in[10], in[9], in[8], in[7], in[6], in[5], in[4], in[3], in[2], in[1], in[0]);
  assign or_2_out = 4'b0000 | {3'b000, in[1]} | {2'b00, in[2], 1'b0} | {2'b00, {2{in[3]}}} | {1'b0, in[4], 2'b00} | {1'b0, in[5], 1'b0, in[5]} | {1'b0, {2{in[6]}}, 1'b0} | {1'b0, {3{in[7]}}} | {in[8], 3'b000} | {in[9], 2'b00, in[9]} | {in[10], 1'b0, in[10], 1'b0} | {in[11], 1'b0, {2{in[11]}}} | {{2{in[12]}}, 2'b00} | {{2{in[13]}}, 1'b0, in[13]} | {{3{in[14]}}, 1'b0} | {4{in[15]}};  // OR_Gate or_2, 4 bits wide
  Register #(.width(4), .trigger("high")) register_1 (.D(or_2_out), .en(1'b1), .Q(out), .clk(pressed));  // open: clr

  assign zero = in[0];
endmodule

module num_input_system_8b_ns (
  input  set,
  input  Bkspace,
  input  [3:0] in,
  input  reset,
  output [7:0] out,
  output overFlow
);

  wire adder_1_cout, and_1_out, not_1_out, not_2_out, on_finder_8b_1_on, or_1_out;
  wire [7:0] adder_1_out, bit_extender_1_out, divider_1_out, multiplexer_1_out, multiplier_1_cout,
       multiplier_1_out, prev_q;

  Register #(.trigger("high")) prev (.D(out), .en(1'b1), .Q(prev_q), .clk(not_1_out), .clr(reset));
  not not_1 (not_1_out, set);
  Divider divider_1 (.a(prev_q), .b(8'ha), .out(divider_1_out));  // open: upper, rem
  Multiplier multiplier_1 (.a(prev_q), .b(8'ha), .out(multiplier_1_out), .cout(multiplier_1_cout));  // open: cin
  assign bit_extender_1_out = {{4{1'b0}}, in};  // Bit_Extender bit_extender_1
  Adder adder_1 (.a(multiplier_1_out), .b(bit_extender_1_out), .out(adder_1_out), .cout(adder_1_cout));  // open: cin
  on_finder_8b on_finder_8b_1 (.in(multiplier_1_cout), .on(on_finder_8b_1_on));
  Multiplexer #(.width(8), .enable("false")) multiplexer_1 (
    .in0(adder_1_out), .in1(divider_1_out), .out(multiplexer_1_out), .sel(Bkspace));
  Register #(.trigger("high")) curr (.D(multiplexer_1_out), .en(1'b1), .Q(out), .clk(set), .clr(reset));
  and and_1 (and_1_out, or_1_out, not_2_out);
  or or_1 (or_1_out, on_finder_8b_1_on, adder_1_cout);
  not not_2 (not_2_out, Bkspace);
  S_R_Flip_Flop #(.trigger("high")) s_r_ff_1 (
    .S(and_1_out), .clk(set), .R(1'b0), .Q(overFlow), .reset(reset), .en(1'b1));  // open: Qn, preset
endmodule

module digit_finder_8b (
  input  [7:0] input_8b,
  output [3:0] digit_0,
  output [3:0] digit_1,
  output [3:0] digit_2
);

  wire [7:0] divider_1_out, divider_2_out, multiplier_1_out, multiplier_2_out, subtractor_1_out,
       subtractor_2_out;

  Bit_Extender #(.out_width(4)) bit_extender_1 (.in(subtractor_1_out), .out(digit_0));
  Subtractor subtractor_1 (.a(input_8b), .b(multiplier_1_out), .out(subtractor_1_out));  // open: bin, bout
  Multiplier multiplier_1 (.a(divider_1_out), .b(8'ha), .out(multiplier_1_out));  // open: cin, cout
  Divider divider_1 (.a(input_8b), .b(8'ha), .out(divider_1_out));  // open: upper, rem
  Bit_Extender #(.out_width(4)) bit_extender_2 (.in(subtractor_2_out), .out(digit_1));
  Subtractor subtractor_2 (.a(divider_1_out), .b(multiplier_2_out), .out(subtractor_2_out));  // open: bin, bout
  Multiplier multiplier_2 (.a(divider_2_out), .b(8'ha), .out(multiplier_2_out));  // open: cin, cout
  Divider divider_2 (.a(divider_1_out), .b(8'ha), .out(divider_2_out));  // open: upper, rem
  Bit_Extender #(.out_width(4)) bit_extender_3 (.in(divider_2_out), .out(digit_2));
endmodule

module store_0 (
);

  wire button_4_out, button_12_out, coder_4b_h_1_pressed, or_1_out;
  wire [3:0] coder_4b_h_1_out, digit_finder_8b_1_digit_0, digit_finder_8b_1_digit_1,
       digit_finder_8b_1_digit_2;
  wire [7:0] bit_extender_2_out;
  wire [9:0] button_11_out;
  wire [15:0] bit_extender_1_out;
  wire [31:0] num_input_system_32b_ns_1_out;

  Button button_1 (.out(button_11_out[7]));
  Button button_2 (.out(button_11_out[4]));
  Button button_3 (.out(button_11_out[1]));
  Button button_4 (.out(button_4_out));
  Button button_5 (.out(button_11_out[9]));
  Button button_6 (.out(button_11_out[8]));
  Button button_7 (.out(button_11_out[5]));
  Button button_8 (.out(button_11_out[6]));
  Button button_9 (.out(button_11_out[3]));
  Button button_10 (.out(button_11_out[2]));
  Button button_11 (.out(button_11_out[0]));
  Button button_12 (.out(button_12_out));
  digit_finder_8b digit_finder_8b_1 (
    .digit_0(digit_finder_8b_1_digit_0), .digit_1(digit_finder_8b_1_digit_1),
    .digit_2(digit_finder_8b_1_digit_2), .input_8b(bit_extender_2_out));
  or or_1 (or_1_out, coder_4b_h_1_pressed, button_4_out);
  assign bit_extender_1_out = {{6{1'b0}}, button_11_out};  // Bit_Extender bit_extender_1
  coder_4b_h coder_4b_h_1 (
    .pressed(coder_4b_h_1_pressed), .in(bit_extender_1_out), .out(coder_4b_h_1_out));  // open: zero
  Hex_Digit_Display hex_digit_display_1 (.value(digit_finder_8b_1_digit_2));  // open: dp
  Hex_Digit_Display hex_digit_display_2 (.value(digit_finder_8b_1_digit_1));  // open: dp
  Hex_Digit_Display hex_digit_display_3 (.value(digit_finder_8b_1_digit_0));  // open: dp
  num_input_system_32b_ns num_input_system_32b_ns_1 (
    .out(num_input_system_32b_ns_1_out), .set(or_1_out), .Bkspace(button_4_out), .in(coder_4b_h_1_out),
    .reset(button_12_out));  // open: overFlow
  Bit_Extender #(.in_width(32), .out_width(8)) bit_extender_2 (
    .in(num_input_system_32b_ns_1_out), .out(bit_extender_2_out));

  // Notes on the sheet:
  //   7
  //   5
  //   4
  //   1
  //   2
  //   bkspce
  //   8
  //   9
  //   6
  //   3
  //   reset
  //   0
endmodule

module test (
  input  [7:0] in_1,
  input  [7:0] in_2,
  input  [3:0] in_3,
  input  [1:0] in_4,
  input  [3:0] in_5,
  input  [31:0] in_6,
  input  [4:0] in_7,
  output [31:0] out_8
);

  cpu_and_ram_32b_ns cpu_and_ram_32b_ns_1 (
    .Ram_WrQ(in_1), .Ram_RQ(in_2), .ReadMux_select_Q(in_3), .RamMux_select_Q(in_4), .ALU_Fnctn(in_5),
    .Ram_out(out_8), .user_0_select_2(in_6), ._0_RAM_Wr_1_RAM_R_2_RAM_Rst_3_Register_A_4_Register_B(in_7));  // open: user_1_select_3, user_10_select_12, ReadMux_in__select_1, RamMux_in__selsect_3, ALU_out, ALU_zero, ReadMux_out, user_2_select_4, user_3_select_5, user_4_select_6, user_5_select_7, user_6_select_8, user_7_select_9, user_8_select_10, user_9_select_11
endmodule
