// Logisim project decimal display.circ as structural Verilog: 2 circuits, main circuit main
module main (
  input  [7:0] in_1
);

  wire [3:0] n8bit_decimal_digit_finder_1_out_2, n8bit_decimal_digit_finder_1_out_3,
       n8bit_decimal_digit_finder_1_out_4;

  _8bit_decimal_digit_finder u_8bit_decimal_digit_finder_1 (
    .in_1(in_1), .out_2(n8bit_decimal_digit_finder_1_out_2), .out_3(n8bit_decimal_digit_finder_1_out_3),
    .out_4(n8bit_decimal_digit_finder_1_out_4));  // open: out_5, out_6, out_7
  Hex_Digit_Display hex_digit_display_1 (.value(n8bit_decimal_digit_finder_1_out_4));  // open: dp
  Hex_Digit_Display hex_digit_display_2 (.value(n8bit_decimal_digit_finder_1_out_3));  // open: dp
  Hex_Digit_Display hex_digit_display_3 (.value(n8bit_decimal_digit_finder_1_out_2));  // open: dp
endmodule

module _8bit_decimal_digit_finder (
  input  [7:0] in_1,
  output [3:0] out_2,
  output [3:0] out_3,
  output [3:0] out_4,
  output out_5,
  output out_6,
  output out_7
);

  wire nor_1_out, nor_2_out, not_1_out, not_2_out, not_3_out;
  wire [7:0] divider_1_out, divider_2_out, multiplier_1_out, multiplier_2_out, subtractor_1_out,
       subtractor_2_out;

  and and_1 (out_5, nor_1_out, nor_2_out);
  and and_2 (out_6, not_1_out, nor_2_out);
  and and_3 (out_7, not_2_out, not_3_out);
  Bit_Extender #(.out_width(4)) bit_extender_1 (.in(subtractor_1_out), .out(out_2));
  Subtractor subtractor_1 (.a(in_1), .b(multiplier_1_out), .out(subtractor_1_out));  // open: bin, bout
  Multiplier multiplier_1 (.a(divider_1_out), .b(8'ha), .out(multiplier_1_out));  // open: cin, cout
  Divider divider_1 (.a(in_1), .b(8'ha), .out(divider_1_out));  // open: upper, rem
  not not_1 (not_1_out, nor_1_out);
  not not_2 (not_2_out, nor_1_out);
  nor nor_1 (nor_1_out, divider_1_out[7], divider_1_out[6], divider_1_out[5], divider_1_out[4], divider_1_out[3], divider_1_out[2], divider_1_out[1], divider_1_out[0]);
  not not_3 (not_3_out, nor_2_out);
  Bit_Extender #(.out_width(4)) bit_extender_2 (.in(subtractor_2_out), .out(out_3));
  Subtractor subtractor_2 (.a(divider_1_out), .b(multiplier_2_out), .out(subtractor_2_out));  // open: bin, bout
  Multiplier multiplier_2 (.a(divider_2_out), .b(8'ha), .out(multiplier_2_out));  // open: cin, cout
  Divider divider_2 (.a(divider_1_out), .b(8'ha), .out(divider_2_out));  // open: upper, rem
  nor nor_2 (nor_2_out, divider_2_out[7], divider_2_out[6], divider_2_out[5], divider_2_out[4], divider_2_out[3], divider_2_out[2], divider_2_out[1], divider_2_out[0]);
  Bit_Extender #(.out_width(4)) bit_extender_3 (.in(divider_2_out), .out(out_4));
endmodule
