// Logisim project divider.circ as structural Verilog: 2 circuits, main circuit main
module main (
  input  [2:0] in_1,
  input  [2:0] A,
  input  [2:0] B,
  output [2:0] \output 
);

  wire comparator_1_eq, comparator_1_gt, comparator_2_eq, comparator_2_gt, comparator_3_eq, comparator_3_gt;
  wire [2:0] adder_1_out, adder_2_out, adder_3_out, bit_extender_1_out, bit_extender_2_out,
       bit_extender_3_out, multiplexer_1_out, multiplexer_2_out, multiplexer_3_out, subtractor_1_out,
       subtractor_2_out, subtractor_3_out, x2_3b_1_out_2, x2_3b_2_out_2, x2_3b_3_out_2;

  assign bit_extender_1_out = {{2{1'b0}}, A[2]};  // Bit_Extender bit_extender_1
  Adder #(.width(3)) adder_1 (.a(bit_extender_1_out), .b(x2_3b_1_out_2), .out(adder_1_out));  // open: cin, cout
  x2_3b x2_3b_1 (.in_1(in_1), .out_2(x2_3b_1_out_2));  // open: out_3
  Comparator #(.width(3), .mode("unsigned")) comparator_1 (
    .a(adder_1_out), .b(B), .gt(comparator_1_gt), .eq(comparator_1_eq));  // open: lt
  or or_1 (\output [2], comparator_1_eq, comparator_1_gt);
  Multiplexer #(.width(3), .enable("false")) multiplexer_1 (
    .in0(3'b000), .in1(B), .out(multiplexer_1_out), .sel(\output [2]));
  Subtractor #(.width(3)) subtractor_1 (
    .a(adder_1_out), .b(multiplexer_1_out), .out(subtractor_1_out));  // open: bin, bout
  assign bit_extender_2_out = {{2{1'b0}}, A[1]};  // Bit_Extender bit_extender_2
  Adder #(.width(3)) adder_2 (.a(bit_extender_2_out), .b(x2_3b_2_out_2), .out(adder_2_out));  // open: cin, cout
  x2_3b x2_3b_2 (.in_1(subtractor_1_out), .out_2(x2_3b_2_out_2));  // open: out_3
  Comparator #(.width(3), .mode("unsigned")) comparator_2 (
    .a(adder_2_out), .b(B), .gt(comparator_2_gt), .eq(comparator_2_eq));  // open: lt
  or or_2 (\output [1], comparator_2_eq, comparator_2_gt);
  Multiplexer #(.width(3), .enable("false")) multiplexer_2 (
    .in0(3'b000), .in1(B), .out(multiplexer_2_out), .sel(\output [1]));
  Subtractor #(.width(3)) subtractor_2 (
    .a(adder_2_out), .b(multiplexer_2_out), .out(subtractor_2_out));  // open: bin, bout
  x2_3b x2_3b_3 (.in_1(subtractor_2_out), .out_2(x2_3b_3_out_2));  // open: out_3
  assign bit_extender_3_out = {{2{1'b0}}, A[0]};  // Bit_Extender bit_extender_3
  Adder #(.width(3)) adder_3 (.a(bit_extender_3_out), .b(x2_3b_3_out_2), .out(adder_3_out));  // open: cin, cout
  Comparator #(.width(3), .mode("unsigned")) comparator_3 (
    .a(adder_3_out), .b(B), .gt(comparator_3_gt), .eq(comparator_3_eq));  // open: lt
  or or_3 (\output [0], comparator_3_eq, comparator_3_gt);
  Multiplexer #(.width(3), .enable("false")) multiplexer_3 (
    .in0(3'b000), .in1(B), .out(multiplexer_3_out), .sel(\output [0]));
  Subtractor #(.width(3)) subtractor_3 (
    .a(adder_3_out), .b(multiplexer_3_out), .out(subtractor_3_out));  // open: bin, bout
endmodule

module x2_3b (
  input  [2:0] in_1,
  output [2:0] out_2,
  output out_3
);


  assign out_2 = {in_1[1:0], 1'b0};
  assign out_3 = in_1[2];
endmodule
