// Logisim project double dable.circ as structural Verilog: 2 circuits, main circuit main
module main (
  input  [7:0] in_1,
  input  [15:0] in_2
);

  wire doubledableunit_1_out_5, doubledableunit_1_out_6, doubledableunit_1_out_7, doubledableunit_1_out_8,
       doubledableunit_2_out_5, doubledableunit_2_out_6, doubledableunit_2_out_7, doubledableunit_2_out_8,
       doubledableunit_3_out_5, doubledableunit_3_out_6, doubledableunit_3_out_7, doubledableunit_3_out_8,
       doubledableunit_4_out_6, doubledableunit_4_out_7, doubledableunit_4_out_8, doubledableunit_5_out_5,
       doubledableunit_5_out_6, doubledableunit_5_out_7, doubledableunit_5_out_8, doubledableunit_6_out_5,
       doubledableunit_6_out_6, doubledableunit_6_out_7, doubledableunit_6_out_8, doubledableunit_7_out_5,
       doubledableunit_7_out_6, doubledableunit_7_out_7, doubledableunit_7_out_8, doubledableunit_8_out_5,
       doubledableunit_8_out_6, doubledableunit_8_out_7, doubledableunit_8_out_8, doubledableunit_11_out_5,
       doubledableunit_11_out_6, doubledableunit_11_out_7, doubledableunit_11_out_8,
       doubledableunit_12_out_5, doubledableunit_12_out_6, doubledableunit_12_out_7,
       doubledableunit_12_out_8, doubledableunit_13_out_5, doubledableunit_13_out_6,
       doubledableunit_13_out_7, doubledableunit_13_out_8, doubledableunit_14_out_5,
       doubledableunit_14_out_6, doubledableunit_14_out_7, doubledableunit_14_out_8,
       doubledableunit_15_out_5, doubledableunit_15_out_6, doubledableunit_15_out_7,
       doubledableunit_15_out_8, doubledableunit_16_out_5, doubledableunit_16_out_6,
       doubledableunit_16_out_7, doubledableunit_16_out_8, doubledableunit_17_out_5,
       doubledableunit_17_out_6, doubledableunit_17_out_7, doubledableunit_17_out_8,
       doubledableunit_18_out_5, doubledableunit_18_out_6, doubledableunit_18_out_7,
       doubledableunit_18_out_8, doubledableunit_19_out_5, doubledableunit_19_out_6,
       doubledableunit_19_out_7, doubledableunit_19_out_8, doubledableunit_20_out_5,
       doubledableunit_20_out_6, doubledableunit_20_out_7, doubledableunit_20_out_8,
       doubledableunit_21_out_5, doubledableunit_21_out_6, doubledableunit_21_out_7,
       doubledableunit_21_out_8, doubledableunit_22_out_5, doubledableunit_22_out_6,
       doubledableunit_22_out_7, doubledableunit_22_out_8, doubledableunit_23_out_5,
       doubledableunit_23_out_6, doubledableunit_23_out_7, doubledableunit_23_out_8,
       doubledableunit_24_out_5, doubledableunit_24_out_6, doubledableunit_24_out_7,
       doubledableunit_24_out_8, doubledableunit_25_out_5, doubledableunit_25_out_6,
       doubledableunit_25_out_7, doubledableunit_25_out_8, doubledableunit_26_out_5,
       doubledableunit_26_out_6, doubledableunit_26_out_7, doubledableunit_26_out_8,
       doubledableunit_27_out_5, doubledableunit_27_out_6, doubledableunit_27_out_7,
       doubledableunit_27_out_8, doubledableunit_28_out_5, doubledableunit_28_out_6,
       doubledableunit_28_out_7, doubledableunit_28_out_8, doubledableunit_29_out_5,
       doubledableunit_29_out_6, doubledableunit_29_out_7, doubledableunit_29_out_8,
       doubledableunit_30_out_5, doubledableunit_30_out_6, doubledableunit_30_out_7,
       doubledableunit_30_out_8, doubledableunit_31_out_5, doubledableunit_31_out_6,
       doubledableunit_31_out_7, doubledableunit_31_out_8, doubledableunit_32_out_5,
       doubledableunit_32_out_6, doubledableunit_32_out_7, doubledableunit_32_out_8,
       doubledableunit_33_out_5, doubledableunit_33_out_6, doubledableunit_33_out_7,
       doubledableunit_33_out_8, doubledableunit_35_out_5, doubledableunit_35_out_6,
       doubledableunit_35_out_7, doubledableunit_35_out_8, doubledableunit_37_out_5,
       doubledableunit_37_out_6, doubledableunit_37_out_7, doubledableunit_37_out_8,
       doubledableunit_39_out_5, doubledableunit_39_out_6, doubledableunit_39_out_7,
       doubledableunit_39_out_8, doubledableunit_41_out_5, doubledableunit_41_out_6,
       doubledableunit_41_out_7, doubledableunit_41_out_8;
  wire [0:0] doubledableunit_34_out_5;
  wire [1:0] doubledableunit_9_out_5;
  wire [3:0] doubledableunit_10_out_5, doubledableunit_36_out_5, doubledableunit_38_out_5,
       doubledableunit_40_out_5, doubledableunit_42_out_5;
  wire [3:1] doubledableunit_10_out_8, doubledableunit_42_out_8;

  DoubleDableUnit doubledableunit_1 (
    .in_1(1'b0), .in_2(in_1[7]), .in_3(in_1[6]), .in_4(in_1[5]), .out_5(doubledableunit_1_out_5),
    .out_6(doubledableunit_1_out_6), .out_7(doubledableunit_1_out_7), .out_8(doubledableunit_1_out_8));
  DoubleDableUnit doubledableunit_2 (
    .in_1(doubledableunit_1_out_6), .in_2(doubledableunit_1_out_7), .in_3(doubledableunit_1_out_8),
    .in_4(in_1[4]), .out_5(doubledableunit_2_out_5), .out_6(doubledableunit_2_out_6),
    .out_7(doubledableunit_2_out_7), .out_8(doubledableunit_2_out_8));
  DoubleDableUnit doubledableunit_3 (
    .in_1(1'b0), .in_2(in_2[15]), .in_3(in_2[14]), .in_4(in_2[13]), .out_5(doubledableunit_3_out_5),
    .out_6(doubledableunit_3_out_6), .out_7(doubledableunit_3_out_7), .out_8(doubledableunit_3_out_8));
  DoubleDableUnit doubledableunit_4 (
    .in_1(1'b0), .in_2(doubledableunit_1_out_5), .in_3(doubledableunit_2_out_5),
    .in_4(doubledableunit_5_out_5), .out_5(doubledableunit_9_out_5[1]), .out_6(doubledableunit_4_out_6),
    .out_7(doubledableunit_4_out_7), .out_8(doubledableunit_4_out_8));
  DoubleDableUnit doubledableunit_5 (
    .in_1(doubledableunit_2_out_6), .in_2(doubledableunit_2_out_7), .in_3(doubledableunit_2_out_8),
    .in_4(in_1[3]), .out_5(doubledableunit_5_out_5), .out_6(doubledableunit_5_out_6),
    .out_7(doubledableunit_5_out_7), .out_8(doubledableunit_5_out_8));
  DoubleDableUnit doubledableunit_6 (
    .in_1(doubledableunit_5_out_6), .in_2(doubledableunit_5_out_7), .in_3(doubledableunit_5_out_8),
    .in_4(in_1[2]), .out_5(doubledableunit_6_out_5), .out_6(doubledableunit_6_out_6),
    .out_7(doubledableunit_6_out_7), .out_8(doubledableunit_6_out_8));
  DoubleDableUnit doubledableunit_7 (
    .in_1(doubledableunit_3_out_6), .in_2(doubledableunit_3_out_7), .in_3(doubledableunit_3_out_8),
    .in_4(in_2[12]), .out_5(doubledableunit_7_out_5), .out_6(doubledableunit_7_out_6),
    .out_7(doubledableunit_7_out_7), .out_8(doubledableunit_7_out_8));
  DoubleDableUnit doubledableunit_8 (
    .in_1(doubledableunit_7_out_6), .in_2(doubledableunit_7_out_7), .in_3(doubledableunit_7_out_8),
    .in_4(in_2[11]), .out_5(doubledableunit_8_out_5), .out_6(doubledableunit_8_out_6),
    .out_7(doubledableunit_8_out_7), .out_8(doubledableunit_8_out_8));
  Hex_Digit_Display hex_digit_display_1 (.value({2'b00, doubledableunit_9_out_5}));  // open: dp
  DoubleDableUnit doubledableunit_9 (
    .in_1(doubledableunit_4_out_6), .in_2(doubledableunit_4_out_7), .in_3(doubledableunit_4_out_8),
    .in_4(doubledableunit_6_out_5), .out_5(doubledableunit_9_out_5[0]), .out_6(doubledableunit_10_out_5[3]),
    .out_7(doubledableunit_10_out_5[2]), .out_8(doubledableunit_10_out_5[1]));
  DoubleDableUnit doubledableunit_10 (
    .in_1(doubledableunit_6_out_6), .in_2(doubledableunit_6_out_7), .in_3(doubledableunit_6_out_8),
    .in_4(in_1[1]), .out_5(doubledableunit_10_out_5[0]), .out_6(doubledableunit_10_out_8[3]),
    .out_7(doubledableunit_10_out_8[2]), .out_8(doubledableunit_10_out_8[1]));
  DoubleDableUnit doubledableunit_11 (
    .in_1(1'b0), .in_2(doubledableunit_3_out_5), .in_3(doubledableunit_7_out_5),
    .in_4(doubledableunit_8_out_5), .out_5(doubledableunit_11_out_5), .out_6(doubledableunit_11_out_6),
    .out_7(doubledableunit_11_out_7), .out_8(doubledableunit_11_out_8));
  DoubleDableUnit doubledableunit_12 (
    .in_1(doubledableunit_11_out_6), .in_2(doubledableunit_11_out_7), .in_3(doubledableunit_11_out_8),
    .in_4(doubledableunit_13_out_5), .out_5(doubledableunit_12_out_5), .out_6(doubledableunit_12_out_6),
    .out_7(doubledableunit_12_out_7), .out_8(doubledableunit_12_out_8));
  DoubleDableUnit doubledableunit_13 (
    .in_1(doubledableunit_8_out_6), .in_2(doubledableunit_8_out_7), .in_3(doubledableunit_8_out_8),
    .in_4(in_2[10]), .out_5(doubledableunit_13_out_5), .out_6(doubledableunit_13_out_6),
    .out_7(doubledableunit_13_out_7), .out_8(doubledableunit_13_out_8));
  DoubleDableUnit doubledableunit_14 (
    .in_1(doubledableunit_13_out_6), .in_2(doubledableunit_13_out_7), .in_3(doubledableunit_13_out_8),
    .in_4(in_2[9]), .out_5(doubledableunit_14_out_5), .out_6(doubledableunit_14_out_6),
    .out_7(doubledableunit_14_out_7), .out_8(doubledableunit_14_out_8));
  Hex_Digit_Display hex_digit_display_2 (.value({doubledableunit_10_out_8, in_1[0]}));  // open: dp
  Hex_Digit_Display hex_digit_display_3 (.value(doubledableunit_10_out_5));  // open: dp
  DoubleDableUnit doubledableunit_15 (
    .in_1(1'b0), .in_2(doubledableunit_11_out_5), .in_3(doubledableunit_12_out_5),
    .in_4(doubledableunit_16_out_5), .out_5(doubledableunit_15_out_5), .out_6(doubledableunit_15_out_6),
    .out_7(doubledableunit_15_out_7), .out_8(doubledableunit_15_out_8));
  DoubleDableUnit doubledableunit_16 (
    .in_1(doubledableunit_12_out_6), .in_2(doubledableunit_12_out_7), .in_3(doubledableunit_12_out_8),
    .in_4(doubledableunit_14_out_5), .out_5(doubledableunit_16_out_5), .out_6(doubledableunit_16_out_6),
    .out_7(doubledableunit_16_out_7), .out_8(doubledableunit_16_out_8));
  DoubleDableUnit doubledableunit_17 (
    .in_1(doubledableunit_16_out_6), .in_2(doubledableunit_16_out_7), .in_3(doubledableunit_16_out_8),
    .in_4(doubledableunit_18_out_5), .out_5(doubledableunit_17_out_5), .out_6(doubledableunit_17_out_6),
    .out_7(doubledableunit_17_out_7), .out_8(doubledableunit_17_out_8));
  DoubleDableUnit doubledableunit_18 (
    .in_1(doubledableunit_14_out_6), .in_2(doubledableunit_14_out_7), .in_3(doubledableunit_14_out_8),
    .in_4(in_2[8]), .out_5(doubledableunit_18_out_5), .out_6(doubledableunit_18_out_6),
    .out_7(doubledableunit_18_out_7), .out_8(doubledableunit_18_out_8));
  DoubleDableUnit doubledableunit_19 (
    .in_1(doubledableunit_18_out_6), .in_2(doubledableunit_18_out_7), .in_3(doubledableunit_18_out_8),
    .in_4(in_2[7]), .out_5(doubledableunit_19_out_5), .out_6(doubledableunit_19_out_6),
    .out_7(doubledableunit_19_out_7), .out_8(doubledableunit_19_out_8));
  DoubleDableUnit doubledableunit_20 (
    .in_1(doubledableunit_15_out_6), .in_2(doubledableunit_15_out_7), .in_3(doubledableunit_15_out_8),
    .in_4(doubledableunit_17_out_5), .out_5(doubledableunit_20_out_5), .out_6(doubledableunit_20_out_6),
    .out_7(doubledableunit_20_out_7), .out_8(doubledableunit_20_out_8));
  DoubleDableUnit doubledableunit_21 (
    .in_1(doubledableunit_20_out_6), .in_2(doubledableunit_20_out_7), .in_3(doubledableunit_20_out_8),
    .in_4(doubledableunit_22_out_5), .out_5(doubledableunit_21_out_5), .out_6(doubledableunit_21_out_6),
    .out_7(doubledableunit_21_out_7), .out_8(doubledableunit_21_out_8));
  DoubleDableUnit doubledableunit_22 (
    .in_1(doubledableunit_17_out_6), .in_2(doubledableunit_17_out_7), .in_3(doubledableunit_17_out_8),
    .in_4(doubledableunit_19_out_5), .out_5(doubledableunit_22_out_5), .out_6(doubledableunit_22_out_6),
    .out_7(doubledableunit_22_out_7), .out_8(doubledableunit_22_out_8));
  DoubleDableUnit doubledableunit_23 (
    .in_1(doubledableunit_22_out_6), .in_2(doubledableunit_22_out_7), .in_3(doubledableunit_22_out_8),
    .in_4(doubledableunit_24_out_5), .out_5(doubledableunit_23_out_5), .out_6(doubledableunit_23_out_6),
    .out_7(doubledableunit_23_out_7), .out_8(doubledableunit_23_out_8));
  DoubleDableUnit doubledableunit_24 (
    .in_1(doubledableunit_19_out_6), .in_2(doubledableunit_19_out_7), .in_3(doubledableunit_19_out_8),
    .in_4(in_2[6]), .out_5(doubledableunit_24_out_5), .out_6(doubledableunit_24_out_6),
    .out_7(doubledableunit_24_out_7), .out_8(doubledableunit_24_out_8));
  DoubleDableUnit doubledableunit_25 (
    .in_1(doubledableunit_24_out_6), .in_2(doubledableunit_24_out_7), .in_3(doubledableunit_24_out_8),
    .in_4(in_2[5]), .out_5(doubledableunit_25_out_5), .out_6(doubledableunit_25_out_6),
    .out_7(doubledableunit_25_out_7), .out_8(doubledableunit_25_out_8));
  DoubleDableUnit doubledableunit_26 (
    .in_1(1'b0), .in_2(doubledableunit_15_out_5), .in_3(doubledableunit_20_out_5),
    .in_4(doubledableunit_21_out_5), .out_5(doubledableunit_26_out_5), .out_6(doubledableunit_26_out_6),
    .out_7(doubledableunit_26_out_7), .out_8(doubledableunit_26_out_8));
  DoubleDableUnit doubledableunit_27 (
    .in_1(doubledableunit_26_out_6), .in_2(doubledableunit_26_out_7), .in_3(doubledableunit_26_out_8),
    .in_4(doubledableunit_28_out_5), .out_5(doubledableunit_27_out_5), .out_6(doubledableunit_27_out_6),
    .out_7(doubledableunit_27_out_7), .out_8(doubledableunit_27_out_8));
  DoubleDableUnit doubledableunit_28 (
    .in_1(doubledableunit_21_out_6), .in_2(doubledableunit_21_out_7), .in_3(doubledableunit_21_out_8),
    .in_4(doubledableunit_23_out_5), .out_5(doubledableunit_28_out_5), .out_6(doubledableunit_28_out_6),
    .out_7(doubledableunit_28_out_7), .out_8(doubledableunit_28_out_8));
  DoubleDableUnit doubledableunit_29 (
    .in_1(doubledableunit_28_out_6), .in_2(doubledableunit_28_out_7), .in_3(doubledableunit_28_out_8),
    .in_4(doubledableunit_30_out_5), .out_5(doubledableunit_29_out_5), .out_6(doubledableunit_29_out_6),
    .out_7(doubledableunit_29_out_7), .out_8(doubledableunit_29_out_8));
  DoubleDableUnit doubledableunit_30 (
    .in_1(doubledableunit_23_out_6), .in_2(doubledableunit_23_out_7), .in_3(doubledableunit_23_out_8),
    .in_4(doubledableunit_25_out_5), .out_5(doubledableunit_30_out_5), .out_6(doubledableunit_30_out_6),
    .out_7(doubledableunit_30_out_7), .out_8(doubledableunit_30_out_8));
  DoubleDableUnit doubledableunit_31 (
    .in_1(doubledableunit_30_out_6), .in_2(doubledableunit_30_out_7), .in_3(doubledableunit_30_out_8),
    .in_4(doubledableunit_32_out_5), .out_5(doubledableunit_31_out_5), .out_6(doubledableunit_31_out_6),
    .out_7(doubledableunit_31_out_7), .out_8(doubledableunit_31_out_8));
  DoubleDableUnit doubledableunit_32 (
    .in_1(doubledableunit_25_out_6), .in_2(doubledableunit_25_out_7), .in_3(doubledableunit_25_out_8),
    .in_4(in_2[4]), .out_5(doubledableunit_32_out_5), .out_6(doubledableunit_32_out_6),
    .out_7(doubledableunit_32_out_7), .out_8(doubledableunit_32_out_8));
  DoubleDableUnit doubledableunit_33 (
    .in_1(doubledableunit_32_out_6), .in_2(doubledableunit_32_out_7), .in_3(doubledableunit_32_out_8),
    .in_4(in_2[3]), .out_5(doubledableunit_33_out_5), .out_6(doubledableunit_33_out_6),
    .out_7(doubledableunit_33_out_7), .out_8(doubledableunit_33_out_8));
  DoubleDableUnit doubledableunit_34 (
    .in_1(1'b0), .in_2(doubledableunit_26_out_5), .in_3(doubledableunit_27_out_5),
    .in_4(doubledableunit_35_out_5), .out_5(doubledableunit_34_out_5[0]),
    .out_6(doubledableunit_36_out_5[3]), .out_7(doubledableunit_36_out_5[2]),
    .out_8(doubledableunit_36_out_5[1]));
  DoubleDableUnit doubledableunit_35 (
    .in_1(doubledableunit_27_out_6), .in_2(doubledableunit_27_out_7), .in_3(doubledableunit_27_out_8),
    .in_4(doubledableunit_29_out_5), .out_5(doubledableunit_35_out_5), .out_6(doubledableunit_35_out_6),
    .out_7(doubledableunit_35_out_7), .out_8(doubledableunit_35_out_8));
  DoubleDableUnit doubledableunit_36 (
    .in_1(doubledableunit_35_out_6), .in_2(doubledableunit_35_out_7), .in_3(doubledableunit_35_out_8),
    .in_4(doubledableunit_37_out_5), .out_5(doubledableunit_36_out_5[0]),
    .out_6(doubledableunit_38_out_5[3]), .out_7(doubledableunit_38_out_5[2]),
    .out_8(doubledableunit_38_out_5[1]));
  DoubleDableUnit doubledableunit_37 (
    .in_1(doubledableunit_29_out_6), .in_2(doubledableunit_29_out_7), .in_3(doubledableunit_29_out_8),
    .in_4(doubledableunit_31_out_5), .out_5(doubledableunit_37_out_5), .out_6(doubledableunit_37_out_6),
    .out_7(doubledableunit_37_out_7), .out_8(doubledableunit_37_out_8));
  DoubleDableUnit doubledableunit_38 (
    .in_1(doubledableunit_37_out_6), .in_2(doubledableunit_37_out_7), .in_3(doubledableunit_37_out_8),
    .in_4(doubledableunit_39_out_5), .out_5(doubledableunit_38_out_5[0]),
    .out_6(doubledableunit_40_out_5[3]), .out_7(doubledableunit_40_out_5[2]),
    .out_8(doubledableunit_40_out_5[1]));
  DoubleDableUnit doubledableunit_39 (
    .in_1(doubledableunit_31_out_6), .in_2(doubledableunit_31_out_7), .in_3(doubledableunit_31_out_8),
    .in_4(doubledableunit_33_out_5), .out_5(doubledableunit_39_out_5), .out_6(doubledableunit_39_out_6),
    .out_7(doubledableunit_39_out_7), .out_8(doubledableunit_39_out_8));
  DoubleDableUnit doubledableunit_40 (
    .in_1(doubledableunit_39_out_6), .in_2(doubledableunit_39_out_7), .in_3(doubledableunit_39_out_8),
    .in_4(doubledableunit_41_out_5), .out_5(doubledableunit_40_out_5[0]),
    .out_6(doubledableunit_42_out_5[3]), .out_7(doubledableunit_42_out_5[2]),
    .out_8(doubledableunit_42_out_5[1]));
  DoubleDableUnit doubledableunit_41 (
    .in_1(doubledableunit_33_out_6), .in_2(doubledableunit_33_out_7), .in_3(doubledableunit_33_out_8),
    .in_4(in_2[2]), .out_5(doubledableunit_41_out_5), .out_6(doubledableunit_41_out_6),
    .out_7(doubledableunit_41_out_7), .out_8(doubledableunit_41_out_8));
  DoubleDableUnit doubledableunit_42 (
    .in_1(doubledableunit_41_out_6), .in_2(doubledableunit_41_out_7), .in_3(doubledableunit_41_out_8),
    .in_4(in_2[1]), .out_5(doubledableunit_42_out_5[0]), .out_6(doubledableunit_42_out_8[3]),
    .out_7(doubledableunit_42_out_8[2]), .out_8(doubledableunit_42_out_8[1]));
  Hex_Digit_Display hex_digit_display_4 (.value({3'b000, doubledableunit_34_out_5[0]}));  // open: dp
  Hex_Digit_Display hex_digit_display_5 (.value(doubledableunit_38_out_5));  // open: dp
  Hex_Digit_Display hex_digit_display_6 (.value(doubledableunit_36_out_5));  // open: dp
  Hex_Digit_Display hex_digit_display_7 (.value(doubledableunit_40_out_5));  // open: dp
  Hex_Digit_Display hex_digit_display_8 (.value(doubledableunit_42_out_5));  // open: dp
  Hex_Digit_Display hex_digit_display_9 (.value({doubledableunit_42_out_8, in_2[0]}));  // open: dp
endmodule

module DoubleDableUnit (
  input  in_1,
  input  in_2,
  input  in_3,
  input  in_4,
  output out_5,
  output out_6,
  output out_7,
  output out_8
);

  wire comparator_1_lt, not_1_out;
  wire [3:0] multiplexer_1_out;

  Comparator #(.width(4), .mode("unsigned")) comparator_1 (
    .a({in_1, in_2, in_3, in_4}), .b(4'b0101), .lt(comparator_1_lt));  // open: gt, eq
  not not_1 (not_1_out, comparator_1_lt);
  Multiplexer #(.width(4), .enable("false")) multiplexer_1 (
    .in0(4'b0000), .in1(4'b0011), .out(multiplexer_1_out), .sel(not_1_out));
  Adder #(.width(4)) adder_1 (
    .a({in_1, in_2, in_3, in_4}), .b(multiplexer_1_out), .out({out_5, out_6, out_7, out_8}));  // open: cin, cout
endmodule
