// Logisim project memory.circ as structural Verilog: 3 circuits, main circuit main
module main (
  input  in_1,
  input  [3:0] in_2,
  output [3:0] out_3,
  output [3:0] out_4,
  output [3:0] out_5
);

  wire not_1_out;

  memory_4b memory_4b_1 (.In(in_2), .Out(out_4), .Write(not_1_out), .Read(1'b1));
  not not_1 (not_1_out, in_1);
  Adder #(.width(4)) adder_1 (.a(out_4), .b(out_5), .out(out_3));  // open: cin, cout
  memory_4b memory_4b_2 (.In(in_2), .Out(out_5), .Write(in_1), .Read(1'b1));
endmodule

module memory_1b (
  input  Write,
  input  In,
  input  Read,
  output Pre_out,
  output Out
);

  wire and_1_out, nor_1_out, not_1_out;

  nor nor_1 (nor_1_out, Write, Pre_out);
  not not_1 (not_1_out, In);
  and and_1 (and_1_out, Write, not_1_out);
  nor nor_2 (Pre_out, nor_1_out, and_1_out);
  and and_2 (Out, Pre_out, Read);
endmodule

module memory_4b (
  input  Write,
  input  Read,
  input  [3:0] In,
  output [3:0] Out
);

  memory_1b memory_1b_1 (.Write(Write), .In(In[0]), .Out(Out[0]), .Read(Read));  // open: Pre_out
  memory_1b memory_1b_2 (.Write(Write), .In(In[1]), .Out(Out[1]), .Read(Read));  // open: Pre_out
  memory_1b memory_1b_3 (.Write(Write), .In(In[2]), .Out(Out[2]), .Read(Read));  // open: Pre_out
  memory_1b memory_1b_4 (.Write(Write), .In(In[3]), .Out(Out[3]), .Read(Read));  // open: Pre_out
endmodule
