// Logisim project multiplier.circ as structural Verilog: 3 circuits, main circuit main
module main (
  input  [3:0] in_1,
  input  [3:0] in_2,
  input  [3:0] in_3,
  input  [3:0] in_4,
  input  [3:0] in_5,
  input  [3:0] in_6,
  input  [3:0] in_7,
  output [3:0] out_8,
  output [3:0] out_9,
  output [3:0] out_10,
  output [3:0] out_11
);

  wire adder_1_cout, adder_2_cout, adder_3_cout, adder_6_cout, adder_11_cout;
  wire [0:0] x2_4b_1_overf, x2_4b_2_overf, x2_4b_3_overf;
  wire [3:0] adder_1_out, adder_2_out, adder_3_out, adder_4_out, adder_5_out, adder_6_out, adder_7_out,
       adder_8_out, adder_10_out, bit_extender_1_out, bit_extender_2_out, bit_extender_3_out,
       bit_extender_4_out, multiplexer_1_out, multiplexer_2_out, multiplexer_3_out, multiplexer_4_out,
       multiplexer_5_out, multiplexer_6_out, multiplexer_7_out, x2_4b_1_out, x2_4b_2_out, x2_4b_3_out;

  Multiplexer #(.width(4), .enable("false")) multiplexer_1 (
    .in0(4'b0000), .in1(in_4), .out(multiplexer_1_out), .sel(in_3[0]));
  Adder #(.width(4)) adder_1 (
    .a(4'b0000), .b(multiplexer_1_out), .out(adder_1_out), .cin(in_1[3]), .cout(adder_1_cout));
  Multiplexer #(.width(4), .enable("false")) multiplexer_2 (
    .in0(4'b0000), .in1({3'b000, x2_4b_1_overf[0]}), .out(multiplexer_2_out), .sel(in_3[1]));
  Adder #(.width(4)) adder_2 (
    .a(adder_1_out), .b(multiplexer_3_out), .out(adder_2_out), .cin(in_1[2]), .cout(adder_2_cout));
  Multiplexer #(.width(4), .enable("false")) multiplexer_3 (
    .in0(4'b0000), .in1(x2_4b_1_out), .out(multiplexer_3_out), .sel(in_3[1]));
  x2_4b x2_4b_1 (.in(in_4), .out(x2_4b_1_out), .overF(x2_4b_1_overf[0]));
  Multiplexer #(.width(4), .enable("false")) multiplexer_4 (
    .in0(4'b0000), .in1(x2_4b_2_out), .out(multiplexer_4_out), .sel(in_3[2]));
  x2_4b x2_4b_2 (.in(x2_4b_1_out), .out(x2_4b_2_out), .overF(x2_4b_2_overf[0]));
  Multiplexer #(.width(4), .enable("false")) multiplexer_5 (
    .in0(4'b0000), .in1({2'b00, x2_4b_1_overf[0], x2_4b_2_overf[0]}), .out(multiplexer_5_out), .sel(in_3[2]));
  Adder #(.width(4)) adder_3 (
    .a(adder_2_out), .b(multiplexer_4_out), .out(adder_3_out), .cin(in_1[1]), .cout(adder_3_cout));
  Multiplier #(.width(4)) multiplier_1 (.a(in_6), .b(in_7), .out(out_10), .cin(in_5), .cout(out_11));
  Multiplexer #(.width(4), .enable("false")) multiplexer_6 (
    .in0(4'b0000), .in1(x2_4b_3_out), .out(multiplexer_6_out), .sel(in_3[3]));
  x2_4b x2_4b_3 (.in(x2_4b_2_out), .out(x2_4b_3_out), .overF(x2_4b_3_overf[0]));
  Multiplexer #(.width(4), .enable("false")) multiplexer_7 (
    .in0(4'b0000), .in1({1'b0, x2_4b_1_overf[0], x2_4b_2_overf[0], x2_4b_3_overf[0]}),
    .out(multiplexer_7_out), .sel(in_3[3]));
  Adder #(.width(4)) adder_4 (.a(multiplexer_2_out), .b(multiplexer_5_out), .out(adder_4_out));  // open: cin, cout
  Adder #(.width(4)) adder_5 (.a(multiplexer_7_out), .b(adder_4_out), .out(adder_5_out));  // open: cin, cout
  Adder #(.width(4)) adder_6 (
    .a(adder_3_out), .b(multiplexer_6_out), .out(adder_6_out), .cin(in_1[0]), .cout(adder_6_cout));
  assign bit_extender_1_out = {{3{1'b0}}, adder_6_cout};  // Bit_Extender bit_extender_1
  assign bit_extender_2_out = {{3{1'b0}}, adder_3_cout};  // Bit_Extender bit_extender_2
  assign bit_extender_3_out = {{3{1'b0}}, adder_2_cout};  // Bit_Extender bit_extender_3
  assign bit_extender_4_out = {{3{1'b0}}, adder_1_cout};  // Bit_Extender bit_extender_4
  Adder #(.width(4)) adder_7 (.a(bit_extender_1_out), .b(bit_extender_2_out), .out(adder_7_out));  // open: cin, cout
  Adder #(.width(4)) adder_8 (.a(adder_7_out), .b(bit_extender_3_out), .out(adder_8_out));  // open: cin, cout
  Adder #(.width(4)) adder_9 (.a(adder_5_out), .b(adder_10_out), .out(out_9), .cin(adder_11_cout));  // open: cout
  Adder #(.width(4)) adder_10 (.a(adder_8_out), .b(bit_extender_4_out), .out(adder_10_out));  // open: cin, cout
  Adder #(.width(4)) adder_11 (.a(in_2), .b(adder_6_out), .out(out_8), .cout(adder_11_cout));  // open: cin
endmodule

module x2_4b (
  input  [3:0] in,
  output [3:0] out,
  output overF
);


  assign out = {in[2:0], 1'b0};
  assign overF = in[3];
endmodule

module egr (
  input  [1:0] in_1,
  input  [1:0] in_2,
  input  [1:0] in_3
);

  wire adder_1_cout, adder_2_cout, undriven_2, undriven_5;
  wire [0:0] undriven_3;
  wire [1:0] adder_1_out, adder_2_out, multiplexer_1_out, multiplexer_2_out, undriven_4;
  wire [3:0] multiplexer_3_out;
  wire [3:2] undriven;

  Multiplexer #(.width(2), .enable("false")) multiplexer_1 (
    .in0(2'b00), .in1(in_3), .out(multiplexer_1_out), .sel(in_2[0]));
  Adder #(.width(2)) adder_1 (
    .a(2'b00), .b(multiplexer_1_out), .out(adder_1_out), .cin(undriven_2), .cout(adder_1_cout));
  Multiplexer #(.width(2), .enable("false")) multiplexer_2 (
    .in0(2'b00), .in1(undriven_4), .out(multiplexer_2_out), .sel(in_2[1]));
  Multiplexer #(.width(4), .enable("false")) multiplexer_3 (
    .in0(4'b0000), .in1({3'b000, undriven_3[0]}), .out(multiplexer_3_out), .sel(in_2[1]));
  Adder #(.width(2)) adder_2 (
    .a(adder_1_out), .b(multiplexer_2_out), .out(adder_2_out), .cin(undriven_5), .cout(adder_2_cout));
  // Pins of 2 and 4 bits meet at 4'b0000
  // Pins of 2 and 4 bits meet at 4'b0000
  // Pins of 2 and 4 bits meet at {undriven, in_2}
endmodule
