// Logisim project small memory.circ as structural Verilog: 2 circuits, main circuit main
module main (
  input  Write,
  input  Set,
  output Out
);

  wire and_1_out, nor_1_out, not_1_out;

  nor nor_1 (nor_1_out, Write, Out);
  not not_1 (not_1_out, Set);
  and and_1 (and_1_out, Write, not_1_out);
  nor nor_2 (Out, nor_1_out, and_1_out);
endmodule

module memory_1b (
  input  Write,
  input  Set,
  input  Read,
  output Pre_out,
  output Out
);

  wire and_1_out, nor_1_out, not_1_out;

  nor nor_1 (nor_1_out, Write, Pre_out);
  not not_1 (not_1_out, Set);
  and and_1 (and_1_out, Write, not_1_out);
  nor nor_2 (Pre_out, nor_1_out, and_1_out);
  and and_2 (Out, Pre_out, Read);
endmodule
